// Logisim project cpu24.circ as structural Verilog: 19 circuits, main circuit ◇单周期MIPS
module \单周期MIPS  (
  input  IR1,
  input  IR2,
  input  IR3,
  output RegWrite,
  output MemWrite,
  output [31:0] PC,
  output [31:0] IR,
  output [31:0] RDin,
  output [31:0] MDin,
  output [31:0] LED
);

  wire and_1_out, and_2_out, and_3_out, and_4_out, and_5_out, BLTZ, CLK, comparator_1_eq, EQU, Go, IR1_t,
       IR2_t, IR3_t, IRA, IRB, IRC, J, JAL, LH, nor_1_out, not_1_out, not_3_out, or_1_out, or_5_out,
       or_6_out, SignedExt, stop, Syscall, W1, W2, W3, \单周期硬布线控制器_1_alu_src , \单周期硬布线控制器_1_beq ,
       \单周期硬布线控制器_1_bne , \单周期硬布线控制器_1_jr , \单周期硬布线控制器_1_memtoreg , \单周期硬布线控制器_1_regdst ;
  wire [3:0] \单周期硬布线控制器_1_alu_op ;
  wire [4:0] multiplexer_2_out, multiplexer_3_out, multiplexer_4_out, multiplexer_5_out;
  wire [15:0] multiplexer_11_out, \总周期数 ;
  wire [31:0] adder_1_out, adder_2_out, bit_extender_1_out, bit_extender_2_out, bit_extender_3_out,
       controlled_buffer_1_out, mips_alu_1_result, multiplexer_1_out, multiplexer_6_out, multiplexer_7_out,
       multiplexer_8_out, multiplexer_10_out, ram_1_data, shifter_1_out, v0;

  Clock #(.highDuration(1), .lowDuration(1)) clock_1 (.out(CLK));
  Button _1 (.out(IRA));
  Button _2 (.out(IRB));
  Button _3 (.out(IRC));
  Button \u_继续运行  (.out(Go));
  LED #(.active("true")) led_1 (.in(W1));
  LED #(.active("true")) led_2 (.in(W2));
  LED #(.active("true")) led_3 (.in(W3));
  nor nor_1 (nor_1_out, \单周期硬布线控制器_1_jr , or_1_out, or_6_out);
  assign controlled_buffer_1_out = nor_1_out ? adder_1_out : 32'bz;  // Controlled_Buffer controlled_buffer_1
  Hex_Digit_Display hex_digit_display_1 (.value(LED[31:28]));  // open: dp
  assign controlled_buffer_1_out = \单周期硬布线控制器_1_jr  ? v0 : 32'bz;  // Controlled_Buffer controlled_buffer_2
  assign controlled_buffer_1_out = or_6_out ? adder_2_out : 32'bz;  // Controlled_Buffer controlled_buffer_3
  or or_1 (or_1_out, JAL, J);
  assign controlled_buffer_1_out = or_1_out ? {adder_1_out[31:28], IR[25:0], 2'b00} : 32'bz;  // Controlled_Buffer controlled_buffer_4
  Hex_Digit_Display hex_digit_display_2 (.value(LED[23:20]));  // open: dp
  Hex_Digit_Display hex_digit_display_3 (.value(LED[27:24]));  // open: dp
  Hex_Digit_Display hex_digit_display_4 (.value(LED[15:12]));  // open: dp
  Hex_Digit_Display hex_digit_display_5 (.value(LED[19:16]));  // open: dp
  Comparator #(.width(32), .mode("twosComplement")) comparator_1 (
    .a(v0), .b(32'h22), .eq(comparator_1_eq));  // open: gt, lt
  Multiplexer #(.select(1), .width(32), .disabled("Z"), .enable("false")) multiplexer_1 (
    .in0(LED), .in1(MDin), .out(multiplexer_1_out), .sel(and_1_out));
  Register #(.width(32), .trigger("rising"), .Select("low")) u_PC (
    .D(controlled_buffer_1_out), .en(stop), .Q(PC), .clk(CLK));  // open: clr
  Hex_Digit_Display hex_digit_display_6 (.value(LED[11:8]));  // open: dp
  Hex_Digit_Display hex_digit_display_7 (.value(LED[7:4]));  // open: dp
  // Probe on \总周期数 
  and and_1 (and_1_out, comparator_1_eq, Syscall);
  Register #(.width(32), .trigger("rising"), .Select("low")) register_1 (
    .D(multiplexer_1_out), .Q(LED), .clk(CLK));  // open: en, clr
  Adder #(.width(32)) adder_1 (.a(PC), .b(32'h4), .out(adder_1_out));  // open: cin, cout
  Hex_Digit_Display hex_digit_display_8 (.value(LED[3:0]));  // open: dp
  not not_1 (not_1_out, comparator_1_eq);
  and and_2 (and_2_out, not_1_out, Syscall);
  not not_2 (stop, and_2_out);
  ROM #(.addrWidth(10), .dataWidth(32), .Select("high")) rom_1 (.addr(PC[11:2]), .data(IR));
  or or_2 (IR1_t, IR1, IRA);
  Multiplexer #(.select(1), .width(5), .disabled("Z"), .enable("false")) multiplexer_2 (
    .in0(IR[25:21]), .in1(5'b00010), .out(multiplexer_2_out), .sel(Syscall));
  Multiplexer #(.select(1), .width(5), .disabled("Z"), .enable("false")) multiplexer_3 (
    .in0(IR[20:16]), .in1(5'b00100), .out(multiplexer_3_out), .sel(Syscall));
  Multiplexer #(.select(1), .width(5), .disabled("Z"), .enable("false")) multiplexer_4 (
    .in0(multiplexer_3_out), .in1(IR[15:11]), .out(multiplexer_4_out), .sel(\单周期硬布线控制器_1_regdst ));
  Multiplexer #(.select(1), .width(5), .disabled("Z"), .enable("false")) multiplexer_5 (
    .in0(multiplexer_4_out), .in1({5{1'b1}}), .out(multiplexer_5_out), .sel(JAL));
  or or_3 (IR2_t, IR2, IRB);
  \单周期硬布线控制器  \u_单周期硬布线控制器_1  (
    .Func(IR[5:0]), .OP(IR[31:26]), .ALU_OP(\单周期硬布线控制器_1_alu_op ), .MemToReg(\单周期硬布线控制器_1_memtoreg ),
    .MemWrite(MemWrite), .ALU_SRC(\单周期硬布线控制器_1_alu_src ), .RegWrite(RegWrite), .SysCALL(Syscall),
    .SignedExt(SignedExt), .RegDst(\单周期硬布线控制器_1_regdst ), .JR(\单周期硬布线控制器_1_jr ), .JMP(J),
    .Beq(\单周期硬布线控制器_1_beq ), .JAL(JAL), .Bne(\单周期硬布线控制器_1_bne ), .LH(LH), .BLTZ(BLTZ));
  assign bit_extender_1_out = {{16{1'b0}}, IR[15:0]};  // Bit_Extender bit_extender_1
  assign bit_extender_2_out = {{16{IR[15]}}, IR[15:0]};  // Bit_Extender bit_extender_2
  and and_3 (and_3_out, EQU, \单周期硬布线控制器_1_beq );
  and and_4 (and_4_out, not_3_out, \单周期硬布线控制器_1_bne );
  not not_3 (not_3_out, EQU);
  MIPS_Regifile mips_regifile_1 (
    .Din(RDin), .Clk(CLK), .R1(v0), .R2(MDin), .WE(RegWrite), .W_num(multiplexer_5_out),
    .R1_num(multiplexer_2_out), .R2_num(multiplexer_3_out));
  Multiplexer #(.select(1), .width(32), .disabled("Z"), .enable("false")) multiplexer_6 (
    .in0(bit_extender_1_out), .in1(bit_extender_2_out), .out(multiplexer_6_out), .sel(SignedExt));
  or or_4 (IR3_t, IR3, IRC);
  or or_5 (or_5_out, and_3_out, and_4_out);
  Multiplexer #(.select(1), .width(32), .disabled("Z"), .enable("false")) multiplexer_7 (
    .in0(MDin), .in1(multiplexer_6_out), .out(multiplexer_7_out), .sel(\单周期硬布线控制器_1_alu_src ));
  and and_5 (and_5_out, BLTZ, v0[31]);
  or or_6 (or_6_out, and_5_out, or_5_out);
  Multiplexer #(.select(1), .width(32), .disabled("Z"), .enable("false")) multiplexer_8 (
    .in0(mips_alu_1_result), .in1(multiplexer_10_out), .out(multiplexer_8_out), .sel(\单周期硬布线控制器_1_memtoreg ));
  Multiplexer #(.select(1), .width(32), .disabled("Z"), .enable("false")) multiplexer_9 (
    .in0(multiplexer_8_out), .in1(adder_1_out), .out(RDin), .sel(JAL));
  Shifter #(.width(32), .shift("ll")) shifter_1 (.in(multiplexer_6_out), .\dist (5'b00010), .out(shifter_1_out));
  MIPS_ALU mips_alu_1 (
    .X(v0), .Y(multiplexer_7_out), .AluOP(\单周期硬布线控制器_1_alu_op ), .Equal(EQU), .Result(mips_alu_1_result),
    .shamt(IR[10:6]));  // open: Result_2
  Adder #(.width(32)) adder_2 (.a(shifter_1_out), .b(adder_1_out), .out(adder_2_out));  // open: cin, cout
  Counter #(.width(16), .max('hffff), .ongoal("wrap"), .trigger("rising"), .behavior("new")) counter_1 (
    .count(stop), .Q(\总周期数 ), .clk(CLK));  // open: load, D, carry, clr, preset, down
  RAM #(.addrWidth(10), .dataWidth(32), .bus("separate"), .Select("high")) ram_1 (
    .addr(mips_alu_1_result[11:2]), .din(MDin), .data(ram_1_data), .str(MemWrite), .clk(CLK));  // open: sel, ld, clr
  Multiplexer #(.select(1), .width(32), .disabled("Z"), .enable("false")) multiplexer_10 (
    .in0(ram_1_data), .in1(bit_extender_3_out), .out(multiplexer_10_out), .sel(LH));
  assign bit_extender_3_out = {{16{multiplexer_11_out[15]}}, multiplexer_11_out};  // Bit_Extender bit_extender_3
  Multiplexer #(.select(1), .width(16), .disabled("Z"), .enable("false")) multiplexer_11 (
    .in0(ram_1_data[15:0]), .in1(ram_1_data[31:16]), .out(multiplexer_11_out), .sel(mips_alu_1_result[1]));

  // Other names for the same wires on the sheet: a0[31:0] = MDin

  // Notes on the sheet:
  //   中断源
  //   中断等待指示
  //   总复位信号应将除ROM以外所有存储组件全部清零
  //   数码管输出
  //   数码管输出应该用寄存器锁存，否则显示数据只能一闪而过
  //   指令存储器
  //   contents of rom_1 (hex, n*v repeats v):
  //   20110001 8000c05 20110001 20120002 20130003 8000c09 20110001 20120002 20130003 8000c0d 20110001
  //   20120002 20130003 8000c11 20110001 20120002 20130003 c000cb8 20100001 20110001 118fc0 112020
  //   20020022 c 118882 12200001 8000c15 112020 20020022 c 20110001 118880 112020 20020022 c 12200001
  //   8000c1f 20110001 118fc0 112020 20020022 c 1188c3 112020 20020022 c 118903 112020 20020022 c 118903
  //   112020 20020022 c 118903 112020 20020022 c 118903 112020 20020022 c 118903 112020 20020022 c 118903
  //   112020 20020022 c 118903 112020 20020022 c 20100001 109fc0 139fc3 8021 2012000c 24160003 26100001
  //   3210000f 20080008 20090001 139900 2709825 132020 20020022 c 1094022 1500fff9 22100001 2018000f
  //   2188024 108700 20080008 20090001 139902 2709825 132021 20020022 c 1094022 1500fff9 108702 2c9b022
  //   12c00001 8000c50 4020 1084027 84400 3508ffff 82021 20020022 c 2010ffff 20110000 ae300000 22100001
  //   22310004 ae300000 22100001 22310004 ae300000 22100001 22310004 ae300000 22100001 22310004 ae300000
  //   22100001 22310004 ae300000 22100001 22310004 ae300000 22100001 22310004 ae300000 22100001 22310004
  //   ae300000 22100001 22310004 ae300000 22100001 22310004 ae300000 22100001 22310004 ae300000 22100001
  //   22310004 ae300000 22100001 22310004 ae300000 22100001 22310004 ae300000 22100001 22310004 ae300000
  //   22100001 22310004 22100001 8020 2011003c 8e130000 8e340000 274402a 11000002 ae330000 ae140000
  //   2231fffc 1611fff8 102020 20020022 c 22100004 2011003c 1611fff2 20020032 c 20100000 22100001 102020
  //   20020022 c 22100002 102020 20020022 c 22100003 102020 20020022 c 22100004 102020 20020022 c 22100005
  //   102020 20020022 c 22100006 102020 20020022 c 22100007 102020 20020022 c 22100008 102020 20020022
  //   20020022 c 3e00008
  //   OP
  //   Func
  //   指令字
  //   rd
  //   JMP
  //   JR
  //   OP
  //   Func
  //   rs
  //   rt
  //   Beq
  //   Bne
  //   MemToReg
  //   MemWrite
  //   AluOP
  //   AluSrcB
  //   RegWrite
  //   JAL
  //   RegDst
  //   Syscall
  //   为方便自动评测，需要输出PC，IR，寄存器堆写如数据RDin
  //   RAM写使能MemWrite、RAM写入数据MDin等信号
endmodule

// 单周期硬布线控制器
module \单周期硬布线控制器  (
  input  [5:0] OP,
  input  [5:0] Func,
  output [3:0] ALU_OP,
  output MemToReg,
  output MemWrite,
  output ALU_SRC,
  output RegWrite,
  output SysCALL,
  output SignedExt,
  output RegDst,
  output Beq,
  output Bne,
  output JR,
  output JMP,
  output JAL,
  output LH,
  output BLTZ
);

  \运算控制器自动生成  \u_运算控制器自动生成_1  (
    .OP0(OP[0]), .OP1(OP[1]), .OP2(OP[2]), .OP3(OP[3]), .OP4(OP[4]), .OP5(OP[5]), .F0(Func[0]), .F1(Func[1]),
    .F2(Func[2]), .F3(Func[3]), .F4(Func[4]), .F5(Func[5]), .S0(ALU_OP[0]), .S1(ALU_OP[1]), .S2(ALU_OP[2]),
    .S3(ALU_OP[3]));
  \控制信号自动生成  \u_控制信号自动生成_1  (
    .OP0(OP[0]), .OP1(OP[1]), .OP2(OP[2]), .OP3(OP[3]), .OP4(OP[4]), .OP5(OP[5]), .F0(Func[0]), .F1(Func[1]),
    .F2(Func[2]), .F3(Func[3]), .F4(Func[4]), .F5(Func[5]), .MemToReg(MemToReg), .MemWrite(MemWrite),
    .ALU_SRC(ALU_SRC), .RegWrite(RegWrite), .SysCALL(SysCALL), .SignedExt(SignedExt), .RegDst(RegDst),
    .BEQ(Beq), .BNE(Bne), .JR(JR), .JUMP(JMP), .JAL(JAL), .LH(LH), .BLTZ(BLTZ));

  // Other names for the same wires on the sheet: OP_CODE[5:0] = OP

  // Notes on the sheet:
  //   运算器控制器，根据指令生成运算器功能选择信号
  //   控制信号生成，产生数据通路需要的其他控制信号
endmodule

// 运算器控制器
module \运算控制器自动生成  (
  input  OP0,
  input  OP1,
  input  OP2,
  input  OP3,
  input  OP4,
  input  OP5,
  input  F0,
  input  F1,
  input  F2,
  input  F3,
  input  F4,
  input  F5,
  output S0,
  output S1,
  output S2,
  output S3
);

  wire and_1_out, and_2_out, and_3_out, and_4_out, and_5_out, and_6_out, and_7_out, and_8_out, and_9_out,
       and_10_out, and_11_out, and_12_out, and_13_out, and_14_out, and_15_out, and_16_out, and_17_out,
       and_18_out, and_19_out, and_20_out, and_21_out, and_22_out, and_23_out, and_24_out, and_25_out,
       and_26_out, and_27_out, and_28_out, and_29_out, and_30_out, and_31_out, and_32_out, and_33_out,
       and_34_out, and_35_out, and_36_out, and_37_out, and_38_out, and_39_out, and_40_out, and_41_out,
       not_1_out, not_2_out, not_3_out, not_4_out, not_5_out, not_6_out, not_7_out, not_8_out, not_9_out,
       not_10_out, not_11_out, not_12_out, not_13_out, not_14_out, not_15_out, not_16_out, not_17_out,
       not_18_out, not_19_out, not_20_out, not_21_out, not_22_out, not_23_out, not_24_out, not_25_out,
       not_26_out, not_27_out, not_28_out, not_29_out, not_30_out, not_31_out, not_32_out, not_33_out,
       not_34_out, not_35_out, not_36_out, not_37_out, not_38_out, not_39_out, not_40_out, not_41_out,
       not_42_out, not_43_out, not_44_out, not_45_out, not_46_out, not_47_out, not_48_out, not_49_out,
       not_50_out, not_51_out, not_52_out, not_53_out, not_54_out, not_55_out, not_56_out, not_57_out,
       not_58_out, not_59_out, not_60_out, not_61_out, not_62_out, not_63_out, not_64_out, not_65_out,
       not_66_out, not_67_out, not_68_out, not_69_out, not_70_out, not_71_out, not_72_out, not_73_out,
       not_74_out, not_75_out, not_76_out, not_77_out, not_78_out, not_79_out, not_80_out, not_81_out,
       not_82_out, not_83_out, not_84_out, not_85_out, not_86_out, not_87_out, not_88_out, not_89_out,
       not_90_out, not_91_out, not_92_out, not_93_out, not_94_out, not_95_out, not_96_out, not_97_out,
       not_98_out, not_99_out, not_100_out, not_101_out, not_102_out, not_103_out, not_104_out, not_105_out,
       not_106_out, not_107_out, not_108_out, not_109_out, not_110_out, not_111_out, not_112_out,
       not_113_out, not_114_out, not_115_out, not_116_out, not_117_out, not_118_out, not_119_out,
       not_120_out, not_121_out, not_122_out, not_123_out, not_124_out, not_125_out, not_126_out,
       not_127_out, not_128_out, not_129_out, not_130_out, not_131_out, not_132_out, not_133_out,
       not_134_out, not_135_out, not_136_out, not_137_out, not_138_out, not_139_out, not_140_out,
       not_141_out, not_142_out, not_143_out, not_144_out, not_145_out, not_146_out, not_147_out,
       not_148_out, not_149_out, not_150_out, not_151_out, not_152_out, not_153_out, not_154_out,
       not_155_out, not_156_out, not_157_out, not_158_out, not_159_out, not_160_out, not_161_out,
       not_162_out, not_163_out, not_164_out, not_165_out, not_166_out, not_167_out, not_168_out,
       not_169_out, not_170_out, not_171_out, not_172_out, not_173_out, not_174_out, not_175_out,
       not_176_out, not_177_out, not_178_out, not_179_out, not_180_out, not_181_out, not_182_out,
       not_183_out, not_184_out, not_185_out, not_186_out, not_187_out, not_188_out, not_189_out,
       not_190_out, not_191_out, not_192_out, not_193_out, not_194_out, not_195_out, not_196_out,
       not_197_out, not_198_out, not_199_out, not_200_out, not_201_out, not_202_out, not_203_out,
       not_204_out, not_205_out, not_206_out, not_207_out, not_208_out, not_209_out, not_210_out,
       not_211_out, not_212_out, not_213_out, not_214_out, not_215_out, not_216_out, not_217_out,
       not_218_out, not_219_out, not_220_out, not_221_out, not_222_out, not_223_out, not_224_out,
       not_225_out, not_226_out, not_227_out, not_228_out, not_229_out, not_230_out, not_231_out,
       not_232_out, not_233_out, not_234_out, not_235_out, not_236_out, not_237_out, not_238_out,
       not_239_out, not_240_out, not_241_out, not_242_out, not_243_out, not_244_out, not_245_out,
       not_246_out, not_247_out, not_248_out, not_249_out, not_250_out, not_251_out, not_252_out,
       not_253_out, not_254_out, not_255_out, not_256_out, not_257_out, not_258_out, not_259_out,
       not_260_out, not_261_out, not_262_out, not_263_out, not_264_out, not_265_out, not_266_out,
       not_267_out, not_268_out, not_269_out, not_270_out, not_271_out, not_272_out, not_273_out,
       not_274_out, not_275_out, not_276_out, not_277_out;

  not not_1 (not_1_out, OP5);
  not not_2 (not_2_out, OP4);
  not not_3 (not_3_out, OP3);
  not not_4 (not_4_out, OP2);
  not not_5 (not_5_out, OP1);
  not not_6 (not_6_out, OP0);
  not not_7 (not_7_out, F5);
  not not_8 (not_8_out, F4);
  not not_9 (not_9_out, F3);
  not not_10 (not_10_out, F2);
  not not_11 (not_11_out, OP5);
  not not_12 (not_12_out, OP4);
  not not_13 (not_13_out, OP3);
  not not_14 (not_14_out, OP2);
  not not_15 (not_15_out, OP1);
  not not_16 (not_16_out, OP0);
  not not_17 (not_17_out, F4);
  not not_18 (not_18_out, F3);
  not not_19 (not_19_out, F2);
  not not_20 (not_20_out, F1);
  not not_21 (not_21_out, F0);
  not not_22 (not_22_out, OP5);
  not not_23 (not_23_out, OP4);
  not not_24 (not_24_out, OP3);
  not not_25 (not_25_out, OP2);
  not not_26 (not_26_out, OP1);
  not not_27 (not_27_out, OP0);
  not not_28 (not_28_out, F4);
  not not_29 (not_29_out, F3);
  not not_30 (not_30_out, F2);
  not not_31 (not_31_out, F1);
  not not_32 (not_32_out, OP5);
  not not_33 (not_33_out, OP4);
  not not_34 (not_34_out, OP3);
  not not_35 (not_35_out, OP2);
  not not_36 (not_36_out, OP1);
  not not_37 (not_37_out, OP0);
  not not_38 (not_38_out, F4);
  not not_39 (not_39_out, F3);
  not not_40 (not_40_out, F1);
  not not_41 (not_41_out, F0);
  not not_42 (not_42_out, OP5);
  not not_43 (not_43_out, OP4);
  not not_44 (not_44_out, OP3);
  not not_45 (not_45_out, OP2);
  not not_46 (not_46_out, OP1);
  not not_47 (not_47_out, OP0);
  not not_48 (not_48_out, F4);
  not not_49 (not_49_out, F2);
  not not_50 (not_50_out, F0);
  not not_51 (not_51_out, OP5);
  not not_52 (not_52_out, OP4);
  not not_53 (not_53_out, OP2);
  not not_54 (not_54_out, OP1);
  not not_55 (not_55_out, OP0);
  not not_56 (not_56_out, OP5);
  not not_57 (not_57_out, OP4);
  not not_58 (not_58_out, OP1);
  not not_59 (not_59_out, OP0);
  not not_60 (not_60_out, OP5);
  not not_61 (not_61_out, OP4);
  not not_62 (not_62_out, OP2);
  not not_63 (not_63_out, OP1);
  not not_64 (not_64_out, OP5);
  not not_65 (not_65_out, OP4);
  not not_66 (not_66_out, OP2);
  not not_67 (not_67_out, OP0);
  not not_68 (not_68_out, OP4);
  not not_69 (not_69_out, OP3);
  not not_70 (not_70_out, OP2);
  not not_71 (not_71_out, OP4);
  not not_72 (not_72_out, OP2);
  not not_73 (not_73_out, OP5);
  not not_74 (not_74_out, OP4);
  not not_75 (not_75_out, OP0);
  not not_76 (not_76_out, OP4);
  not not_77 (not_77_out, OP3);
  not not_78 (not_78_out, OP2);
  not not_79 (not_79_out, OP1);
  not not_80 (not_80_out, OP5);
  not not_81 (not_81_out, OP4);
  not not_82 (not_82_out, OP3);
  not not_83 (not_83_out, OP2);
  not not_84 (not_84_out, OP1);
  not not_85 (not_85_out, OP0);
  not not_86 (not_86_out, F5);
  not not_87 (not_87_out, F4);
  not not_88 (not_88_out, F3);
  not not_89 (not_89_out, F2);
  not not_90 (not_90_out, F0);
  not not_91 (not_91_out, OP5);
  not not_92 (not_92_out, OP4);
  not not_93 (not_93_out, OP3);
  not not_94 (not_94_out, OP2);
  not not_95 (not_95_out, OP1);
  not not_96 (not_96_out, OP0);
  not not_97 (not_97_out, F4);
  not not_98 (not_98_out, F3);
  not not_99 (not_99_out, F2);
  not not_100 (not_100_out, F0);
  not not_101 (not_101_out, OP5);
  not not_102 (not_102_out, OP4);
  not not_103 (not_103_out, OP3);
  not not_104 (not_104_out, OP2);
  not not_105 (not_105_out, OP1);
  not not_106 (not_106_out, OP0);
  not not_107 (not_107_out, F4);
  not not_108 (not_108_out, F3);
  not not_109 (not_109_out, F1);
  not not_110 (not_110_out, F0);
  not not_111 (not_111_out, OP5);
  not not_112 (not_112_out, OP4);
  not not_113 (not_113_out, OP3);
  not not_114 (not_114_out, OP2);
  not not_115 (not_115_out, OP1);
  not not_116 (not_116_out, OP0);
  not not_117 (not_117_out, F4);
  not not_118 (not_118_out, F3);
  not not_119 (not_119_out, OP5);
  not not_120 (not_120_out, OP4);
  not not_121 (not_121_out, OP3);
  not not_122 (not_122_out, OP2);
  not not_123 (not_123_out, OP1);
  not not_124 (not_124_out, OP0);
  not not_125 (not_125_out, F4);
  not not_126 (not_126_out, F2);
  not not_127 (not_127_out, F0);
  not not_128 (not_128_out, OP5);
  not not_129 (not_129_out, OP4);
  not not_130 (not_130_out, OP1);
  not not_131 (not_131_out, OP0);
  not not_132 (not_132_out, OP5);
  not not_133 (not_133_out, OP4);
  not not_134 (not_134_out, OP2);
  not not_135 (not_135_out, OP0);
  not not_136 (not_136_out, OP5);
  not not_137 (not_137_out, OP4);
  not not_138 (not_138_out, OP3);
  not not_139 (not_139_out, OP2);
  not not_140 (not_140_out, OP1);
  not not_141 (not_141_out, OP0);
  not not_142 (not_142_out, F4);
  not not_143 (not_143_out, F3);
  not not_144 (not_144_out, F2);
  not not_145 (not_145_out, OP5);
  not not_146 (not_146_out, OP4);
  not not_147 (not_147_out, OP3);
  not not_148 (not_148_out, OP2);
  not not_149 (not_149_out, OP1);
  not not_150 (not_150_out, OP0);
  not not_151 (not_151_out, F4);
  not not_152 (not_152_out, F3);
  not not_153 (not_153_out, F2);
  not not_154 (not_154_out, F1);
  not not_155 (not_155_out, F0);
  not not_156 (not_156_out, OP5);
  not not_157 (not_157_out, OP4);
  not not_158 (not_158_out, OP3);
  not not_159 (not_159_out, OP2);
  not not_160 (not_160_out, OP1);
  not not_161 (not_161_out, OP0);
  not not_162 (not_162_out, F4);
  not not_163 (not_163_out, F3);
  not not_164 (not_164_out, F2);
  not not_165 (not_165_out, F1);
  not not_166 (not_166_out, OP5);
  not not_167 (not_167_out, OP4);
  not not_168 (not_168_out, OP3);
  not not_169 (not_169_out, OP2);
  not not_170 (not_170_out, OP1);
  not not_171 (not_171_out, OP0);
  not not_172 (not_172_out, F4);
  not not_173 (not_173_out, F3);
  not not_174 (not_174_out, F2);
  not not_175 (not_175_out, F0);
  not not_176 (not_176_out, OP5);
  not not_177 (not_177_out, OP4);
  not not_178 (not_178_out, OP3);
  not not_179 (not_179_out, OP2);
  not not_180 (not_180_out, OP1);
  not not_181 (not_181_out, OP0);
  not not_182 (not_182_out, F4);
  not not_183 (not_183_out, F3);
  not not_184 (not_184_out, F1);
  not not_185 (not_185_out, F0);
  not not_186 (not_186_out, OP5);
  not not_187 (not_187_out, OP4);
  not not_188 (not_188_out, OP3);
  not not_189 (not_189_out, OP2);
  not not_190 (not_190_out, OP1);
  not not_191 (not_191_out, OP0);
  not not_192 (not_192_out, F4);
  not not_193 (not_193_out, F2);
  not not_194 (not_194_out, OP5);
  not not_195 (not_195_out, OP4);
  not not_196 (not_196_out, OP2);
  not not_197 (not_197_out, OP1);
  not not_198 (not_198_out, OP0);
  not not_199 (not_199_out, OP5);
  not not_200 (not_200_out, OP4);
  not not_201 (not_201_out, OP1);
  not not_202 (not_202_out, OP0);
  not not_203 (not_203_out, OP5);
  not not_204 (not_204_out, OP4);
  not not_205 (not_205_out, OP2);
  not not_206 (not_206_out, OP1);
  not not_207 (not_207_out, OP4);
  not not_208 (not_208_out, OP3);
  not not_209 (not_209_out, OP2);
  not not_210 (not_210_out, OP4);
  not not_211 (not_211_out, OP2);
  not not_212 (not_212_out, OP5);
  not not_213 (not_213_out, OP4);
  not not_214 (not_214_out, OP3);
  not not_215 (not_215_out, OP2);
  not not_216 (not_216_out, OP1);
  not not_217 (not_217_out, OP0);
  not not_218 (not_218_out, F4);
  not not_219 (not_219_out, F3);
  not not_220 (not_220_out, F2);
  not not_221 (not_221_out, OP4);
  not not_222 (not_222_out, OP3);
  not not_223 (not_223_out, OP2);
  not not_224 (not_224_out, OP1);
  not not_225 (not_225_out, OP5);
  not not_226 (not_226_out, OP4);
  not not_227 (not_227_out, OP3);
  not not_228 (not_228_out, OP2);
  not not_229 (not_229_out, OP1);
  not not_230 (not_230_out, OP0);
  not not_231 (not_231_out, F4);
  not not_232 (not_232_out, F3);
  not not_233 (not_233_out, F1);
  not not_234 (not_234_out, OP5);
  not not_235 (not_235_out, OP4);
  not not_236 (not_236_out, OP3);
  not not_237 (not_237_out, OP2);
  not not_238 (not_238_out, OP1);
  not not_239 (not_239_out, OP0);
  not not_240 (not_240_out, F4);
  not not_241 (not_241_out, F3);
  not not_242 (not_242_out, OP5);
  not not_243 (not_243_out, OP4);
  not not_244 (not_244_out, OP3);
  not not_245 (not_245_out, OP2);
  not not_246 (not_246_out, OP1);
  not not_247 (not_247_out, OP0);
  not not_248 (not_248_out, F4);
  not not_249 (not_249_out, F2);
  not not_250 (not_250_out, F0);
  not not_251 (not_251_out, OP5);
  not not_252 (not_252_out, OP4);
  not not_253 (not_253_out, OP3);
  not not_254 (not_254_out, OP2);
  not not_255 (not_255_out, OP1);
  not not_256 (not_256_out, OP0);
  not not_257 (not_257_out, F4);
  not not_258 (not_258_out, F2);
  not not_259 (not_259_out, OP5);
  not not_260 (not_260_out, OP4);
  not not_261 (not_261_out, OP2);
  not not_262 (not_262_out, OP0);
  not not_263 (not_263_out, OP5);
  not not_264 (not_264_out, OP4);
  not not_265 (not_265_out, OP1);
  not not_266 (not_266_out, OP5);
  not not_267 (not_267_out, OP4);
  not not_268 (not_268_out, OP3);
  not not_269 (not_269_out, OP2);
  not not_270 (not_270_out, OP1);
  not not_271 (not_271_out, OP0);
  not not_272 (not_272_out, F4);
  not not_273 (not_273_out, F3);
  not not_274 (not_274_out, F2);
  not not_275 (not_275_out, OP5);
  not not_276 (not_276_out, OP4);
  not not_277 (not_277_out, OP0);
  and and_1 (and_1_out, not_1_out, not_2_out, not_3_out, not_4_out, not_5_out, not_6_out, not_7_out, not_8_out, not_9_out, not_10_out, F1, F0);
  and and_2 (and_2_out, not_11_out, not_12_out, not_13_out, not_14_out, not_15_out, not_16_out, F5, not_17_out, not_18_out, not_19_out, not_20_out, not_21_out);
  and and_3 (and_3_out, not_22_out, not_23_out, not_24_out, not_25_out, not_26_out, not_27_out, F5, not_28_out, not_29_out, not_30_out, not_31_out, F0);
  and and_4 (and_4_out, not_32_out, not_33_out, not_34_out, not_35_out, not_36_out, not_37_out, F5, not_38_out, not_39_out, F2, not_40_out, not_41_out);
  and and_5 (and_5_out, not_42_out, not_43_out, not_44_out, not_45_out, not_46_out, not_47_out, F5, not_48_out, F3, not_49_out, F1, not_50_out);
  and and_6 (and_6_out, not_51_out, not_52_out, OP3, not_53_out, not_54_out, not_55_out);
  and and_7 (and_7_out, not_56_out, not_57_out, OP3, OP2, not_58_out, not_59_out);
  and and_8 (and_8_out, not_60_out, not_61_out, OP3, not_62_out, not_63_out, OP0);
  and and_9 (and_9_out, not_64_out, not_65_out, OP3, not_66_out, OP1, not_67_out);
  and and_10 (and_10_out, OP5, not_68_out, not_69_out, not_70_out, OP1, OP0);
  and and_11 (and_11_out, OP5, not_71_out, OP3, not_72_out, OP1, OP0);
  and and_12 (and_12_out, not_73_out, not_74_out, OP3, OP2, OP1, not_75_out);
  and and_13 (and_13_out, OP5, not_76_out, not_77_out, not_78_out, not_79_out, OP0);
  and and_14 (and_14_out, not_80_out, not_81_out, not_82_out, not_83_out, not_84_out, not_85_out, not_86_out, not_87_out, not_88_out, not_89_out, F1, not_90_out);
  and and_15 (and_15_out, not_91_out, not_92_out, not_93_out, not_94_out, not_95_out, not_96_out, F5, not_97_out, not_98_out, not_99_out, F1, not_100_out);
  and and_16 (and_16_out, not_101_out, not_102_out, not_103_out, not_104_out, not_105_out, not_106_out, F5, not_107_out, not_108_out, F2, not_109_out, not_110_out);
  and and_17 (and_17_out, not_111_out, not_112_out, not_113_out, not_114_out, not_115_out, not_116_out, F5, not_117_out, not_118_out, F2, F1, F0);
  and and_18 (and_18_out, not_119_out, not_120_out, not_121_out, not_122_out, not_123_out, not_124_out, F5, not_125_out, F3, not_126_out, F1, not_127_out);
  and and_19 (and_19_out, not_128_out, not_129_out, OP3, OP2, not_130_out, not_131_out);
  and and_20 (and_20_out, not_132_out, not_133_out, OP3, not_134_out, OP1, not_135_out);
  and and_21 (and_21_out, not_136_out, not_137_out, not_138_out, not_139_out, not_140_out, not_141_out, F5, not_142_out, not_143_out, not_144_out, F1, F0);
  and and_22 (and_22_out, not_145_out, not_146_out, not_147_out, not_148_out, not_149_out, not_150_out, F5, not_151_out, not_152_out, not_153_out, not_154_out, not_155_out);
  and and_23 (and_23_out, not_156_out, not_157_out, not_158_out, not_159_out, not_160_out, not_161_out, F5, not_162_out, not_163_out, not_164_out, not_165_out, F0);
  and and_24 (and_24_out, not_166_out, not_167_out, not_168_out, not_169_out, not_170_out, not_171_out, F5, not_172_out, not_173_out, not_174_out, F1, not_175_out);
  and and_25 (and_25_out, not_176_out, not_177_out, not_178_out, not_179_out, not_180_out, not_181_out, F5, not_182_out, not_183_out, F2, not_184_out, not_185_out);
  and and_26 (and_26_out, not_186_out, not_187_out, not_188_out, not_189_out, not_190_out, not_191_out, F5, not_192_out, F3, not_193_out, F1, F0);
  and and_27 (and_27_out, not_194_out, not_195_out, OP3, not_196_out, not_197_out, not_198_out);
  and and_28 (and_28_out, not_199_out, not_200_out, OP3, OP2, not_201_out, not_202_out);
  and and_29 (and_29_out, not_203_out, not_204_out, OP3, not_205_out, not_206_out, OP0);
  and and_30 (and_30_out, OP5, not_207_out, not_208_out, not_209_out, OP1, OP0);
  and and_31 (and_31_out, OP5, not_210_out, OP3, not_211_out, OP1, OP0);
  and and_32 (and_32_out, not_212_out, not_213_out, not_214_out, not_215_out, not_216_out, not_217_out, F5, not_218_out, not_219_out, not_220_out, F1, F0);
  and and_33 (and_33_out, OP5, not_221_out, not_222_out, not_223_out, not_224_out, OP0);
  and and_34 (and_34_out, not_225_out, not_226_out, not_227_out, not_228_out, not_229_out, not_230_out, F5, not_231_out, not_232_out, F2, not_233_out, F0);
  and and_35 (and_35_out, not_234_out, not_235_out, not_236_out, not_237_out, not_238_out, not_239_out, F5, not_240_out, not_241_out, F2, F1, F0);
  and and_36 (and_36_out, not_242_out, not_243_out, not_244_out, not_245_out, not_246_out, not_247_out, F5, not_248_out, F3, not_249_out, F1, not_250_out);
  and and_37 (and_37_out, not_251_out, not_252_out, not_253_out, not_254_out, not_255_out, not_256_out, F5, not_257_out, F3, not_258_out, F1, F0);
  and and_38 (and_38_out, not_259_out, not_260_out, OP3, not_261_out, OP1, not_262_out);
  and and_39 (and_39_out, not_263_out, not_264_out, OP3, OP2, not_265_out, OP0);
  and and_40 (and_40_out, not_266_out, not_267_out, not_268_out, not_269_out, not_270_out, not_271_out, F5, not_272_out, not_273_out, not_274_out, F1, F0);
  and and_41 (and_41_out, not_275_out, not_276_out, OP3, OP2, OP1, not_277_out);
  or or_1 (S1, and_14_out, and_15_out, and_16_out, and_17_out, and_18_out, and_19_out, and_20_out, and_21_out);
  or or_2 (S3, and_34_out, and_35_out, and_36_out, and_37_out, and_38_out, and_39_out, and_40_out, and_41_out);
  or or_3 (S0, and_1_out, and_2_out, and_3_out, and_4_out, and_5_out, and_6_out, and_7_out, and_8_out, and_9_out, and_10_out, and_11_out, and_12_out, and_13_out);
  or or_4 (S2, and_22_out, and_23_out, and_24_out, and_25_out, and_26_out, and_27_out, and_28_out, and_29_out, and_30_out, and_31_out, and_32_out, and_33_out);
endmodule

// 控制信号生成
module \控制信号自动生成  (
  input  OP0,
  input  OP1,
  input  OP2,
  input  OP3,
  input  OP4,
  input  OP5,
  input  F0,
  input  F1,
  input  F2,
  input  F3,
  input  F4,
  input  F5,
  output MemToReg,
  output MemWrite,
  output ALU_SRC,
  output RegWrite,
  output SysCALL,
  output SignedExt,
  output RegDst,
  output BEQ,
  output BNE,
  output JR,
  output JUMP,
  output JAL,
  output LH,
  output BLTZ
);

  wire and_1_out, and_2_out, and_4_out, and_5_out, and_6_out, and_7_out, and_8_out, and_9_out, and_10_out,
       and_11_out, and_12_out, and_13_out, and_14_out, and_15_out, and_16_out, and_17_out, and_18_out,
       and_19_out, and_20_out, and_21_out, and_22_out, and_23_out, and_24_out, and_25_out, and_26_out,
       and_27_out, and_28_out, and_29_out, and_30_out, and_31_out, and_32_out, and_33_out, and_35_out,
       and_36_out, and_37_out, and_38_out, and_39_out, and_40_out, and_41_out, and_42_out, and_43_out,
       and_44_out, and_45_out, and_46_out, and_47_out, and_48_out, and_49_out, and_50_out, and_51_out,
       and_52_out, and_53_out, and_54_out, and_55_out, not_1_out, not_2_out, not_3_out, not_4_out, not_5_out,
       not_6_out, not_7_out, not_8_out, not_9_out, not_10_out, not_11_out, not_12_out, not_13_out,
       not_14_out, not_15_out, not_16_out, not_17_out, not_18_out, not_19_out, not_20_out, not_21_out,
       not_22_out, not_23_out, not_24_out, not_25_out, not_26_out, not_27_out, not_28_out, not_29_out,
       not_30_out, not_31_out, not_32_out, not_33_out, not_34_out, not_35_out, not_36_out, not_37_out,
       not_38_out, not_39_out, not_40_out, not_41_out, not_42_out, not_43_out, not_44_out, not_45_out,
       not_46_out, not_47_out, not_48_out, not_49_out, not_50_out, not_51_out, not_52_out, not_53_out,
       not_54_out, not_55_out, not_56_out, not_57_out, not_58_out, not_59_out, not_60_out, not_61_out,
       not_62_out, not_63_out, not_64_out, not_65_out, not_66_out, not_67_out, not_68_out, not_69_out,
       not_70_out, not_71_out, not_72_out, not_73_out, not_74_out, not_75_out, not_76_out, not_77_out,
       not_78_out, not_79_out, not_80_out, not_81_out, not_82_out, not_83_out, not_84_out, not_85_out,
       not_86_out, not_87_out, not_88_out, not_89_out, not_90_out, not_91_out, not_92_out, not_93_out,
       not_94_out, not_95_out, not_96_out, not_97_out, not_98_out, not_99_out, not_100_out, not_101_out,
       not_102_out, not_103_out, not_104_out, not_105_out, not_106_out, not_107_out, not_108_out,
       not_109_out, not_110_out, not_111_out, not_112_out, not_113_out, not_114_out, not_115_out,
       not_116_out, not_117_out, not_118_out, not_119_out, not_120_out, not_121_out, not_122_out,
       not_123_out, not_124_out, not_125_out, not_126_out, not_127_out, not_128_out, not_129_out,
       not_130_out, not_131_out, not_132_out, not_133_out, not_134_out, not_135_out, not_136_out,
       not_137_out, not_138_out, not_139_out, not_140_out, not_141_out, not_142_out, not_143_out,
       not_144_out, not_145_out, not_146_out, not_147_out, not_148_out, not_149_out, not_150_out,
       not_151_out, not_152_out, not_153_out, not_154_out, not_155_out, not_156_out, not_157_out,
       not_158_out, not_159_out, not_160_out, not_161_out, not_162_out, not_163_out, not_164_out,
       not_165_out, not_166_out, not_167_out, not_168_out, not_169_out, not_170_out, not_171_out,
       not_172_out, not_173_out, not_174_out, not_175_out, not_176_out, not_177_out, not_178_out,
       not_179_out, not_180_out, not_181_out, not_182_out, not_183_out, not_184_out, not_185_out,
       not_186_out, not_187_out, not_188_out, not_189_out, not_190_out, not_191_out, not_192_out,
       not_193_out, not_194_out, not_195_out, not_196_out, not_197_out, not_198_out, not_199_out,
       not_200_out, not_201_out, not_202_out, not_203_out, not_204_out, not_205_out, not_206_out,
       not_207_out, not_208_out, not_209_out, not_210_out, not_211_out, not_212_out, not_213_out,
       not_214_out, not_215_out, not_216_out, not_217_out, not_218_out, not_219_out, not_220_out,
       not_221_out, not_222_out, not_223_out, not_224_out, not_225_out, not_226_out, not_227_out,
       not_228_out, not_229_out, not_230_out, not_231_out, not_232_out, not_233_out, not_234_out,
       not_235_out, not_236_out, not_237_out, not_238_out, not_239_out, not_240_out, not_241_out,
       not_242_out, not_243_out, not_244_out, not_245_out, not_246_out, not_247_out, not_248_out,
       not_249_out, not_250_out, not_251_out, not_252_out, not_253_out, not_254_out, not_255_out,
       not_256_out, not_257_out, not_258_out, not_259_out, not_260_out, not_261_out, not_262_out,
       not_263_out, not_264_out, not_265_out, not_266_out, not_267_out, not_268_out, not_269_out,
       not_270_out, not_271_out, not_272_out, not_273_out, not_274_out, not_275_out, not_276_out,
       not_277_out, not_278_out, not_279_out, not_280_out, not_281_out, not_282_out, not_283_out,
       not_284_out, not_285_out, not_286_out, not_287_out, not_288_out, not_289_out, not_290_out,
       not_291_out, not_292_out, not_293_out, not_294_out, not_295_out, not_296_out, not_297_out,
       not_298_out, not_299_out, not_300_out, not_301_out, not_302_out, not_303_out, not_304_out,
       not_305_out, not_306_out, not_307_out, not_308_out, not_309_out, not_310_out, not_311_out,
       not_312_out, not_313_out, not_314_out, not_315_out, not_316_out, not_317_out, not_318_out,
       not_319_out, not_320_out, not_321_out, not_322_out, not_323_out, not_324_out, not_325_out,
       not_326_out, not_327_out, not_328_out, not_329_out, not_330_out, not_331_out, not_332_out,
       not_333_out, not_334_out, not_335_out, not_336_out, not_337_out, not_338_out, not_339_out,
       not_340_out, not_341_out, not_342_out, not_343_out, not_344_out, not_345_out, not_346_out,
       not_347_out, not_348_out, not_349_out, not_350_out, not_351_out, not_352_out, not_353_out,
       not_354_out, not_355_out, not_356_out, not_357_out, not_358_out, not_359_out, not_360_out,
       not_361_out, not_362_out, not_363_out, not_364_out, not_365_out, not_366_out, not_367_out,
       not_368_out, not_369_out, not_370_out, not_371_out, not_372_out, not_373_out, not_374_out,
       not_375_out, not_376_out, not_377_out, not_378_out, not_379_out, not_380_out, not_381_out,
       not_382_out, not_383_out, not_384_out, not_385_out, not_386_out, not_387_out, not_388_out,
       not_389_out, not_390_out, not_391_out, not_392_out, not_393_out;

  not not_1 (not_1_out, OP4);
  not not_2 (not_2_out, OP3);
  not not_3 (not_3_out, OP2);
  not not_4 (not_4_out, OP4);
  not not_5 (not_5_out, OP3);
  not not_6 (not_6_out, OP2);
  not not_7 (not_7_out, OP1);
  not not_8 (not_8_out, OP4);
  not not_9 (not_9_out, OP2);
  not not_10 (not_10_out, OP5);
  not not_11 (not_11_out, OP4);
  not not_12 (not_12_out, OP2);
  not not_13 (not_13_out, OP1);
  not not_14 (not_14_out, OP0);
  not not_15 (not_15_out, OP5);
  not not_16 (not_16_out, OP4);
  not not_17 (not_17_out, OP1);
  not not_18 (not_18_out, OP0);
  not not_19 (not_19_out, OP5);
  not not_20 (not_20_out, OP4);
  not not_21 (not_21_out, OP2);
  not not_22 (not_22_out, OP1);
  not not_23 (not_23_out, OP5);
  not not_24 (not_24_out, OP4);
  not not_25 (not_25_out, OP2);
  not not_26 (not_26_out, OP0);
  not not_27 (not_27_out, OP5);
  not not_28 (not_28_out, OP4);
  not not_29 (not_29_out, OP1);
  not not_30 (not_30_out, OP4);
  not not_31 (not_31_out, OP3);
  not not_32 (not_32_out, OP2);
  not not_33 (not_33_out, OP4);
  not not_34 (not_34_out, OP2);
  not not_35 (not_35_out, OP5);
  not not_36 (not_36_out, OP4);
  not not_37 (not_37_out, OP0);
  not not_38 (not_38_out, OP4);
  not not_39 (not_39_out, OP3);
  not not_40 (not_40_out, OP2);
  not not_41 (not_41_out, OP1);
  not not_42 (not_42_out, OP5);
  not not_43 (not_43_out, OP4);
  not not_44 (not_44_out, OP3);
  not not_45 (not_45_out, OP2);
  not not_46 (not_46_out, OP1);
  not not_47 (not_47_out, OP0);
  not not_48 (not_48_out, F5);
  not not_49 (not_49_out, F4);
  not not_50 (not_50_out, F3);
  not not_51 (not_51_out, F2);
  not not_52 (not_52_out, F1);
  not not_53 (not_53_out, F0);
  not not_54 (not_54_out, OP5);
  not not_55 (not_55_out, OP4);
  not not_56 (not_56_out, OP3);
  not not_57 (not_57_out, OP2);
  not not_58 (not_58_out, OP1);
  not not_59 (not_59_out, OP0);
  not not_60 (not_60_out, F5);
  not not_61 (not_61_out, F4);
  not not_62 (not_62_out, F3);
  not not_63 (not_63_out, F2);
  not not_64 (not_64_out, OP5);
  not not_65 (not_65_out, OP4);
  not not_66 (not_66_out, OP3);
  not not_67 (not_67_out, OP2);
  not not_68 (not_68_out, OP1);
  not not_69 (not_69_out, OP0);
  not not_70 (not_70_out, F5);
  not not_71 (not_71_out, F4);
  not not_72 (not_72_out, F3);
  not not_73 (not_73_out, F2);
  not not_74 (not_74_out, F0);
  not not_75 (not_75_out, OP5);
  not not_76 (not_76_out, OP4);
  not not_77 (not_77_out, OP3);
  not not_78 (not_78_out, OP2);
  not not_79 (not_79_out, OP1);
  not not_80 (not_80_out, OP0);
  not not_81 (not_81_out, F4);
  not not_82 (not_82_out, F3);
  not not_83 (not_83_out, F2);
  not not_84 (not_84_out, F1);
  not not_85 (not_85_out, F0);
  not not_86 (not_86_out, OP5);
  not not_87 (not_87_out, OP4);
  not not_88 (not_88_out, OP3);
  not not_89 (not_89_out, OP2);
  not not_90 (not_90_out, OP1);
  not not_91 (not_91_out, OP0);
  not not_92 (not_92_out, F4);
  not not_93 (not_93_out, F3);
  not not_94 (not_94_out, F2);
  not not_95 (not_95_out, F1);
  not not_96 (not_96_out, OP5);
  not not_97 (not_97_out, OP4);
  not not_98 (not_98_out, OP3);
  not not_99 (not_99_out, OP2);
  not not_100 (not_100_out, OP1);
  not not_101 (not_101_out, OP0);
  not not_102 (not_102_out, F4);
  not not_103 (not_103_out, F3);
  not not_104 (not_104_out, F2);
  not not_105 (not_105_out, F0);
  not not_106 (not_106_out, OP5);
  not not_107 (not_107_out, OP4);
  not not_108 (not_108_out, OP3);
  not not_109 (not_109_out, OP2);
  not not_110 (not_110_out, OP1);
  not not_111 (not_111_out, OP0);
  not not_112 (not_112_out, F4);
  not not_113 (not_113_out, F3);
  not not_114 (not_114_out, F1);
  not not_115 (not_115_out, F0);
  not not_116 (not_116_out, OP5);
  not not_117 (not_117_out, OP4);
  not not_118 (not_118_out, OP3);
  not not_119 (not_119_out, OP2);
  not not_120 (not_120_out, OP1);
  not not_121 (not_121_out, OP0);
  not not_122 (not_122_out, F4);
  not not_123 (not_123_out, F3);
  not not_124 (not_124_out, F1);
  not not_125 (not_125_out, OP5);
  not not_126 (not_126_out, OP4);
  not not_127 (not_127_out, OP3);
  not not_128 (not_128_out, OP2);
  not not_129 (not_129_out, OP1);
  not not_130 (not_130_out, OP0);
  not not_131 (not_131_out, F4);
  not not_132 (not_132_out, F3);
  not not_133 (not_133_out, OP5);
  not not_134 (not_134_out, OP4);
  not not_135 (not_135_out, OP3);
  not not_136 (not_136_out, OP2);
  not not_137 (not_137_out, OP1);
  not not_138 (not_138_out, OP0);
  not not_139 (not_139_out, F4);
  not not_140 (not_140_out, F2);
  not not_141 (not_141_out, F0);
  not not_142 (not_142_out, OP5);
  not not_143 (not_143_out, OP4);
  not not_144 (not_144_out, OP3);
  not not_145 (not_145_out, OP2);
  not not_146 (not_146_out, OP1);
  not not_147 (not_147_out, OP0);
  not not_148 (not_148_out, F4);
  not not_149 (not_149_out, F2);
  not not_150 (not_150_out, OP5);
  not not_151 (not_151_out, OP4);
  not not_152 (not_152_out, OP3);
  not not_153 (not_153_out, OP2);
  not not_154 (not_154_out, OP5);
  not not_155 (not_155_out, OP4);
  not not_156 (not_156_out, OP2);
  not not_157 (not_157_out, OP1);
  not not_158 (not_158_out, OP0);
  not not_159 (not_159_out, OP5);
  not not_160 (not_160_out, OP4);
  not not_161 (not_161_out, OP1);
  not not_162 (not_162_out, OP0);
  not not_163 (not_163_out, OP5);
  not not_164 (not_164_out, OP4);
  not not_165 (not_165_out, OP2);
  not not_166 (not_166_out, OP1);
  not not_167 (not_167_out, OP5);
  not not_168 (not_168_out, OP4);
  not not_169 (not_169_out, OP2);
  not not_170 (not_170_out, OP0);
  not not_171 (not_171_out, OP5);
  not not_172 (not_172_out, OP4);
  not not_173 (not_173_out, OP1);
  not not_174 (not_174_out, OP4);
  not not_175 (not_175_out, OP3);
  not not_176 (not_176_out, OP2);
  not not_177 (not_177_out, OP5);
  not not_178 (not_178_out, OP4);
  not not_179 (not_179_out, OP3);
  not not_180 (not_180_out, OP2);
  not not_181 (not_181_out, OP1);
  not not_182 (not_182_out, OP0);
  not not_183 (not_183_out, F4);
  not not_184 (not_184_out, F3);
  not not_185 (not_185_out, F2);
  not not_186 (not_186_out, OP5);
  not not_187 (not_187_out, OP4);
  not not_188 (not_188_out, OP0);
  not not_189 (not_189_out, OP4);
  not not_190 (not_190_out, OP3);
  not not_191 (not_191_out, OP2);
  not not_192 (not_192_out, OP1);
  not not_193 (not_193_out, OP5);
  not not_194 (not_194_out, OP4);
  not not_195 (not_195_out, OP3);
  not not_196 (not_196_out, OP2);
  not not_197 (not_197_out, OP1);
  not not_198 (not_198_out, OP0);
  not not_199 (not_199_out, F5);
  not not_200 (not_200_out, F4);
  not not_201 (not_201_out, F1);
  not not_202 (not_202_out, F0);
  not not_203 (not_203_out, OP5);
  not not_204 (not_204_out, OP4);
  not not_205 (not_205_out, OP3);
  not not_206 (not_206_out, OP1);
  not not_207 (not_207_out, OP0);
  not not_208 (not_208_out, OP5);
  not not_209 (not_209_out, OP4);
  not not_210 (not_210_out, OP3);
  not not_211 (not_211_out, OP1);
  not not_212 (not_212_out, OP5);
  not not_213 (not_213_out, OP4);
  not not_214 (not_214_out, OP2);
  not not_215 (not_215_out, OP1);
  not not_216 (not_216_out, OP0);
  not not_217 (not_217_out, OP5);
  not not_218 (not_218_out, OP4);
  not not_219 (not_219_out, OP2);
  not not_220 (not_220_out, OP1);
  not not_221 (not_221_out, OP5);
  not not_222 (not_222_out, OP4);
  not not_223 (not_223_out, OP2);
  not not_224 (not_224_out, OP0);
  not not_225 (not_225_out, OP4);
  not not_226 (not_226_out, OP3);
  not not_227 (not_227_out, OP2);
  not not_228 (not_228_out, OP4);
  not not_229 (not_229_out, OP2);
  not not_230 (not_230_out, OP4);
  not not_231 (not_231_out, OP3);
  not not_232 (not_232_out, OP2);
  not not_233 (not_233_out, OP1);
  not not_234 (not_234_out, OP5);
  not not_235 (not_235_out, OP4);
  not not_236 (not_236_out, OP3);
  not not_237 (not_237_out, OP2);
  not not_238 (not_238_out, OP1);
  not not_239 (not_239_out, OP5);
  not not_240 (not_240_out, OP4);
  not not_241 (not_241_out, OP3);
  not not_242 (not_242_out, OP2);
  not not_243 (not_243_out, OP1);
  not not_244 (not_244_out, OP0);
  not not_245 (not_245_out, F5);
  not not_246 (not_246_out, F4);
  not not_247 (not_247_out, F3);
  not not_248 (not_248_out, F2);
  not not_249 (not_249_out, F1);
  not not_250 (not_250_out, F0);
  not not_251 (not_251_out, OP5);
  not not_252 (not_252_out, OP4);
  not not_253 (not_253_out, OP3);
  not not_254 (not_254_out, OP2);
  not not_255 (not_255_out, OP1);
  not not_256 (not_256_out, OP0);
  not not_257 (not_257_out, F5);
  not not_258 (not_258_out, F4);
  not not_259 (not_259_out, F3);
  not not_260 (not_260_out, F2);
  not not_261 (not_261_out, OP5);
  not not_262 (not_262_out, OP4);
  not not_263 (not_263_out, OP3);
  not not_264 (not_264_out, OP2);
  not not_265 (not_265_out, OP1);
  not not_266 (not_266_out, OP0);
  not not_267 (not_267_out, F5);
  not not_268 (not_268_out, F4);
  not not_269 (not_269_out, F3);
  not not_270 (not_270_out, F2);
  not not_271 (not_271_out, F0);
  not not_272 (not_272_out, OP5);
  not not_273 (not_273_out, OP4);
  not not_274 (not_274_out, OP3);
  not not_275 (not_275_out, OP2);
  not not_276 (not_276_out, OP1);
  not not_277 (not_277_out, OP0);
  not not_278 (not_278_out, F4);
  not not_279 (not_279_out, F3);
  not not_280 (not_280_out, F2);
  not not_281 (not_281_out, F1);
  not not_282 (not_282_out, F0);
  not not_283 (not_283_out, OP5);
  not not_284 (not_284_out, OP4);
  not not_285 (not_285_out, OP3);
  not not_286 (not_286_out, OP2);
  not not_287 (not_287_out, OP1);
  not not_288 (not_288_out, OP0);
  not not_289 (not_289_out, F4);
  not not_290 (not_290_out, F3);
  not not_291 (not_291_out, F2);
  not not_292 (not_292_out, F1);
  not not_293 (not_293_out, OP5);
  not not_294 (not_294_out, OP4);
  not not_295 (not_295_out, OP3);
  not not_296 (not_296_out, OP2);
  not not_297 (not_297_out, OP1);
  not not_298 (not_298_out, OP0);
  not not_299 (not_299_out, F4);
  not not_300 (not_300_out, F3);
  not not_301 (not_301_out, F2);
  not not_302 (not_302_out, F0);
  not not_303 (not_303_out, OP5);
  not not_304 (not_304_out, OP4);
  not not_305 (not_305_out, OP3);
  not not_306 (not_306_out, OP2);
  not not_307 (not_307_out, OP1);
  not not_308 (not_308_out, OP0);
  not not_309 (not_309_out, F4);
  not not_310 (not_310_out, F3);
  not not_311 (not_311_out, F1);
  not not_312 (not_312_out, F0);
  not not_313 (not_313_out, OP5);
  not not_314 (not_314_out, OP4);
  not not_315 (not_315_out, OP3);
  not not_316 (not_316_out, OP2);
  not not_317 (not_317_out, OP1);
  not not_318 (not_318_out, OP0);
  not not_319 (not_319_out, F4);
  not not_320 (not_320_out, F3);
  not not_321 (not_321_out, F1);
  not not_322 (not_322_out, OP5);
  not not_323 (not_323_out, OP4);
  not not_324 (not_324_out, OP3);
  not not_325 (not_325_out, OP2);
  not not_326 (not_326_out, OP1);
  not not_327 (not_327_out, OP0);
  not not_328 (not_328_out, F4);
  not not_329 (not_329_out, F3);
  not not_330 (not_330_out, OP5);
  not not_331 (not_331_out, OP4);
  not not_332 (not_332_out, OP3);
  not not_333 (not_333_out, OP2);
  not not_334 (not_334_out, OP1);
  not not_335 (not_335_out, OP0);
  not not_336 (not_336_out, F4);
  not not_337 (not_337_out, F2);
  not not_338 (not_338_out, F0);
  not not_339 (not_339_out, OP5);
  not not_340 (not_340_out, OP4);
  not not_341 (not_341_out, OP3);
  not not_342 (not_342_out, OP2);
  not not_343 (not_343_out, OP1);
  not not_344 (not_344_out, OP0);
  not not_345 (not_345_out, F4);
  not not_346 (not_346_out, F2);
  not not_347 (not_347_out, OP5);
  not not_348 (not_348_out, OP4);
  not not_349 (not_349_out, OP3);
  not not_350 (not_350_out, OP2);
  not not_351 (not_351_out, OP1);
  not not_352 (not_352_out, OP0);
  not not_353 (not_353_out, F4);
  not not_354 (not_354_out, F3);
  not not_355 (not_355_out, F2);
  not not_356 (not_356_out, OP5);
  not not_357 (not_357_out, OP4);
  not not_358 (not_358_out, OP3);
  not not_359 (not_359_out, OP1);
  not not_360 (not_360_out, OP0);
  not not_361 (not_361_out, OP5);
  not not_362 (not_362_out, OP4);
  not not_363 (not_363_out, OP3);
  not not_364 (not_364_out, OP1);
  not not_365 (not_365_out, OP5);
  not not_366 (not_366_out, OP4);
  not not_367 (not_367_out, OP3);
  not not_368 (not_368_out, OP2);
  not not_369 (not_369_out, OP1);
  not not_370 (not_370_out, OP0);
  not not_371 (not_371_out, F5);
  not not_372 (not_372_out, F4);
  not not_373 (not_373_out, F2);
  not not_374 (not_374_out, F1);
  not not_375 (not_375_out, F0);
  not not_376 (not_376_out, OP5);
  not not_377 (not_377_out, OP4);
  not not_378 (not_378_out, OP3);
  not not_379 (not_379_out, OP2);
  not not_380 (not_380_out, OP0);
  not not_381 (not_381_out, OP5);
  not not_382 (not_382_out, OP4);
  not not_383 (not_383_out, OP3);
  not not_384 (not_384_out, OP2);
  not not_385 (not_385_out, OP4);
  not not_386 (not_386_out, OP3);
  not not_387 (not_387_out, OP2);
  not not_388 (not_388_out, OP1);
  not not_389 (not_389_out, OP5);
  not not_390 (not_390_out, OP4);
  not not_391 (not_391_out, OP3);
  not not_392 (not_392_out, OP2);
  not not_393 (not_393_out, OP1);
  and and_1 (and_1_out, OP5, not_1_out, not_2_out, not_3_out, OP1, OP0);
  and and_2 (and_2_out, OP5, not_4_out, not_5_out, not_6_out, not_7_out, OP0);
  and and_3 (MemWrite, OP5, not_8_out, OP3, not_9_out, OP1, OP0);
  and and_4 (and_4_out, not_10_out, not_11_out, OP3, not_12_out, not_13_out, not_14_out);
  and and_5 (and_5_out, not_15_out, not_16_out, OP3, OP2, not_17_out, not_18_out);
  and and_6 (and_6_out, not_19_out, not_20_out, OP3, not_21_out, not_22_out, OP0);
  and and_7 (and_7_out, not_23_out, not_24_out, OP3, not_25_out, OP1, not_26_out);
  and and_8 (and_8_out, not_27_out, not_28_out, OP3, OP2, not_29_out, OP0);
  and and_9 (and_9_out, OP5, not_30_out, not_31_out, not_32_out, OP1, OP0);
  and and_10 (and_10_out, OP5, not_33_out, OP3, not_34_out, OP1, OP0);
  and and_11 (and_11_out, not_35_out, not_36_out, OP3, OP2, OP1, not_37_out);
  and and_12 (and_12_out, OP5, not_38_out, not_39_out, not_40_out, not_41_out, OP0);
  and and_13 (and_13_out, not_42_out, not_43_out, not_44_out, not_45_out, not_46_out, not_47_out, not_48_out, not_49_out, not_50_out, not_51_out, not_52_out, not_53_out);
  and and_14 (and_14_out, not_54_out, not_55_out, not_56_out, not_57_out, not_58_out, not_59_out, not_60_out, not_61_out, not_62_out, not_63_out, F1, F0);
  and and_15 (and_15_out, not_64_out, not_65_out, not_66_out, not_67_out, not_68_out, not_69_out, not_70_out, not_71_out, not_72_out, not_73_out, F1, not_74_out);
  and and_16 (and_16_out, not_75_out, not_76_out, not_77_out, not_78_out, not_79_out, not_80_out, F5, not_81_out, not_82_out, not_83_out, not_84_out, not_85_out);
  and and_17 (and_17_out, not_86_out, not_87_out, not_88_out, not_89_out, not_90_out, not_91_out, F5, not_92_out, not_93_out, not_94_out, not_95_out, F0);
  and and_18 (and_18_out, not_96_out, not_97_out, not_98_out, not_99_out, not_100_out, not_101_out, F5, not_102_out, not_103_out, not_104_out, F1, not_105_out);
  and and_19 (and_19_out, not_106_out, not_107_out, not_108_out, not_109_out, not_110_out, not_111_out, F5, not_112_out, not_113_out, F2, not_114_out, not_115_out);
  and and_20 (and_20_out, not_116_out, not_117_out, not_118_out, not_119_out, not_120_out, not_121_out, F5, not_122_out, not_123_out, F2, not_124_out, F0);
  and and_21 (and_21_out, not_125_out, not_126_out, not_127_out, not_128_out, not_129_out, not_130_out, F5, not_131_out, not_132_out, F2, F1, F0);
  and and_22 (and_22_out, not_133_out, not_134_out, not_135_out, not_136_out, not_137_out, not_138_out, F5, not_139_out, F3, not_140_out, F1, not_141_out);
  and and_23 (and_23_out, not_142_out, not_143_out, not_144_out, not_145_out, not_146_out, not_147_out, F5, not_148_out, F3, not_149_out, F1, F0);
  and and_24 (and_24_out, not_150_out, not_151_out, not_152_out, not_153_out, OP1, OP0);
  and and_25 (and_25_out, not_154_out, not_155_out, OP3, not_156_out, not_157_out, not_158_out);
  and and_26 (and_26_out, not_159_out, not_160_out, OP3, OP2, not_161_out, not_162_out);
  and and_27 (and_27_out, not_163_out, not_164_out, OP3, not_165_out, not_166_out, OP0);
  and and_28 (and_28_out, not_167_out, not_168_out, OP3, not_169_out, OP1, not_170_out);
  and and_29 (and_29_out, not_171_out, not_172_out, OP3, OP2, not_173_out, OP0);
  and and_30 (and_30_out, OP5, not_174_out, not_175_out, not_176_out, OP1, OP0);
  and and_31 (and_31_out, not_177_out, not_178_out, not_179_out, not_180_out, not_181_out, not_182_out, F5, not_183_out, not_184_out, not_185_out, F1, F0);
  and and_32 (and_32_out, not_186_out, not_187_out, OP3, OP2, OP1, not_188_out);
  and and_33 (and_33_out, OP5, not_189_out, not_190_out, not_191_out, not_192_out, OP0);
  and and_34 (SysCALL, not_193_out, not_194_out, not_195_out, not_196_out, not_197_out, not_198_out, not_199_out, not_200_out, F3, F2, not_201_out, not_202_out);
  and and_35 (and_35_out, not_203_out, not_204_out, not_205_out, OP2, not_206_out, not_207_out);
  and and_36 (and_36_out, not_208_out, not_209_out, not_210_out, OP2, not_211_out, OP0);
  and and_37 (and_37_out, not_212_out, not_213_out, OP3, not_214_out, not_215_out, not_216_out);
  and and_38 (and_38_out, not_217_out, not_218_out, OP3, not_219_out, not_220_out, OP0);
  and and_39 (and_39_out, not_221_out, not_222_out, OP3, not_223_out, OP1, not_224_out);
  and and_40 (and_40_out, OP5, not_225_out, not_226_out, not_227_out, OP1, OP0);
  and and_41 (and_41_out, OP5, not_228_out, OP3, not_229_out, OP1, OP0);
  and and_42 (and_42_out, OP5, not_230_out, not_231_out, not_232_out, not_233_out, OP0);
  and and_43 (and_43_out, not_234_out, not_235_out, not_236_out, not_237_out, not_238_out, OP0);
  and and_44 (and_44_out, not_239_out, not_240_out, not_241_out, not_242_out, not_243_out, not_244_out, not_245_out, not_246_out, not_247_out, not_248_out, not_249_out, not_250_out);
  and and_45 (and_45_out, not_251_out, not_252_out, not_253_out, not_254_out, not_255_out, not_256_out, not_257_out, not_258_out, not_259_out, not_260_out, F1, F0);
  and and_46 (and_46_out, not_261_out, not_262_out, not_263_out, not_264_out, not_265_out, not_266_out, not_267_out, not_268_out, not_269_out, not_270_out, F1, not_271_out);
  and and_47 (and_47_out, not_272_out, not_273_out, not_274_out, not_275_out, not_276_out, not_277_out, F5, not_278_out, not_279_out, not_280_out, not_281_out, not_282_out);
  and and_48 (and_48_out, not_283_out, not_284_out, not_285_out, not_286_out, not_287_out, not_288_out, F5, not_289_out, not_290_out, not_291_out, not_292_out, F0);
  and and_49 (and_49_out, not_293_out, not_294_out, not_295_out, not_296_out, not_297_out, not_298_out, F5, not_299_out, not_300_out, not_301_out, F1, not_302_out);
  and and_50 (and_50_out, not_303_out, not_304_out, not_305_out, not_306_out, not_307_out, not_308_out, F5, not_309_out, not_310_out, F2, not_311_out, not_312_out);
  and and_51 (and_51_out, not_313_out, not_314_out, not_315_out, not_316_out, not_317_out, not_318_out, F5, not_319_out, not_320_out, F2, not_321_out, F0);
  and and_52 (and_52_out, not_322_out, not_323_out, not_324_out, not_325_out, not_326_out, not_327_out, F5, not_328_out, not_329_out, F2, F1, F0);
  and and_53 (and_53_out, not_330_out, not_331_out, not_332_out, not_333_out, not_334_out, not_335_out, F5, not_336_out, F3, not_337_out, F1, not_338_out);
  and and_54 (and_54_out, not_339_out, not_340_out, not_341_out, not_342_out, not_343_out, not_344_out, F5, not_345_out, F3, not_346_out, F1, F0);
  and and_55 (and_55_out, not_347_out, not_348_out, not_349_out, not_350_out, not_351_out, not_352_out, F5, not_353_out, not_354_out, not_355_out, F1, F0);
  and and_56 (BEQ, not_356_out, not_357_out, not_358_out, OP2, not_359_out, not_360_out);
  and and_57 (BNE, not_361_out, not_362_out, not_363_out, OP2, not_364_out, OP0);
  and and_58 (JR, not_365_out, not_366_out, not_367_out, not_368_out, not_369_out, not_370_out, not_371_out, not_372_out, F3, not_373_out, not_374_out, not_375_out);
  and and_59 (JUMP, not_376_out, not_377_out, not_378_out, not_379_out, OP1, not_380_out);
  and and_60 (JAL, not_381_out, not_382_out, not_383_out, not_384_out, OP1, OP0);
  and and_61 (LH, OP5, not_385_out, not_386_out, not_387_out, not_388_out, OP0);
  and and_62 (BLTZ, not_389_out, not_390_out, not_391_out, not_392_out, not_393_out, OP0);
  or or_1 (MemToReg, and_1_out, and_2_out);
  or or_2 (ALU_SRC, and_4_out, and_5_out, and_6_out, and_7_out, and_8_out, and_9_out, and_10_out, and_11_out, and_12_out);
  or or_3 (SignedExt, and_35_out, and_36_out, and_37_out, and_38_out, and_39_out, and_40_out, and_41_out, and_42_out, and_43_out);
  or or_4 (RegWrite, and_13_out, and_14_out, and_15_out, and_16_out, and_17_out, and_18_out, and_19_out, and_20_out, and_21_out, and_22_out, and_23_out, and_24_out, and_25_out, and_26_out, and_27_out, and_28_out, and_29_out, and_30_out, and_31_out, and_32_out, and_33_out);
  or or_5 (RegDst, and_44_out, and_45_out, and_46_out, and_47_out, and_48_out, and_49_out, and_50_out, and_51_out, and_52_out, and_53_out, and_54_out, and_55_out);
endmodule

// ALU
module MIPS_ALU (
  input  [4:0] shamt,
  input  [31:0] X,
  input  [31:0] Y,
  input  [3:0] AluOP,
  output Equal,
  output [31:0] Result,
  output [31:0] Result_2
);

  wire [0:0] comparator_1_lt, comparator_2_lt;
  wire [31:0] ADD, adder_1_out, adder_2_out, adder_3_out, adder_4_out, adder_5_out, AND_out, divider_1_out,
       divider_1_rem, multiplier_1_cout, multiplier_1_out, negator_1_out, negator_2_out, negator_3_out,
       negator_4_out, negator_5_out, negator_6_out, negator_7_out, negator_8_out, negator_9_out, NOR_out,
       OR_out, shifter_1_out, shifter_2_out, shifter_3_out, subtractor_1_out, subtractor_2_out,
       subtractor_3_out, subtractor_4_out, subtractor_5_out, SUBU, XOR_out;

  assign AND_out = X & Y;  // AND_Gate AND, 32 bits wide
  assign OR_out = X | Y;  // OR_Gate OR, 32 bits wide
  Shifter #(.width(32), .shift("ll")) shifter_1 (.in(Y), .\dist (shamt), .out(shifter_1_out));
  Shifter #(.width(32), .shift("ar")) shifter_2 (.in(Y), .\dist (shamt), .out(shifter_2_out));
  Shifter #(.width(32), .shift("lr")) shifter_3 (.in(Y), .\dist (shamt), .out(shifter_3_out));
  Multiplier #(.width(32)) multiplier_1 (.a(X), .b(Y), .out(multiplier_1_out), .cout(multiplier_1_cout));  // open: cin
  Divider #(.width(32)) divider_1 (.a(X), .b(Y), .out(divider_1_out), .rem(divider_1_rem));  // open: upper
  Adder #(.width(32)) adder_1 (.a(X), .b(Y), .out(adder_1_out));  // open: cin, cout
  Subtractor #(.width(32)) subtractor_1 (.a(X), .b(Y), .out(subtractor_1_out));  // open: bin, bout
  assign XOR_out = X ^ Y;  // XOR_Gate XOR, 32 bits wide
  assign NOR_out = ~(X | Y);  // NOR_Gate NOR, 32 bits wide
  Comparator #(.width(32), .mode("twosComplement")) comparator_1 (
    .a(X), .b(Y), .eq(Equal), .lt(comparator_1_lt[0]));  // open: gt
  Comparator #(.width(32), .mode("unsigned")) comparator_2 (.a(X), .b(Y), .lt(comparator_2_lt[0]));  // open: gt, eq
  Multiplexer #(.select(4), .width(32), .disabled("Z"), .enable("false")) multiplexer_1 (
    .in0(shifter_1_out), .in1(shifter_2_out), .in2(shifter_3_out), .in3(multiplier_1_out),
    .in4(divider_1_out), .in5(adder_1_out), .in6(subtractor_1_out), .in7(AND_out), .in8(OR_out),
    .in9(XOR_out), .in10(NOR_out), .in11({{31{1'b0}}, comparator_1_lt[0]}),
    .in12({{31{1'b0}}, comparator_2_lt[0]}), .in13(ADD), .in14(SUBU), .in15({32{1'b0}}), .out(Result),
    .sel(AluOP));
  Multiplexer #(.select(4), .width(32), .disabled("Z"), .enable("false")) multiplexer_2 (
    .in0({32{1'b0}}), .in1({32{1'b0}}), .in2({32{1'b0}}), .in3(multiplier_1_cout), .in4(divider_1_rem),
    .in5({32{1'b0}}), .in6({32{1'b0}}), .in7({32{1'b0}}), .in8({32{1'b0}}), .in9({32{1'b0}}),
    .in10({32{1'b0}}), .in11({32{1'b0}}), .in12({32{1'b0}}), .in13({32{1'b0}}), .in14({32{1'b0}}),
    .in15({32{1'b0}}), .out(Result_2), .sel(AluOP));
  Negator #(.width(32)) negator_1 (.in(Y), .out(negator_1_out));
  Negator #(.width(32)) negator_2 (.in(X), .out(negator_2_out));
  Negator #(.width(32)) negator_3 (.in(Y), .out(negator_3_out));
  Adder #(.width(32)) adder_2 (.a(X), .b(Y), .out(adder_2_out));  // open: cin, cout
  Negator #(.width(32)) negator_4 (.in(Y), .out(negator_4_out));
  Negator #(.width(32)) negator_5 (.in(X), .out(negator_5_out));
  Negator #(.width(32)) negator_6 (.in(X), .out(negator_6_out));
  Negator #(.width(32)) negator_7 (.in(Y), .out(negator_7_out));
  Subtractor #(.width(32)) subtractor_2 (.a(X), .b(Y), .out(subtractor_2_out));  // open: bin, bout
  Adder #(.width(32)) adder_3 (.a(negator_2_out), .b(Y), .out(adder_3_out));  // open: cin, cout
  Subtractor #(.width(32)) subtractor_3 (.a(negator_3_out), .b(X), .out(subtractor_3_out));  // open: bin, bout
  Subtractor #(.width(32)) subtractor_4 (.a(X), .b(negator_4_out), .out(subtractor_4_out));  // open: bin, bout
  Subtractor #(.width(32)) subtractor_5 (.a(Y), .b(negator_5_out), .out(subtractor_5_out));  // open: bin, bout
  Adder #(.width(32)) adder_4 (.a(negator_6_out), .b(negator_7_out), .out(adder_4_out));  // open: cin, cout
  Adder #(.width(32)) adder_5 (.a(X), .b(negator_1_out), .out(adder_5_out));  // open: cin, cout
  Negator #(.width(32)) negator_8 (.in(adder_3_out), .out(negator_8_out));
  Negator #(.width(32)) negator_9 (.in(adder_4_out), .out(negator_9_out));
  Multiplexer #(.select(2), .width(32), .disabled("Z"), .enable("false")) multiplexer_3 (
    .in0(adder_2_out), .in1(subtractor_4_out), .in2(subtractor_5_out), .in3(negator_9_out), .out(ADD),
    .sel({Y[31], X[31]}));
  Multiplexer #(.select(2), .width(32), .disabled("Z"), .enable("false")) multiplexer_4 (
    .in0(subtractor_2_out), .in1(adder_5_out), .in2(negator_8_out), .in3(subtractor_3_out), .out(SUBU),
    .sel({Y[31], X[31]}));

  // Other names for the same wires on the sheet: Result2[31:0] = Result_2; S[3:0] = AluOP

  // Notes on the sheet:
  //   不要改变此引脚区域内容，也不要改变ALU封装形式
  //   输入引脚
  //   输出引脚
endmodule

module MIPS_Regifile (
  input  [31:0] Din,
  input  Clk,
  input  WE,
  input  [4:0] R1_num,
  input  [4:0] W_num,
  input  [4:0] R2_num,
  output [31:0] R1,
  output [31:0] R2
);

  // RegisterFile registerfile_1: pin names not known; wires that end beside it: Din, Clk, WE, W_num, R1_num, R2_num, R1, R2
endmodule

module \理想流水线  (
  output RegWrite,
  output MemWrite,
  output [31:0] IF_PC,
  output [31:0] ID_PC,
  output [31:0] EX_PC,
  output [31:0] M_PC,
  output [31:0] WB_PC,
  output [31:0] RDin,
  output [31:0] MDin,
  output [31:0] LedData
);

  wire and_1_out, and_2_out, and_3_out, and_4_out, Beq, Bne, CLK, comparator_1_eq, EQU, ex_mem_1_jal_2,
       ex_mem_1_memtoreg_2, ex_mem_1_regwrite_2, ex_mem_1_syscall_2, Go, id_ex_1_alusrcb_2,
       id_ex_1_memtoreg_2, id_ex_1_memwrite_2, id_ex_1_regwrite_2, id_ex_1_syscall_2, IR1, IR2, IR3, J, JAL,
       JR, mem_wb_1_jal_2, mem_wb_1_memtoreg_2, nor_1_out, not_1_out, not_2_out, or_1_out, or_2_out, RST,
       SignedExt, stop, Syscall, W1, W2, W3, \单周期硬布线控制器_1_alu_src , \单周期硬布线控制器_1_beq , \单周期硬布线控制器_1_bne ,
       \单周期硬布线控制器_1_jal , \单周期硬布线控制器_1_jmp , \单周期硬布线控制器_1_jr , \单周期硬布线控制器_1_memtoreg ,
       \单周期硬布线控制器_1_memwrite , \单周期硬布线控制器_1_regdst , \单周期硬布线控制器_1_regwrite , \单周期硬布线控制器_1_syscall ;
  wire [3:0] id_ex_1_aluop_2, \单周期硬布线控制器_1_alu_op ;
  wire [4:0] ex_mem_1_w_num_2, id_ex_1_w_num_2, mem_wb_1_w_num_2, multiplexer_1_out, multiplexer_2_out,
       multiplexer_3_out, multiplexer_4_out;
  wire [15:0] \LoadUse次数 , \总周期数 , \插入气泡数 , \无条件分支数 , \条件分支成功数 ;
  wire [31:0] a0, adder_1_out, adder_2_out, bit_extender_1_out, bit_extender_2_out, controlled_buffer_1_out,
       EX_IR, ex_mem_1_alures_2, ex_mem_1_ir_2, ex_mem_1_pc_4_2, ex_mem_1_r1_2, id_ex_1_ir_2, id_ex_1_pc_4_2,
       id_ex_1_r1_2, id_ex_1_r2_2, id_ex_1_signext_2, ID_IR, if_id_1_ir_2, if_id_1_pc_4_2, IF_IR, MEM_IR,
       mem_wb_1_alures_2, mem_wb_1_memdata_2, mem_wb_1_pc_4_2, mips_alu_1_result, mips_regifile_1_r1,
       mips_regifile_1_r2, multiplexer_5_out, multiplexer_6_out, multiplexer_7_out, multiplexer_8_out,
       ram_1_data, rom_1_data, shifter_1_out, v0, WB_IR;

  Button \u_总复位  (.out(RST));
  Button _1 (.out(IR1));
  Button _2 (.out(IR2));
  Button _3 (.out(IR3));
  // Probe on \总周期数 
  // Probe on \总周期数 
  Button \u_继续运行  (.out(Go));
  LED #(.active("true")) led_1 (.in(W1));
  LED #(.active("true")) led_2 (.in(W2));
  LED #(.active("true")) led_3 (.in(W3));
  nor nor_1 (nor_1_out, JR, or_2_out, or_1_out);
  assign controlled_buffer_1_out = nor_1_out ? adder_1_out : 32'bz;  // Controlled_Buffer controlled_buffer_1
  assign controlled_buffer_1_out = JR ? id_ex_1_r1_2 : 32'bz;  // Controlled_Buffer controlled_buffer_2
  or or_1 (or_1_out, JAL, J);
  Hex_Digit_Display hex_digit_display_1 (.value(LedData[31:28]));  // open: dp
  // Probe on IF_PC[19:0]
  // Mips_Probe mips_probe_1: pin names not known; wires that end beside it: IF_IR
  assign controlled_buffer_1_out = or_2_out ? adder_2_out : 32'bz;  // Controlled_Buffer controlled_buffer_3
  assign controlled_buffer_1_out = or_1_out ? {id_ex_1_pc_4_2[31:28], id_ex_1_ir_2[25:0], 2'b00} : 32'bz;  // Controlled_Buffer controlled_buffer_4
  and and_1 (and_1_out, EQU, Beq);
  not not_1 (not_1_out, EQU);
  Hex_Digit_Display hex_digit_display_2 (.value(LedData[23:20]));  // open: dp
  Hex_Digit_Display hex_digit_display_3 (.value(LedData[27:24]));  // open: dp
  // Probe on ID_PC[19:0]
  // Mips_Probe mips_probe_2: pin names not known; wires that end beside it: ID_IR
  Register #(.width(32), .trigger("rising"), .Select("low")) PC (
    .D(controlled_buffer_1_out), .en(stop), .Q(IF_PC), .clk(CLK));  // open: clr
  or or_2 (or_2_out, and_1_out, and_2_out);
  and and_2 (and_2_out, not_1_out, Bne);
  Hex_Digit_Display hex_digit_display_4 (.value(LedData[19:16]));  // open: dp
  Hex_Digit_Display hex_digit_display_5 (.value(LedData[15:12]));  // open: dp
  Hex_Digit_Display hex_digit_display_6 (.value(LedData[7:4]));  // open: dp
  Hex_Digit_Display hex_digit_display_7 (.value(LedData[11:8]));  // open: dp
  Clock #(.highDuration(1), .lowDuration(1)) clock_1 (.out(CLK));
  // Probe on EX_PC[19:0]
  // Mips_Probe mips_probe_3: pin names not known; wires that end beside it: EX_IR
  Adder #(.width(32)) adder_1 (.a(32'h4), .b(IF_PC), .out(adder_1_out));  // open: cin, cout
  Hex_Digit_Display hex_digit_display_8 (.value(LedData[3:0]));  // open: dp
  ROM #(.addrWidth(10), .dataWidth(32), .Select("high")) rom_1 (.addr(IF_PC[11:2]), .data(rom_1_data));
  // Probe on \总周期数 
  // Probe on M_PC[19:0]
  // Mips_Probe mips_probe_4: pin names not known; wires that end beside it: MEM_IR
  IF_ID if_id_1 (
    .PC_4(adder_1_out), .clk(CLK), .PC_4_2(if_id_1_pc_4_2), .IR(rom_1_data), .IR_2(if_id_1_ir_2), .PC(IF_PC),
    .PC_2(ID_PC), .en(stop), .\清空 (1'b0));
  // Probe on \总周期数 
  // Probe on \无条件分支数 
  // Probe on \条件分支成功数 
  // Probe on \插入气泡数 
  // Probe on \LoadUse次数 
  // Probe on IF_PC[11:0]
  // Probe on WB_PC[19:0]
  // Mips_Probe mips_probe_5: pin names not known; wires that end beside it: WB_IR
  // Probe on ID_PC[11:0]
  // Probe on EX_PC[11:0]
  \单周期硬布线控制器  \u_单周期硬布线控制器_1  (
    .Func(if_id_1_ir_2[5:0]), .OP(if_id_1_ir_2[31:26]), .ALU_OP(\单周期硬布线控制器_1_alu_op ),
    .MemToReg(\单周期硬布线控制器_1_memtoreg ), .MemWrite(\单周期硬布线控制器_1_memwrite ), .ALU_SRC(\单周期硬布线控制器_1_alu_src ),
    .RegWrite(\单周期硬布线控制器_1_regwrite ), .SysCALL(\单周期硬布线控制器_1_syscall ), .SignedExt(SignedExt),
    .RegDst(\单周期硬布线控制器_1_regdst ), .JR(\单周期硬布线控制器_1_jr ), .JMP(\单周期硬布线控制器_1_jmp ), .Beq(\单周期硬布线控制器_1_beq ),
    .JAL(\单周期硬布线控制器_1_jal ), .Bne(\单周期硬布线控制器_1_bne ));  // open: LH, BLTZ
  // Probe on M_PC[11:0]
  Counter #(.width(16), .max('hffff), .ongoal("wrap"), .trigger("rising"), .behavior("new")) counter_1 (
    .count(stop), .Q(\总周期数 ), .clk(CLK));  // open: load, D, carry, clr, preset, down
  Multiplexer #(.select(1), .width(5), .disabled("Z"), .enable("false")) multiplexer_1 (
    .in0(if_id_1_ir_2[25:21]), .in1(5'b00010), .out(multiplexer_1_out), .sel(\单周期硬布线控制器_1_syscall ));
  Multiplexer #(.select(1), .width(5), .disabled("Z"), .enable("false")) multiplexer_2 (
    .in0(if_id_1_ir_2[20:16]), .in1(5'b00100), .out(multiplexer_2_out), .sel(\单周期硬布线控制器_1_syscall ));
  Multiplexer #(.select(1), .width(5), .disabled("Z"), .enable("false")) multiplexer_3 (
    .in0(multiplexer_2_out), .in1(if_id_1_ir_2[15:11]), .out(multiplexer_3_out), .sel(\单周期硬布线控制器_1_regdst ));
  Multiplexer #(.select(1), .width(5), .disabled("Z"), .enable("false")) multiplexer_4 (
    .in0(multiplexer_3_out), .in1({5{1'b1}}), .out(multiplexer_4_out), .sel(\单周期硬布线控制器_1_jal ));
  assign bit_extender_1_out = {{16{1'b0}}, if_id_1_ir_2[15:0]};  // Bit_Extender bit_extender_1
  assign bit_extender_2_out = {{16{if_id_1_ir_2[15]}}, if_id_1_ir_2[15:0]};  // Bit_Extender bit_extender_2
  // Probe on WB_PC[11:0]
  Multiplexer #(.select(1), .width(32), .disabled("Z"), .enable("false")) multiplexer_5 (
    .in0(bit_extender_1_out), .in1(bit_extender_2_out), .out(multiplexer_5_out), .sel(SignedExt));
  MIPS_Regifile mips_regifile_1 (
    .Din(RDin), .Clk(CLK), .R1(mips_regifile_1_r1), .R2(mips_regifile_1_r2), .WE(RegWrite),
    .W_num(mem_wb_1_w_num_2), .R1_num(multiplexer_1_out), .R2_num(multiplexer_2_out));
  ID_EX id_ex_1 (
    .clk(CLK), .PC_4(if_id_1_pc_4_2), .PC_4_2(id_ex_1_pc_4_2), .IR(if_id_1_ir_2), .IR_2(id_ex_1_ir_2),
    .PC(ID_PC), .PC_2(EX_PC), .RegWrite(\单周期硬布线控制器_1_regwrite ), .RegWrite_2(id_ex_1_regwrite_2),
    .W_num(multiplexer_4_out), .W_num_2(id_ex_1_w_num_2), .MemWrite(\单周期硬布线控制器_1_memwrite ),
    .MemWrite_2(id_ex_1_memwrite_2), .AluSrcB(\单周期硬布线控制器_1_alu_src ), .AluSrcB_2(id_ex_1_alusrcb_2),
    .AluOP(\单周期硬布线控制器_1_alu_op ), .AluOP_2(id_ex_1_aluop_2), .MemToReg(\单周期硬布线控制器_1_memtoreg ),
    .MemToReg_2(id_ex_1_memtoreg_2), .Bne(\单周期硬布线控制器_1_bne ), .Bne_2(Bne), .Beq(\单周期硬布线控制器_1_beq ),
    .Beq_2(Beq), .Jmp(\单周期硬布线控制器_1_jmp ), .Jmp_2(J), .Jr(\单周期硬布线控制器_1_jr ), .Jr_2(JR),
    .Jal(\单周期硬布线控制器_1_jal ), .Jal_2(JAL), .R1(mips_regifile_1_r1), .R1_2(id_ex_1_r1_2),
    .R2(mips_regifile_1_r2), .R2_2(id_ex_1_r2_2), .SignExt(multiplexer_5_out), .SignExt_2(id_ex_1_signext_2),
    .Syscall(\单周期硬布线控制器_1_syscall ), .Syscall_2(id_ex_1_syscall_2), .en(stop), .\清空 (1'b0));  // open: LH, LH_2, BLTZ, BLTZ_2
  Multiplexer #(.select(1), .width(32), .disabled("Z"), .enable("false")) multiplexer_6 (
    .in0(id_ex_1_r2_2), .in1(id_ex_1_signext_2), .out(multiplexer_6_out), .sel(id_ex_1_alusrcb_2));
  Comparator #(.width(32), .mode("twosComplement")) comparator_1 (
    .a(v0), .b(32'h22), .eq(comparator_1_eq));  // open: gt, lt
  Shifter #(.width(32), .shift("ll")) shifter_1 (.in(id_ex_1_signext_2), .\dist (5'b00010), .out(shifter_1_out));
  Multiplexer #(.select(1), .width(32), .disabled("Z"), .enable("false")) multiplexer_7 (
    .in0(LedData), .in1(a0), .out(multiplexer_7_out), .sel(and_3_out));
  MIPS_ALU mips_alu_1 (
    .X(id_ex_1_r1_2), .Y(multiplexer_6_out), .AluOP(id_ex_1_aluop_2), .Equal(EQU),
    .Result(mips_alu_1_result), .shamt(id_ex_1_ir_2[10:6]));  // open: Result_2
  Adder #(.width(32)) adder_2 (.a(shifter_1_out), .b(id_ex_1_pc_4_2), .out(adder_2_out));  // open: cin, cout
  not not_2 (not_2_out, comparator_1_eq);
  and and_3 (and_3_out, comparator_1_eq, Syscall);
  Register #(.width(32), .trigger("rising"), .Select("low")) register_1 (
    .D(multiplexer_7_out), .Q(LedData), .clk(CLK));  // open: en, clr
  and and_4 (and_4_out, not_2_out, Syscall);
  not not_3 (stop, and_4_out);
  EX_MEM ex_mem_1 (
    .clk(CLK), .PC(EX_PC), .PC_2(M_PC), .IR(id_ex_1_ir_2), .IR_2(ex_mem_1_ir_2), .PC_4(id_ex_1_pc_4_2),
    .PC_4_2(ex_mem_1_pc_4_2), .RegWrite(id_ex_1_regwrite_2), .RegWrite_2(ex_mem_1_regwrite_2),
    .W_num(id_ex_1_w_num_2), .W_num_2(ex_mem_1_w_num_2), .MemWrite(id_ex_1_memwrite_2),
    .MemWrite_2(MemWrite), .MemToReg(id_ex_1_memtoreg_2), .MemToReg_2(ex_mem_1_memtoreg_2),
    .ALUres(mips_alu_1_result), .ALUres_2(ex_mem_1_alures_2), .R2(id_ex_1_r2_2), .R2_2(MDin), .Jal(JAL),
    .Jal_2(ex_mem_1_jal_2), .en(stop), .Syscall(id_ex_1_syscall_2), .Syscall_2(ex_mem_1_syscall_2),
    .R1(id_ex_1_r1_2), .R1_2(ex_mem_1_r1_2));  // open: LH, LH_2, 清空
  RAM #(.addrWidth(10), .dataWidth(32), .bus("separate"), .Select("high")) ram_1 (
    .addr(ex_mem_1_alures_2[11:2]), .din(MDin), .data(ram_1_data), .str(MemWrite), .clk(CLK));  // open: sel, ld, clr
  MEM_WB mem_wb_1 (
    .clk(CLK), .PC(M_PC), .PC_2(WB_PC), .IR(ex_mem_1_ir_2), .IR_2(WB_IR), .PC_4(ex_mem_1_pc_4_2),
    .PC_4_2(mem_wb_1_pc_4_2), .RegWrite(ex_mem_1_regwrite_2), .RegWrite_2(RegWrite),
    .W_num(ex_mem_1_w_num_2), .W_num_2(mem_wb_1_w_num_2), .MemToReg(ex_mem_1_memtoreg_2),
    .MemToReg_2(mem_wb_1_memtoreg_2), .Jal(ex_mem_1_jal_2), .Jal_2(mem_wb_1_jal_2), .MemData(ram_1_data),
    .MemData_2(mem_wb_1_memdata_2), .ALUres(ex_mem_1_alures_2), .ALUres_2(mem_wb_1_alures_2), .en(stop),
    .Syscall(ex_mem_1_syscall_2), .Syscall_2(Syscall), .R1(ex_mem_1_r1_2), .R1_3(v0), .R2(MDin), .R1_2(a0));  // open: LH片选, LH片选_2, LH, LH_2
  Multiplexer #(.select(1), .width(32), .disabled("Z"), .enable("false")) multiplexer_8 (
    .in0(mem_wb_1_alures_2), .in1(mem_wb_1_memdata_2), .out(multiplexer_8_out), .sel(mem_wb_1_memtoreg_2));
  Multiplexer #(.select(1), .width(32), .disabled("Z"), .enable("false")) multiplexer_9 (
    .in0(multiplexer_8_out), .in1(mem_wb_1_pc_4_2), .out(RDin), .sel(mem_wb_1_jal_2));

  // Other names for the same wires on the sheet: LED[31:0] = LedData; MEM_PC[31:0] = M_PC

  // Notes on the sheet:
  //   中断源
  //   时空图监测，可删除
  //   中断等待指示
  //   数码管输出
  //   指令存储器
  //   contents of rom_1 (hex, n*v repeats v):
  //   20100000 20110000 20120000 20130000 36100000 36310001 36520002 36730003 ae100000 ae110004 ae120008
  //   ae13000c 2002000a 20110000 20120000 20130000 c
  //   IF/ID
  //   OP
  //   指令字
  //   Beq
  //   JMP
  //   JR
  //   Bne
  //   OP
  //   JAL
  //   Func
  //   Syscall
  //   rd
  //   流水调试日志用
  //   MemToReg
  //   MemWrite
  //   AluOP
  //   AluSrcB
  //   RegWrite
  //   RegDst
  //   rs
  //   rt
  //   ID/EX
  //   PC和IR
  //   WB信号
  //   Mem信号
  //   EX信号
  //   为方便自动评测，需要输出流水线各段保存的PC值，注意是PC不是PC+4，另外ID段寄存器写入信息，Mem段内存写入信息也要输出
  //   EX/MEM
  //   MEM/WB
endmodule

module \气泡流水线  (
  output RegWrite,
  output MemWrite,
  output [31:0] IF_PC,
  output [31:0] ID_PC,
  output [31:0] EX_PC,
  output [31:0] M_PC,
  output [31:0] WB_PC,
  output [31:0] RDin,
  output [31:0] MDin,
  output [31:0] LedData
);

  wire and_1_out, and_2_out, and_3_out, and_4_out, and_5_out, and_6_out, and_7_out, and_8_out, and_9_out,
       and_10_out, Beq, BLTZ, Bne, CLK, clock_1_out, comparator_1_eq, comparator_2_eq, comparator_2_lt,
       d_ff_1_q, dataint, EQU, ex_mem_1_jal_2, ex_mem_1_lh_2, ex_mem_1_memtoreg_2, ex_mem_1_regwrite_2,
       ex_mem_1_syscall_2, Go, id_ex_1_alusrcb_2, id_ex_1_lh_2, id_ex_1_memtoreg_2, id_ex_1_memwrite_2,
       id_ex_1_regwrite_2, id_ex_1_syscall_2, IDBLTZ, IDLH, IDSyscall, IR1, IR2, IR3, \ir判断电路_1_out_5 ,
       \ir判断电路_2_out_5 , J, JAL, JR, jumpint, mem_wb_1_jal_2, mem_wb_1_lh_2, \mem_wb_1_lh片选_2 ,
       mem_wb_1_memtoreg_2, nand_1_out, not_1_out, not_2_out, not_3_out, not_4_out, not_5_out, or_2_out,
       or_3_out, or_7_out, RST, SignedExt, stop, Syscall, W1, W2, W3, wutiaojian, youtiaojian,
       \单周期硬布线控制器_1_alu_src , \单周期硬布线控制器_1_beq , \单周期硬布线控制器_1_bne , \单周期硬布线控制器_1_jal , \单周期硬布线控制器_1_jmp ,
       \单周期硬布线控制器_1_jr , \单周期硬布线控制器_1_memtoreg , \单周期硬布线控制器_1_memwrite , \单周期硬布线控制器_1_regdst ,
       \单周期硬布线控制器_1_regwrite ;
  wire [3:0] id_ex_1_aluop_2, \单周期硬布线控制器_1_alu_op ;
  wire [4:0] ex_mem_1_w_num_2, id_ex_1_w_num_2, mem_wb_1_w_num_2, multiplexer_1_out, multiplexer_2_out,
       multiplexer_3_out, multiplexer_4_out;
  wire [12:0] CNT_num;
  wire [15:0] \LoadUse次数 , multiplexer_11_out, \总周期数 , \插入气泡数 , \无条件分支数 , \条件分支成功数 ;
  wire [31:0] a0, adder_1_out, adder_2_out, bit_extender_1_out, bit_extender_2_out, bit_extender_3_out,
       controlled_buffer_1_out, EX_IR, ex_mem_1_alures_2, ex_mem_1_pc_4_2, ex_mem_1_r1_2, id_ex_1_pc_4_2,
       id_ex_1_r1_2, id_ex_1_r2_2, id_ex_1_signext_2, ID_IR, if_id_1_pc_4_2, IF_IR, MEM_IR,
       mem_wb_1_alures_2, mem_wb_1_memdata_2, mem_wb_1_pc_4_2, mips_alu_1_result, mips_regifile_1_r1,
       mips_regifile_1_r2, multiplexer_5_out, multiplexer_6_out, multiplexer_7_out, multiplexer_9_out,
       multiplexer_10_out, ram_1_data, shifter_1_out, v0, WB_IR;

  Button \u_总复位  (.out(RST));
  Button _1 (.out(IR1));
  Button _2 (.out(IR2));
  Button _3 (.out(IR3));
  // Probe on \总周期数 
  // Probe on \总周期数 
  Button \u_继续运行  (.out(Go));
  LED #(.active("true")) led_1 (.in(W1));
  LED #(.active("true")) led_2 (.in(W2));
  LED #(.active("true")) led_3 (.in(W3));
  or or_1 (jumpint, JR, youtiaojian, or_2_out);
  not not_1 (not_1_out, jumpint);
  assign controlled_buffer_1_out = not_1_out ? adder_1_out : 32'bz;  // Controlled_Buffer controlled_buffer_1
  assign controlled_buffer_1_out = JR ? id_ex_1_r1_2 : 32'bz;  // Controlled_Buffer controlled_buffer_2
  or or_2 (or_2_out, JAL, J);
  Hex_Digit_Display hex_digit_display_1 (.value(LedData[31:28]));  // open: dp
  // Probe on IF_PC[19:0]
  // Mips_Probe mips_probe_1: pin names not known; wires that end beside it: IF_IR
  assign controlled_buffer_1_out = youtiaojian ? adder_2_out : 32'bz;  // Controlled_Buffer controlled_buffer_3
  assign controlled_buffer_1_out = or_2_out ? {id_ex_1_pc_4_2[31:28], EX_IR[25:0], 2'b00} : 32'bz;  // Controlled_Buffer controlled_buffer_4
  and and_1 (and_1_out, EQU, Beq);
  not not_2 (not_2_out, EQU);
  Hex_Digit_Display hex_digit_display_2 (.value(LedData[23:20]));  // open: dp
  Hex_Digit_Display hex_digit_display_3 (.value(LedData[27:24]));  // open: dp
  // Probe on ID_PC[19:0]
  // Mips_Probe mips_probe_2: pin names not known; wires that end beside it: ID_IR
  Register #(.width(32), .trigger("rising"), .Select("low")) PC (
    .D(controlled_buffer_1_out), .en(and_4_out), .Q(IF_PC), .clk(CLK));  // open: clr
  or or_3 (or_3_out, and_1_out, and_2_out);
  and and_2 (and_2_out, not_2_out, Bne);
  Hex_Digit_Display hex_digit_display_4 (.value(LedData[15:12]));  // open: dp
  Hex_Digit_Display hex_digit_display_5 (.value(LedData[19:16]));  // open: dp
  or or_4 (wutiaojian, or_2_out, JR);
  and and_3 (and_3_out, BLTZ, v0[31]);
  or or_5 (youtiaojian, and_3_out, or_3_out);
  Hex_Digit_Display hex_digit_display_6 (.value(LedData[11:8]));  // open: dp
  Hex_Digit_Display hex_digit_display_7 (.value(LedData[7:4]));  // open: dp
  // Probe on EX_PC[19:0]
  // Mips_Probe mips_probe_3: pin names not known; wires that end beside it: EX_IR
  not not_3 (not_3_out, dataint);
  and and_4 (and_4_out, not_3_out, stop);
  Adder #(.width(32)) adder_1 (.a(32'h4), .b(IF_PC), .out(adder_1_out));  // open: cin, cout
  Hex_Digit_Display hex_digit_display_8 (.value(LedData[3:0]));  // open: dp
  ROM #(.addrWidth(10), .dataWidth(32), .Select("high")) rom_1 (.addr(IF_PC[11:2]), .data(IF_IR));
  not not_4 (not_4_out, dataint);
  and and_5 (and_5_out, not_4_out, stop);
  // Probe on \总周期数 
  // Probe on M_PC[19:0]
  // Mips_Probe mips_probe_4: pin names not known; wires that end beside it: MEM_IR
  IF_ID if_id_1 (
    .PC_4(adder_1_out), .clk(CLK), .PC_4_2(if_id_1_pc_4_2), .IR(IF_IR), .IR_2(ID_IR), .PC(IF_PC),
    .PC_2(ID_PC), .en(and_5_out), .\清空 (jumpint));
  // Probe on \总周期数 
  // Probe on \无条件分支数 
  // Probe on \条件分支成功数 
  // Probe on \插入气泡数 
  // Probe on \LoadUse次数 
  // Probe on IF_PC[11:0]
  // Probe on WB_PC[19:0]
  // Mips_Probe mips_probe_5: pin names not known; wires that end beside it: WB_IR
  // Probe on ID_PC[11:0]
  // Probe on EX_PC[11:0]
  \单周期硬布线控制器  \u_单周期硬布线控制器_1  (
    .Func(ID_IR[5:0]), .OP(ID_IR[31:26]), .ALU_OP(\单周期硬布线控制器_1_alu_op ), .MemToReg(\单周期硬布线控制器_1_memtoreg ),
    .MemWrite(\单周期硬布线控制器_1_memwrite ), .ALU_SRC(\单周期硬布线控制器_1_alu_src ), .RegWrite(\单周期硬布线控制器_1_regwrite ),
    .SysCALL(IDSyscall), .SignedExt(SignedExt), .RegDst(\单周期硬布线控制器_1_regdst ), .JR(\单周期硬布线控制器_1_jr ),
    .JMP(\单周期硬布线控制器_1_jmp ), .Beq(\单周期硬布线控制器_1_beq ), .JAL(\单周期硬布线控制器_1_jal ), .Bne(\单周期硬布线控制器_1_bne ),
    .LH(IDLH), .BLTZ(IDBLTZ));
  // Probe on M_PC[11:0]
  Counter #(.width(16), .max('hffff), .ongoal("wrap"), .trigger("rising"), .behavior("new")) counter_1 (
    .count(stop), .Q(\总周期数 ), .clk(CLK));  // open: load, D, carry, clr, preset, down
  Multiplexer #(.select(1), .width(5), .disabled("Z"), .enable("false")) multiplexer_1 (
    .in0(ID_IR[25:21]), .in1(5'b00010), .out(multiplexer_1_out), .sel(IDSyscall));
  Multiplexer #(.select(1), .width(5), .disabled("Z"), .enable("false")) multiplexer_2 (
    .in0(ID_IR[20:16]), .in1(5'b00100), .out(multiplexer_2_out), .sel(IDSyscall));
  Multiplexer #(.select(1), .width(5), .disabled("Z"), .enable("false")) multiplexer_3 (
    .in0(multiplexer_2_out), .in1(ID_IR[15:11]), .out(multiplexer_3_out), .sel(\单周期硬布线控制器_1_regdst ));
  Multiplexer #(.select(1), .width(5), .disabled("Z"), .enable("false")) multiplexer_4 (
    .in0(multiplexer_3_out), .in1({5{1'b1}}), .out(multiplexer_4_out), .sel(\单周期硬布线控制器_1_jal ));
  assign bit_extender_1_out = {{16{1'b0}}, ID_IR[15:0]};  // Bit_Extender bit_extender_1
  assign bit_extender_2_out = {{16{ID_IR[15]}}, ID_IR[15:0]};  // Bit_Extender bit_extender_2
  \IR判断电路  \ir判断电路_1  (.\被比较IR (ID_IR), .\比较IR (EX_IR), .out_5(\ir判断电路_1_out_5 ), .Syscall(IDSyscall));  // open: BA
  \IR判断电路  \ir判断电路_2  (.\被比较IR (ID_IR), .\比较IR (MEM_IR), .out_5(\ir判断电路_2_out_5 ), .Syscall(IDSyscall));  // open: BA
  // Probe on WB_PC[11:0]
  Multiplexer #(.select(1), .width(32), .disabled("Z"), .enable("false")) multiplexer_5 (
    .in0(bit_extender_1_out), .in1(bit_extender_2_out), .out(multiplexer_5_out), .sel(SignedExt));
  MIPS_Regifile mips_regifile_1 (
    .Din(RDin), .Clk(CLK), .R1(mips_regifile_1_r1), .R2(mips_regifile_1_r2), .WE(RegWrite),
    .W_num(mem_wb_1_w_num_2), .R1_num(multiplexer_1_out), .R2_num(multiplexer_2_out));
  and and_6 (and_6_out, dataint, stop);
  Counter #(.width(16), .max('hffff), .ongoal("wrap"), .trigger("rising"), .behavior("new")) counter_2 (
    .count(and_6_out), .Q(\插入气泡数 ), .clk(CLK));  // open: load, D, carry, clr, preset, down
  and and_7 (and_7_out, wutiaojian, stop);
  Counter #(.width(16), .max('hffff), .ongoal("wrap"), .trigger("rising"), .behavior("new")) counter_3 (
    .count(and_7_out), .Q(\无条件分支数 ), .clk(CLK));  // open: load, D, carry, clr, preset, down
  or or_6 (dataint, \ir判断电路_1_out_5 , \ir判断电路_2_out_5 );
  and and_8 (and_8_out, youtiaojian, stop);
  Counter #(.width(16), .max('hffff), .ongoal("wrap"), .trigger("rising"), .behavior("new")) counter_4 (
    .count(and_8_out), .Q(\条件分支成功数 ), .clk(CLK));  // open: load, D, carry, clr, preset, down
  ID_EX id_ex_1 (
    .clk(CLK), .PC_4(if_id_1_pc_4_2), .PC_4_2(id_ex_1_pc_4_2), .IR(ID_IR), .IR_2(EX_IR), .PC(ID_PC),
    .PC_2(EX_PC), .RegWrite(\单周期硬布线控制器_1_regwrite ), .RegWrite_2(id_ex_1_regwrite_2),
    .W_num(multiplexer_4_out), .W_num_2(id_ex_1_w_num_2), .MemWrite(\单周期硬布线控制器_1_memwrite ),
    .MemWrite_2(id_ex_1_memwrite_2), .AluSrcB(\单周期硬布线控制器_1_alu_src ), .AluSrcB_2(id_ex_1_alusrcb_2),
    .AluOP(\单周期硬布线控制器_1_alu_op ), .AluOP_2(id_ex_1_aluop_2), .MemToReg(\单周期硬布线控制器_1_memtoreg ),
    .MemToReg_2(id_ex_1_memtoreg_2), .Bne(\单周期硬布线控制器_1_bne ), .Bne_2(Bne), .Beq(\单周期硬布线控制器_1_beq ),
    .Beq_2(Beq), .Jmp(\单周期硬布线控制器_1_jmp ), .Jmp_2(J), .Jr(\单周期硬布线控制器_1_jr ), .Jr_2(JR),
    .Jal(\单周期硬布线控制器_1_jal ), .Jal_2(JAL), .R1(mips_regifile_1_r1), .R1_2(id_ex_1_r1_2),
    .R2(mips_regifile_1_r2), .R2_2(id_ex_1_r2_2), .SignExt(multiplexer_5_out), .SignExt_2(id_ex_1_signext_2),
    .Syscall(IDSyscall), .Syscall_2(id_ex_1_syscall_2), .en(stop), .\清空 (or_7_out), .LH(IDLH),
    .LH_2(id_ex_1_lh_2), .BLTZ(IDBLTZ), .BLTZ_2(BLTZ));
  or or_7 (or_7_out, jumpint, dataint);
  Comparator #(.width(32), .mode("twosComplement")) comparator_1 (
    .a(v0), .b(32'h22), .eq(comparator_1_eq));  // open: gt, lt
  Multiplexer #(.select(1), .width(32), .disabled("Z"), .enable("false")) multiplexer_6 (
    .in0(LedData), .in1(a0), .out(multiplexer_6_out), .sel(and_9_out));
  Multiplexer #(.select(1), .width(32), .disabled("Z"), .enable("false")) multiplexer_7 (
    .in0(id_ex_1_r2_2), .in1(id_ex_1_signext_2), .out(multiplexer_7_out), .sel(id_ex_1_alusrcb_2));
  not not_5 (not_5_out, comparator_1_eq);
  and and_9 (and_9_out, comparator_1_eq, Syscall);
  Register #(.width(32), .trigger("rising"), .Select("low")) register_1 (
    .D(multiplexer_6_out), .Q(LedData), .clk(CLK));  // open: en, clr
  MIPS_ALU mips_alu_1 (
    .X(id_ex_1_r1_2), .Y(multiplexer_7_out), .AluOP(id_ex_1_aluop_2), .Equal(EQU),
    .Result(mips_alu_1_result), .shamt(EX_IR[10:6]));  // open: Result_2
  Shifter #(.width(32), .shift("ll")) shifter_1 (.in(id_ex_1_signext_2), .\dist (5'b00010), .out(shifter_1_out));
  Adder #(.width(32)) adder_2 (.a(shifter_1_out), .b(id_ex_1_pc_4_2), .out(adder_2_out));  // open: cin, cout
  and and_10 (and_10_out, not_5_out, Syscall);
  not not_6 (stop, and_10_out);
  EX_MEM ex_mem_1 (
    .clk(CLK), .PC(EX_PC), .PC_2(M_PC), .IR(EX_IR), .IR_2(MEM_IR), .PC_4(id_ex_1_pc_4_2),
    .PC_4_2(ex_mem_1_pc_4_2), .RegWrite(id_ex_1_regwrite_2), .RegWrite_2(ex_mem_1_regwrite_2),
    .W_num(id_ex_1_w_num_2), .W_num_2(ex_mem_1_w_num_2), .MemWrite(id_ex_1_memwrite_2),
    .MemWrite_2(MemWrite), .MemToReg(id_ex_1_memtoreg_2), .MemToReg_2(ex_mem_1_memtoreg_2),
    .ALUres(mips_alu_1_result), .ALUres_2(ex_mem_1_alures_2), .R2(id_ex_1_r2_2), .R2_2(MDin), .Jal(JAL),
    .Jal_2(ex_mem_1_jal_2), .en(stop), .Syscall(id_ex_1_syscall_2), .Syscall_2(ex_mem_1_syscall_2),
    .LH(id_ex_1_lh_2), .LH_2(ex_mem_1_lh_2), .R1(id_ex_1_r1_2), .R1_2(ex_mem_1_r1_2), .\清空 (1'b0));
  RAM #(.addrWidth(10), .dataWidth(32), .bus("separate"), .Select("high")) ram_1 (
    .addr(ex_mem_1_alures_2[11:2]), .din(MDin), .data(ram_1_data), .str(MemWrite), .clk(CLK));  // open: sel, ld, clr
  MEM_WB mem_wb_1 (
    .clk(CLK), .PC(M_PC), .PC_2(WB_PC), .IR(MEM_IR), .IR_2(WB_IR), .PC_4(ex_mem_1_pc_4_2),
    .PC_4_2(mem_wb_1_pc_4_2), .RegWrite(ex_mem_1_regwrite_2), .RegWrite_2(RegWrite),
    .W_num(ex_mem_1_w_num_2), .W_num_2(mem_wb_1_w_num_2), .MemToReg(ex_mem_1_memtoreg_2),
    .MemToReg_2(mem_wb_1_memtoreg_2), .Jal(ex_mem_1_jal_2), .Jal_2(mem_wb_1_jal_2), .MemData(ram_1_data),
    .MemData_2(mem_wb_1_memdata_2), .ALUres(ex_mem_1_alures_2), .ALUres_2(mem_wb_1_alures_2), .en(stop),
    .Syscall(ex_mem_1_syscall_2), .Syscall_2(Syscall), .\LH片选 (ex_mem_1_alures_2[1]),
    .\LH片选_2 (\mem_wb_1_lh片选_2 ), .LH(ex_mem_1_lh_2), .LH_2(mem_wb_1_lh_2), .R1(ex_mem_1_r1_2), .R1_3(v0),
    .R2(MDin), .R1_2(a0));
  D_Flip_Flop #(.trigger("high"), .Pre_Clr_Positions("LEGACY"), .NegatePresetClear("false"), .enable("true"), .NewFFLayout("false")) d_ff_1 (.Q(d_ff_1_q));  // open: clk, D, Qn, preset, en, reset
  // Probe on 13'h374
  Clock #(.highDuration(1), .lowDuration(1)) clock_1 (.out(clock_1_out));
  Multiplexer #(.select(1), .width(32), .disabled("Z"), .enable("false")) multiplexer_8 (
    .in0(multiplexer_9_out), .in1(mem_wb_1_pc_4_2), .out(RDin), .sel(mem_wb_1_jal_2));
  Comparator #(.width(13), .mode("twosComplement")) comparator_2 (
    .a(CNT_num), .b(13'h374), .eq(comparator_2_eq), .lt(comparator_2_lt));  // open: gt
  Multiplexer #(.select(1), .width(32), .disabled("Z"), .enable("false")) multiplexer_9 (
    .in0(mem_wb_1_alures_2), .in1(multiplexer_10_out), .out(multiplexer_9_out), .sel(mem_wb_1_memtoreg_2));
  nand nand_1 (nand_1_out, d_ff_1_q, comparator_2_eq);
  Counter #(.width(13), .max('h1fff), .ongoal("stay"), .trigger("rising"), .behavior("old")) counter_5 (
    .count(comparator_2_lt), .Q(CNT_num), .clk(clock_1_out));  // open: load, D, carry, clr, preset
  Multiplexer #(.select(1), .width(32), .disabled("Z"), .enable("false")) multiplexer_10 (
    .in0(mem_wb_1_memdata_2), .in1(bit_extender_3_out), .out(multiplexer_10_out), .sel(mem_wb_1_lh_2));
  assign CLK = nand_1_out ? clock_1_out : 1'bz;  // Controlled_Buffer controlled_buffer_5
  Pull_Resistor #(.pull(1)) pull_resistor_1 (.node(CLK));
  assign bit_extender_3_out = {{16{multiplexer_11_out[15]}}, multiplexer_11_out};  // Bit_Extender bit_extender_3
  Multiplexer #(.select(1), .width(16), .disabled("Z"), .enable("false")) multiplexer_11 (
    .in0(mem_wb_1_memdata_2[15:0]), .in1(mem_wb_1_memdata_2[31:16]), .out(multiplexer_11_out),
    .sel(\mem_wb_1_lh片选_2 ));

  // Other names for the same wires on the sheet: LED[31:0] = LedData; MEM_PC[31:0] = M_PC

  // Notes on the sheet:
  //   中断源
  //   时空图监测，可删除
  //   中断等待指示
  //   数码管输出
  //   指令存储器
  //   contents of rom_1 (hex, n*v repeats v):
  //   20110001 8000c05 20110001 20120002 20130003 8000c09 20110001 20120002 20130003 8000c0d 20110001
  //   20120002 20130003 8000c11 20110001 20120002 20130003 c000cb8 20100001 20110001 118fc0 112020
  //   20020022 c 118882 12200001 8000c15 112020 20020022 c 20110001 118880 112020 20020022 c 12200001
  //   8000c1f 20110001 118fc0 112020 20020022 c 1188c3 112020 20020022 c 118903 112020 20020022 c 118903
  //   112020 20020022 c 118903 112020 20020022 c 118903 112020 20020022 c 118903 112020 20020022 c 118903
  //   112020 20020022 c 118903 112020 20020022 c 20100001 109fc0 139fc3 8021 2012000c 24160003 26100001
  //   3210000f 20080008 20090001 139900 2709825 132020 20020022 c 1094022 1500fff9 22100001 2018000f
  //   2188024 108700 20080008 20090001 139902 2709825 132021 20020022 c 1094022 1500fff9 108702 2c9b022
  //   12c00001 8000c50 4020 1084027 84400 3508ffff 82021 20020022 c 2010ffff 20110000 ae300000 22100001
  //   22310004 ae300000 22100001 22310004 ae300000 22100001 22310004 ae300000 22100001 22310004 ae300000
  //   22100001 22310004 ae300000 22100001 22310004 ae300000 22100001 22310004 ae300000 22100001 22310004
  //   ae300000 22100001 22310004 ae300000 22100001 22310004 ae300000 22100001 22310004 ae300000 22100001
  //   22310004 ae300000 22100001 22310004 ae300000 22100001 22310004 ae300000 22100001 22310004 ae300000
  //   22100001 22310004 22100001 8020 2011003c 8e130000 8e340000 274402a 11000002 ae330000 ae140000
  //   2231fffc 1611fff8 102020 20020022 c 22100004 2011003c 1611fff2 20020032 c 20100000 22100001 102020
  //   20020022 c 22100002 102020 20020022 c 22100003 102020 20020022 c 22100004 102020 20020022 c 22100005
  //   102020 20020022 c 22100006 102020 20020022 c 22100007 102020 20020022 c 22100008 102020 20020022
  //   20020022 c 3e00008
  //   IF/ID
  //   OP
  //   指令字
  //   Beq
  //   JMP
  //   JR
  //   Bne
  //   OP
  //   JAL
  //   Func
  //   Syscall
  //   rd
  //   流水调试日志用
  //   MemToReg
  //   MemWrite
  //   AluOP
  //   AluSrcB
  //   RegWrite
  //   RegDst
  //   rs
  //   rt
  //   ID/EX
  //   PC和IR
  //   WB信号
  //   Mem信号
  //   EX信号
  //   为方便自动评测，需要输出流水线各段保存的PC值，注意是PC不是PC+4，另外ID段寄存器写入信息，Mem段内存写入信息也要输出
  //   EX/MEM
  //   控制位
  //   暂停节拍，不能为0
  //   MEM/WB
  //   戳工具置1进入计数暂停模式，ctrl+k时钟自动运行到对应节拍暂停
  //   ctrl+k关闭时钟连续运行，将控制位置零，进入单步调试模式调试
  //   用这个时钟源需要去掉电路中的其他时钟源
  //   可计数暂停的时钟源
endmodule
module \重定向流水线  (
  output RegWrite,
  output MemWrite,
  output [31:0] IF_PC,
  output [31:0] ID_PC,
  output [31:0] EX_PC,
  output [31:0] M_PC,
  output [31:0] WB_PC,
  output [31:0] RDin,
  output [31:0] MDin,
  output [31:0] LedData
);

  wire and_1_out, and_2_out, and_3_out, and_4_out, and_5_out, and_6_out, and_7_out, and_9_out, and_10_out,
       and_11_out, Beq, BLTZ, Bne, CLK, clock_1_out, comparator_1_eq, comparator_2_eq, comparator_2_lt,
       d_ff_1_q, EQU, ex_mem_1_jal_2, ex_mem_1_lh_2, ex_mem_1_regwrite_2, ex_mem_1_syscall_2, EXMemWrite,
       EXSyscall, Go, id_ex_1_alusrcb_2, id_ex_1_lh_2, id_ex_1_memwrite_2, id_ex_1_regwrite_2, IDBLTZ, IDLH,
       IDSyscall, IR1, IR2, IR3, \ir判断电路_1_out_5 , J, JAL, JR, jumpint, LoadUse, mem_wb_1_jal_2,
       mem_wb_1_lh_2, \mem_wb_1_lh片选_2 , MEMMemWrite, nand_1_out, not_1_out, not_2_out, not_3_out, not_4_out,
       not_5_out, not_7_out, not_8_out, or_2_out, or_5_out, or_6_out, or_7_out, RST, SignedExt, stop,
       Syscall, W1, W2, W3, WBMemWrite, wutiaojian, youtiaojian, \单周期硬布线控制器_1_alu_src , \单周期硬布线控制器_1_beq ,
       \单周期硬布线控制器_1_bne , \单周期硬布线控制器_1_jal , \单周期硬布线控制器_1_jmp , \单周期硬布线控制器_1_jr , \单周期硬布线控制器_1_memtoreg ,
       \单周期硬布线控制器_1_memwrite , \单周期硬布线控制器_1_regdst , \单周期硬布线控制器_1_regwrite , \重定向判断电路_1_out_5 ,
       \重定向判断电路_2_out_5 ;
  wire [1:0] A2A1, B2B1, multiplexer_10_out, multiplexer_11_out, multiplexer_12_out, multiplexer_14_out,
       multiplexer_15_out, multiplexer_16_out, SA, SB;
  wire [2:0] and_12_out;
  wire [3:0] id_ex_1_aluop_2, \单周期硬布线控制器_1_alu_op ;
  wire [4:0] ex_mem_1_w_num_2, id_ex_1_w_num_2, mem_wb_1_w_num_2, multiplexer_1_out, multiplexer_2_out,
       multiplexer_3_out, multiplexer_4_out;
  wire [12:0] CNT_num;
  wire [15:0] \LoadUse次数 , multiplexer_21_out, \总周期数 , \插入气泡数 , \无条件分支数 , \条件分支成功数 ;
  wire [31:0] a0, adder_1_out, adder_2_out, bit_extender_1_out, bit_extender_2_out, bit_extender_3_out,
       controlled_buffer_1_out, EX_IR, ex_mem_1_alures_2, ex_mem_1_pc_4_2, ex_mem_1_r1_2, id_ex_1_pc_4_2,
       id_ex_1_r1_2, id_ex_1_r2_2, id_ex_1_signext_2, ID_IR, if_id_1_pc_4_2, IF_IR, MEM_IR,
       mem_wb_1_alures_2, mem_wb_1_memdata_2, mem_wb_1_pc_4_2, mips_alu_1_result, mips_regifile_1_r1,
       mips_regifile_1_r2, multiplexer_5_out, multiplexer_6_out, multiplexer_7_out, multiplexer_8_out,
       multiplexer_9_out, multiplexer_18_out, multiplexer_20_out, ram_1_data, shifter_1_out, v0, WB_IR;

  Button \u_总复位  (.out(RST));
  Button _1 (.out(IR1));
  Button _2 (.out(IR2));
  Button _3 (.out(IR3));
  // Probe on \总周期数 
  // Probe on \总周期数 
  Button \u_继续运行  (.out(Go));
  LED #(.active("true")) led_1 (.in(W1));
  LED #(.active("true")) led_2 (.in(W2));
  LED #(.active("true")) led_3 (.in(W3));
  Hex_Digit_Display hex_digit_display_1 (.value(LedData[31:28]));  // open: dp
  // Probe on IF_PC[19:0]
  // Mips_Probe mips_probe_1: pin names not known; wires that end beside it: IF_IR
  Hex_Digit_Display hex_digit_display_2 (.value(LedData[27:24]));  // open: dp
  Hex_Digit_Display hex_digit_display_3 (.value(LedData[23:20]));  // open: dp
  // Probe on ID_PC[19:0]
  // Mips_Probe mips_probe_2: pin names not known; wires that end beside it: ID_IR
  Hex_Digit_Display hex_digit_display_4 (.value(LedData[15:12]));  // open: dp
  Hex_Digit_Display hex_digit_display_5 (.value(LedData[19:16]));  // open: dp
  not not_1 (not_1_out, jumpint);
  or or_1 (jumpint, JR, youtiaojian, or_2_out);
  assign controlled_buffer_1_out = not_1_out ? adder_1_out : 32'bz;  // Controlled_Buffer controlled_buffer_1
  assign controlled_buffer_1_out = JR ? multiplexer_7_out : 32'bz;  // Controlled_Buffer controlled_buffer_2
  Hex_Digit_Display hex_digit_display_6 (.value(LedData[7:4]));  // open: dp
  Hex_Digit_Display hex_digit_display_7 (.value(LedData[11:8]));  // open: dp
  // Probe on EX_PC[19:0]
  // Mips_Probe mips_probe_3: pin names not known; wires that end beside it: EX_IR
  assign controlled_buffer_1_out = youtiaojian ? adder_2_out : 32'bz;  // Controlled_Buffer controlled_buffer_3
  or or_2 (or_2_out, JAL, J);
  assign controlled_buffer_1_out = or_2_out ? {id_ex_1_pc_4_2[31:28], EX_IR[25:0], 2'b00} : 32'bz;  // Controlled_Buffer controlled_buffer_4
  and and_1 (and_1_out, EQU, Beq);
  not not_2 (not_2_out, EQU);
  Hex_Digit_Display hex_digit_display_8 (.value(LedData[3:0]));  // open: dp
  and and_2 (and_2_out, not_2_out, Bne);
  // Probe on \总周期数 
  // Probe on M_PC[19:0]
  // Mips_Probe mips_probe_4: pin names not known; wires that end beside it: MEM_IR
  Register #(.width(32), .trigger("rising"), .Select("low")) PC (
    .D(controlled_buffer_1_out), .en(and_4_out), .Q(IF_PC), .clk(CLK));  // open: clr
  or or_3 (wutiaojian, or_2_out, JR);
  and and_3 (and_3_out, BLTZ, v0[31]);
  or or_4 (youtiaojian, and_3_out, or_5_out);
  or or_5 (or_5_out, and_1_out, and_2_out);
  // Probe on \总周期数 
  // Probe on \无条件分支数 
  // Probe on \条件分支成功数 
  // Probe on \插入气泡数 
  // Probe on \LoadUse次数 
  and and_4 (and_4_out, not_3_out, stop);
  Adder #(.width(32)) adder_1 (.a(32'h4), .b(IF_PC), .out(adder_1_out));  // open: cin, cout
  // Probe on IF_PC[11:0]
  // Probe on WB_PC[19:0]
  // Mips_Probe mips_probe_5: pin names not known; wires that end beside it: WB_IR
  not not_3 (not_3_out, LoadUse);
  ROM #(.addrWidth(10), .dataWidth(32), .Select("high")) rom_1 (.addr(IF_PC[11:2]), .data(IF_IR));
  not not_4 (not_4_out, LoadUse);
  // Probe on ID_PC[11:0]
  // Probe on EX_PC[11:0]
  and and_5 (and_5_out, not_4_out, stop);
  // Probe on M_PC[11:0]
  Counter #(.width(16), .max('hffff), .ongoal("wrap"), .trigger("rising"), .behavior("new")) counter_1 (
    .count(stop), .Q(\总周期数 ), .clk(CLK));  // open: load, D, carry, clr, preset, down
  IF_ID if_id_1 (
    .PC_4(adder_1_out), .clk(CLK), .PC_4_2(if_id_1_pc_4_2), .IR(IF_IR), .IR_2(ID_IR), .PC(IF_PC),
    .PC_2(ID_PC), .en(and_5_out), .\清空 (jumpint));
  // Probe on WB_PC[11:0]
  \IR判断电路  \ir判断电路_1  (.\被比较IR (ID_IR), .\比较IR (EX_IR), .out_5(\ir判断电路_1_out_5 ), .Syscall(IDSyscall));  // open: BA
  and and_6 (and_6_out, wutiaojian, stop);
  Counter #(.width(16), .max('hffff), .ongoal("wrap"), .trigger("rising"), .behavior("new")) counter_2 (
    .count(and_6_out), .Q(\无条件分支数 ), .clk(CLK));  // open: load, D, carry, clr, preset, down
  \单周期硬布线控制器  \u_单周期硬布线控制器_1  (
    .Func(ID_IR[5:0]), .OP(ID_IR[31:26]), .ALU_OP(\单周期硬布线控制器_1_alu_op ), .MemToReg(\单周期硬布线控制器_1_memtoreg ),
    .MemWrite(\单周期硬布线控制器_1_memwrite ), .ALU_SRC(\单周期硬布线控制器_1_alu_src ), .RegWrite(\单周期硬布线控制器_1_regwrite ),
    .SysCALL(IDSyscall), .SignedExt(SignedExt), .RegDst(\单周期硬布线控制器_1_regdst ), .JR(\单周期硬布线控制器_1_jr ),
    .JMP(\单周期硬布线控制器_1_jmp ), .Beq(\单周期硬布线控制器_1_beq ), .JAL(\单周期硬布线控制器_1_jal ), .Bne(\单周期硬布线控制器_1_bne ),
    .LH(IDLH), .BLTZ(IDBLTZ));
  Multiplexer #(.select(1), .width(5), .disabled("Z"), .enable("false")) multiplexer_1 (
    .in0(ID_IR[25:21]), .in1(5'b00010), .out(multiplexer_1_out), .sel(IDSyscall));
  Multiplexer #(.select(1), .width(5), .disabled("Z"), .enable("false")) multiplexer_2 (
    .in0(ID_IR[20:16]), .in1(5'b00100), .out(multiplexer_2_out), .sel(IDSyscall));
  Multiplexer #(.select(1), .width(5), .disabled("Z"), .enable("false")) multiplexer_3 (
    .in0(multiplexer_2_out), .in1(ID_IR[15:11]), .out(multiplexer_3_out), .sel(\单周期硬布线控制器_1_regdst ));
  Multiplexer #(.select(1), .width(5), .disabled("Z"), .enable("false")) multiplexer_4 (
    .in0(multiplexer_3_out), .in1({5{1'b1}}), .out(multiplexer_4_out), .sel(\单周期硬布线控制器_1_jal ));
  assign bit_extender_1_out = {{16{1'b0}}, ID_IR[15:0]};  // Bit_Extender bit_extender_1
  assign bit_extender_2_out = {{16{ID_IR[15]}}, ID_IR[15:0]};  // Bit_Extender bit_extender_2
  Multiplexer #(.select(1), .width(32), .disabled("Z"), .enable("false")) multiplexer_5 (
    .in0(bit_extender_1_out), .in1(bit_extender_2_out), .out(multiplexer_5_out), .sel(SignedExt));
  MIPS_Regifile mips_regifile_1 (
    .Din(RDin), .Clk(CLK), .R1(mips_regifile_1_r1), .R2(mips_regifile_1_r2), .WE(RegWrite),
    .W_num(mem_wb_1_w_num_2), .R1_num(multiplexer_1_out), .R2_num(multiplexer_2_out));
  and and_7 (and_7_out, youtiaojian, stop);
  Counter #(.width(16), .max('hffff), .ongoal("wrap"), .trigger("rising"), .behavior("new")) counter_3 (
    .count(and_7_out), .Q(\条件分支成功数 ), .clk(CLK));  // open: load, D, carry, clr, preset, down
  and and_8 (LoadUse, \ir判断电路_1_out_5 , EXMemWrite);
  ID_EX id_ex_1 (
    .clk(CLK), .PC_4(if_id_1_pc_4_2), .PC_4_2(id_ex_1_pc_4_2), .IR(ID_IR), .IR_2(EX_IR), .PC(ID_PC),
    .PC_2(EX_PC), .RegWrite(\单周期硬布线控制器_1_regwrite ), .RegWrite_2(id_ex_1_regwrite_2),
    .W_num(multiplexer_4_out), .W_num_2(id_ex_1_w_num_2), .MemWrite(\单周期硬布线控制器_1_memwrite ),
    .MemWrite_2(id_ex_1_memwrite_2), .AluSrcB(\单周期硬布线控制器_1_alu_src ), .AluSrcB_2(id_ex_1_alusrcb_2),
    .AluOP(\单周期硬布线控制器_1_alu_op ), .AluOP_2(id_ex_1_aluop_2), .MemToReg(\单周期硬布线控制器_1_memtoreg ),
    .MemToReg_2(EXMemWrite), .Bne(\单周期硬布线控制器_1_bne ), .Bne_2(Bne), .Beq(\单周期硬布线控制器_1_beq ), .Beq_2(Beq),
    .Jmp(\单周期硬布线控制器_1_jmp ), .Jmp_2(J), .Jr(\单周期硬布线控制器_1_jr ), .Jr_2(JR), .Jal(\单周期硬布线控制器_1_jal ),
    .Jal_2(JAL), .R1(mips_regifile_1_r1), .R1_2(id_ex_1_r1_2), .R2(mips_regifile_1_r2), .R2_2(id_ex_1_r2_2),
    .SignExt(multiplexer_5_out), .SignExt_2(id_ex_1_signext_2), .Syscall(IDSyscall), .Syscall_2(EXSyscall),
    .en(stop), .\清空 (or_6_out), .LH(IDLH), .LH_2(id_ex_1_lh_2), .BLTZ(IDBLTZ), .BLTZ_2(BLTZ));
  or or_6 (or_6_out, LoadUse, jumpint);
  and and_9 (and_9_out, LoadUse, stop);
  Counter #(.width(16), .max('hffff), .ongoal("wrap"), .trigger("rising"), .behavior("new")) counter_4 (
    .count(and_9_out), .Q(\LoadUse次数 ), .clk(CLK));  // open: load, D, carry, clr, preset, down
  Comparator #(.width(32), .mode("twosComplement")) comparator_1 (
    .a(v0), .b(32'h22), .eq(comparator_1_eq));  // open: gt, lt
  Multiplexer #(.select(1), .width(32), .disabled("Z"), .enable("false")) multiplexer_6 (
    .in0(LedData), .in1(a0), .out(multiplexer_6_out), .sel(and_10_out));
  or or_7 (or_7_out, LoadUse, jumpint);
  not not_5 (not_5_out, comparator_1_eq);
  and and_10 (and_10_out, comparator_1_eq, Syscall);
  Register #(.width(32), .trigger("rising"), .Select("low")) register_1 (
    .D(multiplexer_6_out), .Q(LedData), .clk(CLK));  // open: en, clr
  Multiplexer #(.select(2), .width(32), .disabled("Z"), .enable("false")) multiplexer_7 (
    .in0(id_ex_1_r1_2), .in1(ex_mem_1_alures_2), .in2(mem_wb_1_memdata_2), .in3(mem_wb_1_alures_2),
    .out(multiplexer_7_out), .sel(SA));
  Multiplexer #(.select(2), .width(32), .disabled("Z"), .enable("false")) multiplexer_8 (
    .in0(id_ex_1_r2_2), .in1(ex_mem_1_alures_2), .in2(mem_wb_1_memdata_2), .in3(mem_wb_1_alures_2),
    .out(multiplexer_8_out), .sel(SB));
  Counter #(.width(16), .max('hffff), .ongoal("wrap"), .trigger("rising"), .behavior("new")) counter_5 (
    .count(or_7_out), .Q(\插入气泡数 ), .clk(CLK));  // open: load, D, carry, clr, preset, down
  and and_11 (and_11_out, not_5_out, Syscall);
  not not_6 (stop, and_11_out);
  \重定向判断电路  \u_重定向判断电路_1  (
    .\被比较IR (EX_IR), .BA({B2B1[0], A2A1[0]}), .\比较IR (MEM_IR), .out_5(\重定向判断电路_1_out_5 ), .Syscall(EXSyscall));
  \重定向判断电路  \u_重定向判断电路_2  (
    .\被比较IR (EX_IR), .BA({B2B1[1], A2A1[1]}), .\比较IR (WB_IR), .out_5(\重定向判断电路_2_out_5 ), .Syscall(EXSyscall));
  Multiplexer #(.select(1), .width(32), .disabled("Z"), .enable("false")) multiplexer_9 (
    .in0(multiplexer_8_out), .in1(id_ex_1_signext_2), .out(multiplexer_9_out), .sel(id_ex_1_alusrcb_2));
  MIPS_ALU mips_alu_1 (
    .X(multiplexer_7_out), .Y(multiplexer_9_out), .AluOP(id_ex_1_aluop_2), .Equal(EQU),
    .Result(mips_alu_1_result), .shamt(EX_IR[10:6]));  // open: Result_2
  Shifter #(.width(32), .shift("ll")) shifter_1 (.in(id_ex_1_signext_2), .\dist (5'b00010), .out(shifter_1_out));
  Adder #(.width(32)) adder_2 (.a(shifter_1_out), .b(id_ex_1_pc_4_2), .out(adder_2_out));  // open: cin, cout
  not not_7 (not_7_out, MEMMemWrite);
  and and_12 (and_12_out[0], \重定向判断电路_1_out_5 , not_7_out);
  and and_13 (and_12_out[1], WBMemWrite, \重定向判断电路_2_out_5 );
  not not_8 (not_8_out, WBMemWrite);
  D_Flip_Flop #(.trigger("high"), .Pre_Clr_Positions("LEGACY"), .NegatePresetClear("false"), .enable("true"), .NewFFLayout("false")) d_ff_1 (.Q(d_ff_1_q));  // open: clk, D, Qn, preset, en, reset
  and and_14 (and_12_out[2], \重定向判断电路_2_out_5 , not_8_out);
  // Probe on 13'h378
  Clock #(.highDuration(1), .lowDuration(1)) clock_1 (.out(clock_1_out));
  EX_MEM ex_mem_1 (
    .clk(CLK), .PC(EX_PC), .PC_2(M_PC), .IR(EX_IR), .IR_2(MEM_IR), .PC_4(id_ex_1_pc_4_2),
    .PC_4_2(ex_mem_1_pc_4_2), .RegWrite(id_ex_1_regwrite_2), .RegWrite_2(ex_mem_1_regwrite_2),
    .W_num(id_ex_1_w_num_2), .W_num_2(ex_mem_1_w_num_2), .MemWrite(id_ex_1_memwrite_2),
    .MemWrite_2(MemWrite), .MemToReg(EXMemWrite), .MemToReg_2(MEMMemWrite), .ALUres(mips_alu_1_result),
    .ALUres_2(ex_mem_1_alures_2), .R2(multiplexer_8_out), .R2_2(MDin), .Jal(JAL), .Jal_2(ex_mem_1_jal_2),
    .en(stop), .Syscall(EXSyscall), .Syscall_2(ex_mem_1_syscall_2), .LH(id_ex_1_lh_2), .LH_2(ex_mem_1_lh_2),
    .R1(multiplexer_7_out), .R1_2(ex_mem_1_r1_2), .\清空 (1'b0));
  Comparator #(.width(13), .mode("twosComplement")) comparator_2 (
    .a(CNT_num), .b(13'h378), .eq(comparator_2_eq), .lt(comparator_2_lt));  // open: gt
  Multiplexer #(.select(2), .width(2), .disabled("Z"), .enable("false")) multiplexer_10 (
    .in0(2'b00), .in1(2'b01), .in2(2'b10), .in3(2'b01), .out(multiplexer_10_out), .sel(A2A1));
  nand nand_1 (nand_1_out, d_ff_1_q, comparator_2_eq);
  Counter #(.width(13), .max('h1fff), .ongoal("stay"), .trigger("rising"), .behavior("old")) counter_6 (
    .count(comparator_2_lt), .Q(CNT_num), .clk(clock_1_out));  // open: load, D, carry, clr, preset
  Multiplexer #(.select(2), .width(2), .disabled("Z"), .enable("false")) multiplexer_11 (
    .in0(2'b00), .in1(2'b01), .in2(2'b11), .in3(2'b01), .out(multiplexer_11_out), .sel(A2A1));
  Multiplexer #(.select(3), .width(2), .disabled("Z"), .enable("false")) multiplexer_12 (
    .in0(2'b00), .in1(2'b01), .in2(2'b10), .in3(multiplexer_10_out), .in4(2'b11), .in5(multiplexer_11_out),
    .in6(2'b00), .in7(2'b00), .out(multiplexer_12_out), .sel(and_12_out));
  assign CLK = nand_1_out ? clock_1_out : 1'bz;  // Controlled_Buffer controlled_buffer_5
  Pull_Resistor #(.pull(1)) pull_resistor_1 (.node(CLK));
  RAM #(.addrWidth(10), .dataWidth(32), .bus("separate"), .Select("high")) ram_1 (
    .addr(ex_mem_1_alures_2[11:2]), .din(MDin), .data(ram_1_data), .str(MemWrite), .clk(CLK));  // open: sel, ld, clr
  Multiplexer #(.select(2), .width(2), .disabled("Z"), .enable("false")) multiplexer_13 (
    .in0(2'b00), .in1(multiplexer_12_out), .in2(multiplexer_12_out), .in3(multiplexer_12_out), .out(SA),
    .sel(A2A1));
  Multiplexer #(.select(2), .width(2), .disabled("Z"), .enable("false")) multiplexer_14 (
    .in0(2'b00), .in1(2'b01), .in2(2'b10), .in3(2'b01), .out(multiplexer_14_out), .sel(B2B1));
  Multiplexer #(.select(3), .width(2), .disabled("Z"), .enable("false")) multiplexer_15 (
    .in0(2'b00), .in1(2'b01), .in2(2'b10), .in3(multiplexer_14_out), .in4(2'b11), .in5(multiplexer_16_out),
    .in6(2'b00), .in7(2'b00), .out(multiplexer_15_out), .sel(and_12_out));
  MEM_WB mem_wb_1 (
    .clk(CLK), .PC(M_PC), .PC_2(WB_PC), .IR(MEM_IR), .IR_2(WB_IR), .PC_4(ex_mem_1_pc_4_2),
    .PC_4_2(mem_wb_1_pc_4_2), .RegWrite(ex_mem_1_regwrite_2), .RegWrite_2(RegWrite),
    .W_num(ex_mem_1_w_num_2), .W_num_2(mem_wb_1_w_num_2), .MemToReg(MEMMemWrite), .MemToReg_2(WBMemWrite),
    .Jal(ex_mem_1_jal_2), .Jal_2(mem_wb_1_jal_2), .MemData(ram_1_data), .MemData_2(mem_wb_1_memdata_2),
    .ALUres(ex_mem_1_alures_2), .ALUres_2(mem_wb_1_alures_2), .en(stop), .Syscall(ex_mem_1_syscall_2),
    .Syscall_2(Syscall), .\LH片选 (ex_mem_1_alures_2[1]), .\LH片选_2 (\mem_wb_1_lh片选_2 ), .LH(ex_mem_1_lh_2),
    .LH_2(mem_wb_1_lh_2), .R1(ex_mem_1_r1_2), .R1_3(v0), .R2(MDin), .R1_2(a0));
  Multiplexer #(.select(2), .width(2), .disabled("Z"), .enable("false")) multiplexer_16 (
    .in0(2'b00), .in1(2'b01), .in2(2'b11), .in3(2'b01), .out(multiplexer_16_out), .sel(B2B1));
  Multiplexer #(.select(2), .width(2), .disabled("Z"), .enable("false")) multiplexer_17 (
    .in0(2'b00), .in1(multiplexer_15_out), .in2(multiplexer_15_out), .in3(multiplexer_15_out), .out(SB),
    .sel(B2B1));
  Multiplexer #(.select(1), .width(32), .disabled("Z"), .enable("false")) multiplexer_18 (
    .in0(mem_wb_1_alures_2), .in1(multiplexer_20_out), .out(multiplexer_18_out), .sel(WBMemWrite));
  Multiplexer #(.select(1), .width(32), .disabled("Z"), .enable("false")) multiplexer_19 (
    .in0(multiplexer_18_out), .in1(mem_wb_1_pc_4_2), .out(RDin), .sel(mem_wb_1_jal_2));
  Multiplexer #(.select(1), .width(32), .disabled("Z"), .enable("false")) multiplexer_20 (
    .in0(mem_wb_1_memdata_2), .in1(bit_extender_3_out), .out(multiplexer_20_out), .sel(mem_wb_1_lh_2));
  Multiplexer #(.select(1), .width(16), .disabled("Z"), .enable("false")) multiplexer_21 (
    .in0(mem_wb_1_memdata_2[15:0]), .in1(mem_wb_1_memdata_2[31:16]), .out(multiplexer_21_out),
    .sel(\mem_wb_1_lh片选_2 ));
  assign bit_extender_3_out = {{16{multiplexer_21_out[15]}}, multiplexer_21_out};  // Bit_Extender bit_extender_3

  // Other names for the same wires on the sheet: LED[31:0] = LedData; MEM_PC[31:0] = M_PC

  // Notes on the sheet:
  //   中断源
  //   时空图监测，可删除
  //   中断等待指示
  //   数码管输出
  //   指令存储器
  //   contents of rom_1 (hex, n*v repeats v):
  //   20110001 8000c05 20110001 20120002 20130003 8000c09 20110001 20120002 20130003 8000c0d 20110001
  //   20120002 20130003 8000c11 20110001 20120002 20130003 c000cb8 20100001 20110001 118fc0 112020
  //   20020022 c 118882 12200001 8000c15 112020 20020022 c 20110001 118880 112020 20020022 c 12200001
  //   8000c1f 20110001 118fc0 112020 20020022 c 1188c3 112020 20020022 c 118903 112020 20020022 c 118903
  //   112020 20020022 c 118903 112020 20020022 c 118903 112020 20020022 c 118903 112020 20020022 c 118903
  //   112020 20020022 c 118903 112020 20020022 c 20100001 109fc0 139fc3 8021 2012000c 24160003 26100001
  //   3210000f 20080008 20090001 139900 2709825 132020 20020022 c 1094022 1500fff9 22100001 2018000f
  //   2188024 108700 20080008 20090001 139902 2709825 132021 20020022 c 1094022 1500fff9 108702 2c9b022
  //   12c00001 8000c50 4020 1084027 84400 3508ffff 82021 20020022 c 2010ffff 20110000 ae300000 22100001
  //   22310004 ae300000 22100001 22310004 ae300000 22100001 22310004 ae300000 22100001 22310004 ae300000
  //   22100001 22310004 ae300000 22100001 22310004 ae300000 22100001 22310004 ae300000 22100001 22310004
  //   ae300000 22100001 22310004 ae300000 22100001 22310004 ae300000 22100001 22310004 ae300000 22100001
  //   22310004 ae300000 22100001 22310004 ae300000 22100001 22310004 ae300000 22100001 22310004 ae300000
  //   22100001 22310004 22100001 8020 2011003c 8e130000 8e340000 274402a 11000002 ae330000 ae140000
  //   2231fffc 1611fff8 102020 20020022 c 22100004 2011003c 1611fff2 20020032 c 20100000 22100001 102020
  //   20020022 c 22100002 102020 20020022 c 22100003 102020 20020022 c 22100004 102020 20020022 c 22100005
  //   102020 20020022 c 22100006 102020 20020022 c 22100007 102020 20020022 c 22100008 102020 20020022
  //   20020022 c 3e00008
  //   流水调试日志用
  //   IF/ID
  //   OP
  //   指令字
  //   JMP
  //   JR
  //   OP
  //   Func
  //   rd
  //   Beq
  //   Bne
  //   MemToReg
  //   MemWrite
  //   AluOP
  //   AluSrcB
  //   RegWrite
  //   JAL
  //   RegDst
  //   Syscall
  //   rs
  //   rt
  //   为方便自动评测，需要输出流水线各段保存的PC值，注意是PC不是PC+4，另外ID段寄存器写入信息，Mem段内存写入信息也要输出
  //   PC和IR
  //   WB信号
  //   Mem信号
  //   EX信号
  //   ID/EX
  //   控制位
  //   暂停节拍，不能为0
  //   用这个时钟源需要去掉电路中的其他时钟源
  //   EX/MEM
  //   戳工具置1进入计数暂停模式，ctrl+k时钟自动运行到对应节拍暂停
  //   ctrl+k关闭时钟连续运行，将控制位置零，进入单步调试模式调试
  //   可计数暂停的时钟源
  //   MEM/WB
endmodule

module \中断按键参考电路  (
  input  \同步清零信号 ,
  output \与中断屏蔽位与 
);

  wire \_1号中断_out , and_1_out, clock_1_out, d_ff_1_q, or_1_out, or_2_out;

  Clock #(.highDuration(1), .lowDuration(1)) clock_1 (.out(clock_1_out));
  Button \_1号中断  (.out(\_1号中断_out ));
  or or_1 (or_1_out, \与中断屏蔽位与 , d_ff_1_q);
  LED #(.active("true")) \_1号中断等待指示灯  (.in(or_1_out));
  D_Flip_Flop #(.trigger("rising"), .Pre_Clr_Positions("LEGACY"), .NegatePresetClear("false"), .enable("true"), .NewFFLayout("false")) d_ff_1 (
    .clk(\_1号中断_out ), .D(1'b1), .Q(d_ff_1_q), .reset(\与中断屏蔽位与 ));  // open: Qn, preset, en
  or or_2 (or_2_out, d_ff_1_q, \与中断屏蔽位与 );
  and and_1 (and_1_out, or_2_out, ~\同步清零信号 );  // AND_Gate
  D_Flip_Flop #(.trigger("rising"), .Pre_Clr_Positions("LEGACY"), .NegatePresetClear("false"), .enable("true"), .NewFFLayout("false")) IR1 (
    .clk(clock_1_out), .D(and_1_out), .Q(\与中断屏蔽位与 ));  // open: Qn, preset, en, reset
  \单周期硬布线控制器  \u_单周期硬布线控制器_1  ();  // open: Func, OP, ALU_OP, MemToReg, MemWrite, ALU_SRC, RegWrite, SysCALL, SignedExt, RegDst, JR, JMP, Beq, JAL, Bne, LH, BLTZ

  // Notes on the sheet:
  //   中断信号采样参考电路
  //   Reset 
endmodule

module \单周期MIPS_单级中断  (
  input  IR1,
  input  IR2,
  input  IR3,
  output RegWrite,
  output MemWrite,
  output [31:0] PC,
  output [31:0] IR,
  output [31:0] RDin,
  output [31:0] MDin,
  output [31:0] LedData
);

  wire CLK, Go, IR1_t, IR2_t, IR3_t, IRA, IRB, IRC, SignedExt, W1, W2, W3, \单周期硬布线控制器_1_alu_src ,
       \单周期硬布线控制器_1_beq , \单周期硬布线控制器_1_bne , \单周期硬布线控制器_1_jal , \单周期硬布线控制器_1_jmp , \单周期硬布线控制器_1_jr ,
       \单周期硬布线控制器_1_memtoreg , \单周期硬布线控制器_1_memwrite , \单周期硬布线控制器_1_regdst , \单周期硬布线控制器_1_regwrite ,
       \单周期硬布线控制器_1_syscall ;
  wire [3:0] \单周期硬布线控制器_1_alu_op ;
  wire [5:0] undriven, undriven_2;
  wire [15:0] \总周期数 ;
  wire [31:0] rom_1_data;

  Clock #(.highDuration(1), .lowDuration(1)) clock_1 (.out(CLK));
  Button _1 (.out(IRA));
  Button _2 (.out(IRB));
  Button _3 (.out(IRC));
  Register #(.width(32), .trigger("rising"), .Select("low")) u_PC ();  // open: D, en, Q, clk, clr
  Button \u_继续运行  (.out(Go));
  LED #(.active("true")) led_1 (.in(W1));
  LED #(.active("true")) led_2 (.in(W2));
  LED #(.active("true")) led_3 (.in(W3));
  Hex_Digit_Display hex_digit_display_1 (.value(LedData[31:28]));  // open: dp
  ROM #(.addrWidth(10), .dataWidth(32), .Select("high")) rom_1 (.data(rom_1_data));  // open: addr
  Hex_Digit_Display hex_digit_display_2 (.value(LedData[23:20]));  // open: dp
  Hex_Digit_Display hex_digit_display_3 (.value(LedData[27:24]));  // open: dp
  // Mips_Probe mips_probe_1: pin names not known; wires that end beside it: rom_1_data
  Hex_Digit_Display hex_digit_display_4 (.value(LedData[19:16]));  // open: dp
  Hex_Digit_Display hex_digit_display_5 (.value(LedData[15:12]));  // open: dp
  Hex_Digit_Display hex_digit_display_6 (.value(LedData[7:4]));  // open: dp
  Hex_Digit_Display hex_digit_display_7 (.value(LedData[11:8]));  // open: dp
  // Probe on \总周期数 
  MIPS_Regifile mips_regifile_1 ();  // open: Din, Clk, R1, R2, WE, W_num, R1_num, R2_num
  Hex_Digit_Display hex_digit_display_8 (.value(LedData[3:0]));  // open: dp
  MIPS_ALU mips_alu_1 ();  // open: X, Y, AluOP, Equal, Result, Result_2, shamt
  or or_1 (IR1_t, IR1, IRA);
  or or_2 (IR2_t, IR2, IRB);
  RAM #(.addrWidth(10), .dataWidth(32), .bus("separate"), .Select("high")) ram_1 ();  // open: addr, din, data, str, sel, clk, ld, clr
  \单周期硬布线控制器  \u_单周期硬布线控制器_1  (
    .Func(undriven_2), .OP(undriven), .ALU_OP(\单周期硬布线控制器_1_alu_op ), .MemToReg(\单周期硬布线控制器_1_memtoreg ),
    .MemWrite(\单周期硬布线控制器_1_memwrite ), .ALU_SRC(\单周期硬布线控制器_1_alu_src ), .RegWrite(\单周期硬布线控制器_1_regwrite ),
    .SysCALL(\单周期硬布线控制器_1_syscall ), .SignedExt(SignedExt), .RegDst(\单周期硬布线控制器_1_regdst ),
    .JR(\单周期硬布线控制器_1_jr ), .JMP(\单周期硬布线控制器_1_jmp ), .Beq(\单周期硬布线控制器_1_beq ), .JAL(\单周期硬布线控制器_1_jal ),
    .Bne(\单周期硬布线控制器_1_bne ));  // open: LH, BLTZ
  or or_3 (IR3_t, IR3, IRC);

  // Notes on the sheet:
  //   中断源
  //   中断等待指示
  //   总复位信号应将除ROM以外所有存储组件全部清零
  //   指令存储器
  //   contents of rom_1 (hex, n*v repeats v):
  //   20110001 8000c05 20110001 20120002 20130003 8000c09 20110001 20120002 20130003 8000c0d 20110001
  //   20120002 20130003 8000c11 20110001 20120002 20130003 c000cb8 20100001 20110001 118fc0 112020
  //   20020022 c 118882 12200001 8000c15 112020 20020022 c 20110001 118880 112020 20020022 c 12200001
  //   8000c1f 20110001 118fc0 112020 20020022 c 1188c3 112020 20020022 c 118903 112020 20020022 c 118903
  //   112020 20020022 c 118903 112020 20020022 c 118903 112020 20020022 c 118903 112020 20020022 c 118903
  //   112020 20020022 c 118903 112020 20020022 c 20100001 109fc0 139fc3 8021 2012000c 24160003 26100001
  //   3210000f 20080008 20090001 139900 2709825 132020 20020022 c 1094022 1500fff9 22100001 2018000f
  //   2188024 108700 20080008 20090001 139902 2709825 132021 20020022 c 1094022 1500fff9 108702 2c9b022
  //   12c00001 8000c50 4020 1084027 84400 3508ffff 82021 20020022 c 2010ffff 20110000 ae300000 22100001
  //   22310004 ae300000 22100001 22310004 ae300000 22100001 22310004 ae300000 22100001 22310004 ae300000
  //   22100001 22310004 ae300000 22100001 22310004 ae300000 22100001 22310004 ae300000 22100001 22310004
  //   ae300000 22100001 22310004 ae300000 22100001 22310004 ae300000 22100001 22310004 ae300000 22100001
  //   22310004 ae300000 22100001 22310004 ae300000 22100001 22310004 ae300000 22100001 22310004 ae300000
  //   22100001 22310004 22100001 8020 2011003c 8e130000 8e340000 274402a 11000002 ae330000 ae140000
  //   2231fffc 1611fff8 102020 20020022 c 22100004 2011003c 1611fff2 2002000a c 20100000 22100001 102020
  //   20020022 c 22100002 102020 20020022 c 22100003 102020 20020022 c 22100004 102020 20020022 c 22100005
  //   102020 20020022 c 22100006 102020 20020022 c 22100007 102020 20020022 c 22100008 102020 20020022
  //   20020022 c 3e00008
  //   OP
  //   Func
  //   rs
  //   指令字
  //   rt
  //   rd
  //   数码管输出
  //   数码管输出应该用寄存器锁存，否则显示数据只能一闪而过
  //   JMP
  //   JR
  //   OP
  //   Func
  //   Syscall
  //   Beq
  //   Bne
  //   MemToReg
  //   MemWrite
  //   AluOP
  //   AluSrcB
  //   RegWrite
  //   JAL
  //   RegDst
  //   为方便自动评测，需要输出PC，IR，寄存器堆写如数据RDin
  //   RAM写使能MemWrite、RAM写入数据MDin等信号
endmodule

module \单周期MIPS_多级中断  (
  input  IR1,
  input  IR2,
  input  IR3,
  output RegWrite,
  output MemWrite,
  output [31:0] PC,
  output [31:0] IR,
  output [31:0] RDin,
  output [31:0] MDin,
  output [31:0] LedData
);

  wire CLK, Go, IR1_t, IR2_t, IR3_t, IRA, IRB, IRC, SignedExt, W1, W2, W3, \单周期硬布线控制器_1_alu_src ,
       \单周期硬布线控制器_1_beq , \单周期硬布线控制器_1_bne , \单周期硬布线控制器_1_jal , \单周期硬布线控制器_1_jmp , \单周期硬布线控制器_1_jr ,
       \单周期硬布线控制器_1_memtoreg , \单周期硬布线控制器_1_memwrite , \单周期硬布线控制器_1_regdst , \单周期硬布线控制器_1_regwrite ,
       \单周期硬布线控制器_1_syscall ;
  wire [3:0] \单周期硬布线控制器_1_alu_op ;
  wire [5:0] undriven, undriven_2;
  wire [15:0] \总周期数 ;
  wire [31:0] rom_1_data;

  Clock #(.highDuration(1), .lowDuration(1)) clock_1 (.out(CLK));
  Button _1 (.out(IRA));
  Button _2 (.out(IRB));
  Button _3 (.out(IRC));
  Register #(.width(32), .trigger("rising"), .Select("low")) u_PC ();  // open: D, en, Q, clk, clr
  Button \u_继续运行  (.out(Go));
  LED #(.active("true")) led_1 (.in(W1));
  LED #(.active("true")) led_2 (.in(W2));
  LED #(.active("true")) led_3 (.in(W3));
  Hex_Digit_Display hex_digit_display_1 (.value(LedData[31:28]));  // open: dp
  ROM #(.addrWidth(10), .dataWidth(32), .Select("high")) rom_1 (.data(rom_1_data));  // open: addr
  Hex_Digit_Display hex_digit_display_2 (.value(LedData[23:20]));  // open: dp
  Hex_Digit_Display hex_digit_display_3 (.value(LedData[27:24]));  // open: dp
  // Mips_Probe mips_probe_1: pin names not known; wires that end beside it: rom_1_data
  Hex_Digit_Display hex_digit_display_4 (.value(LedData[15:12]));  // open: dp
  Hex_Digit_Display hex_digit_display_5 (.value(LedData[19:16]));  // open: dp
  Hex_Digit_Display hex_digit_display_6 (.value(LedData[11:8]));  // open: dp
  Hex_Digit_Display hex_digit_display_7 (.value(LedData[7:4]));  // open: dp
  // Probe on \总周期数 
  MIPS_Regifile mips_regifile_1 ();  // open: Din, Clk, R1, R2, WE, W_num, R1_num, R2_num
  Hex_Digit_Display hex_digit_display_8 (.value(LedData[3:0]));  // open: dp
  MIPS_ALU mips_alu_1 ();  // open: X, Y, AluOP, Equal, Result, Result_2, shamt
  or or_1 (IR1_t, IR1, IRA);
  or or_2 (IR2_t, IR2, IRB);
  RAM #(.addrWidth(10), .dataWidth(32), .bus("separate"), .Select("high")) ram_1 ();  // open: addr, din, data, str, sel, clk, ld, clr
  \单周期硬布线控制器  \u_单周期硬布线控制器_1  (
    .Func(undriven_2), .OP(undriven), .ALU_OP(\单周期硬布线控制器_1_alu_op ), .MemToReg(\单周期硬布线控制器_1_memtoreg ),
    .MemWrite(\单周期硬布线控制器_1_memwrite ), .ALU_SRC(\单周期硬布线控制器_1_alu_src ), .RegWrite(\单周期硬布线控制器_1_regwrite ),
    .SysCALL(\单周期硬布线控制器_1_syscall ), .SignedExt(SignedExt), .RegDst(\单周期硬布线控制器_1_regdst ),
    .JR(\单周期硬布线控制器_1_jr ), .JMP(\单周期硬布线控制器_1_jmp ), .Beq(\单周期硬布线控制器_1_beq ), .JAL(\单周期硬布线控制器_1_jal ),
    .Bne(\单周期硬布线控制器_1_bne ));  // open: LH, BLTZ
  or or_3 (IR3_t, IR3, IRC);

  // Notes on the sheet:
  //   中断源
  //   中断等待指示
  //   总复位信号应将除ROM以外所有存储组件全部清零
  //   指令存储器
  //   contents of rom_1 (hex, n*v repeats v):
  //   20110001 8000c05 20110001 20120002 20130003 8000c09 20110001 20120002 20130003 8000c0d 20110001
  //   20120002 20130003 8000c11 20110001 20120002 20130003 c000cb8 20100001 20110001 118fc0 112020
  //   20020022 c 118882 12200001 8000c15 112020 20020022 c 20110001 118880 112020 20020022 c 12200001
  //   8000c1f 20110001 118fc0 112020 20020022 c 1188c3 112020 20020022 c 118903 112020 20020022 c 118903
  //   112020 20020022 c 118903 112020 20020022 c 118903 112020 20020022 c 118903 112020 20020022 c 118903
  //   112020 20020022 c 118903 112020 20020022 c 20100001 109fc0 139fc3 8021 2012000c 24160003 26100001
  //   3210000f 20080008 20090001 139900 2709825 132020 20020022 c 1094022 1500fff9 22100001 2018000f
  //   2188024 108700 20080008 20090001 139902 2709825 132021 20020022 c 1094022 1500fff9 108702 2c9b022
  //   12c00001 8000c50 4020 1084027 84400 3508ffff 82021 20020022 c 2010ffff 20110000 ae300000 22100001
  //   22310004 ae300000 22100001 22310004 ae300000 22100001 22310004 ae300000 22100001 22310004 ae300000
  //   22100001 22310004 ae300000 22100001 22310004 ae300000 22100001 22310004 ae300000 22100001 22310004
  //   ae300000 22100001 22310004 ae300000 22100001 22310004 ae300000 22100001 22310004 ae300000 22100001
  //   22310004 ae300000 22100001 22310004 ae300000 22100001 22310004 ae300000 22100001 22310004 ae300000
  //   22100001 22310004 22100001 8020 2011003c 8e130000 8e340000 274402a 11000002 ae330000 ae140000
  //   2231fffc 1611fff8 102020 20020022 c 22100004 2011003c 1611fff2 2002000a c 20100000 22100001 102020
  //   20020022 c 22100002 102020 20020022 c 22100003 102020 20020022 c 22100004 102020 20020022 c 22100005
  //   102020 20020022 c 22100006 102020 20020022 c 22100007 102020 20020022 c 22100008 102020 20020022
  //   20020022 c 3e00008
  //   OP
  //   Func
  //   rs
  //   指令字
  //   rt
  //   rd
  //   数码管输出
  //   数码管输出应该用寄存器锁存，否则显示数据只能一闪而过
  //   JMP
  //   JR
  //   OP
  //   Func
  //   Syscall
  //   Beq
  //   Bne
  //   MemToReg
  //   MemWrite
  //   AluOP
  //   AluSrcB
  //   RegWrite
  //   JAL
  //   RegDst
  //   为方便自动评测，需要输出PC，IR，寄存器堆写如数据RDin
  //   RAM写使能MemWrite、RAM写入数据MDin等信号
endmodule

module \封装正确性测试  (
);

  wire IR1, IR2, IR3, MemW, RegW;
  wire [31:0] EX_PC, ID_PC, IF_PC, IR, LED, MDin, MDinr, MEM_PC, PC, RDin, RDinr, WB_PC;

  \单周期MIPS  \u_单周期mips_1  (
    .RegWrite(RegW), .MemWrite(MemW), .PC(PC), .IR(IR), .RDin(RDin), .MDin(MDin), .LED(LED));  // open: IR1, IR2, IR3
  \气泡流水线  \u_气泡流水线_1  (
    .RegWrite(RegW), .MemWrite(MemW), .IF_PC(IF_PC), .ID_PC(ID_PC), .EX_PC(EX_PC), .M_PC(MEM_PC),
    .WB_PC(WB_PC), .RDin(RDinr), .MDin(MDinr), .LedData(LED));
  \单周期MIPS_单级中断  \u_单周期mips_单级中断_1  (
    .IR1(IR1), .IR2(IR2), .IR3(IR3), .RegWrite(RegW), .MemWrite(MemW), .PC(PC), .IR(IR), .RDin(RDin),
    .MDin(MDin), .LedData(LED));
  \理想流水线  \u_理想流水线_1  (
    .RegWrite(RegW), .MemWrite(MemW), .IF_PC(IF_PC), .ID_PC(ID_PC), .EX_PC(EX_PC), .M_PC(MEM_PC),
    .WB_PC(WB_PC), .RDin(RDinr), .MDin(MDinr), .LedData(LED));
  \气泡流水线  \u_气泡流水线_2  (
    .RegWrite(RegW), .MemWrite(MemW), .IF_PC(IF_PC), .ID_PC(ID_PC), .EX_PC(EX_PC), .M_PC(MEM_PC),
    .WB_PC(WB_PC), .RDin(RDinr), .MDin(MDinr), .LedData(LED));
  \单周期MIPS_多级中断  \u_单周期mips_多级中断_1  (
    .IR1(IR1), .IR2(IR2), .IR3(IR3), .RegWrite(RegW), .MemWrite(MemW), .PC(PC), .IR(IR), .RDin(RDin),
    .MDin(MDin), .LedData(LED));

  // Notes on the sheet:
  //   单周期封装测试
  //   气泡流水封装测试
  //   单周期+单级中断封装测试
  //   请检查上面封装有无位宽不匹配，引脚标签是否和连接的标签相对应，否则无法在educoder平台上正确测试
  //   理想流水封装测试
  //   重定向流水封装测试
  //   单周期+多级中断封装测试
endmodule

module ID_EX (
  input  clk,
  input  \清空 ,
  input  en,
  input  Beq,
  input  MemWrite,
  input  [31:0] PC,
  input  Jmp,
  input  AluSrcB,
  input  [31:0] IR,
  input  Jr,
  input  [3:0] AluOP,
  input  [31:0] PC_4,
  input  Jal,
  input  MemToReg,
  input  RegWrite,
  input  Bne,
  input  Syscall,
  input  [4:0] W_num,
  input  LH,
  input  BLTZ,
  input  [31:0] R1,
  input  [31:0] R2,
  input  [31:0] SignExt,
  output Beq_2,
  output MemWrite_2,
  output [31:0] PC_2,
  output Jmp_2,
  output AluSrcB_2,
  output [31:0] IR_2,
  output Jr_2,
  output [3:0] AluOP_2,
  output [31:0] PC_4_2,
  output Jal_2,
  output MemToReg_2,
  output RegWrite_2,
  output Bne_2,
  output Syscall_2,
  output [4:0] W_num_2,
  output LH_2,
  output BLTZ_2,
  output [31:0] R1_2,
  output [31:0] R2_2,
  output [31:0] SignExt_2
);

  wire multiplexer_4_out, multiplexer_10_out, multiplexer_11_out, multiplexer_12_out, multiplexer_13_out,
       multiplexer_14_out, multiplexer_15_out, multiplexer_16_out, multiplexer_17_out, multiplexer_18_out,
       multiplexer_19_out, multiplexer_20_out, undriven, undriven_2;
  wire [3:0] multiplexer_9_out;
  wire [4:0] multiplexer_5_out;
  wire [31:0] multiplexer_1_out, multiplexer_2_out, multiplexer_3_out, multiplexer_6_out, multiplexer_7_out,
       multiplexer_8_out;

  Multiplexer #(.select(1), .width(32), .disabled("Z"), .enable("false")) multiplexer_1 (
    .in0(PC), .in1({32{1'b0}}), .out(multiplexer_1_out), .sel(\清空 ));
  Multiplexer #(.select(1), .width(32), .disabled("Z"), .enable("false")) multiplexer_2 (
    .in0(IR), .in1({32{1'b0}}), .out(multiplexer_2_out), .sel(\清空 ));
  Multiplexer #(.select(1), .width(32), .disabled("Z"), .enable("false")) multiplexer_3 (
    .in0(PC_4), .in1({32{1'b0}}), .out(multiplexer_3_out), .sel(\清空 ));
  Multiplexer #(.select(1), .width(1), .disabled("Z"), .enable("false")) multiplexer_4 (
    .in0(RegWrite), .in1(1'b0), .out(multiplexer_4_out), .sel(\清空 ));
  Multiplexer #(.select(1), .width(5), .disabled("Z"), .enable("false")) multiplexer_5 (
    .in0(W_num), .in1({5{1'b0}}), .out(multiplexer_5_out), .sel(\清空 ));
  Multiplexer #(.select(1), .width(32), .disabled("Z"), .enable("false")) multiplexer_6 (
    .in0(R1), .in1({32{1'b0}}), .out(multiplexer_6_out), .sel(\清空 ));
  Multiplexer #(.select(1), .width(32), .disabled("Z"), .enable("false")) multiplexer_7 (
    .in0(R2), .in1({32{1'b0}}), .out(multiplexer_7_out), .sel(\清空 ));
  Multiplexer #(.select(1), .width(32), .disabled("Z"), .enable("false")) multiplexer_8 (
    .in0(SignExt), .in1({32{1'b0}}), .out(multiplexer_8_out), .sel(\清空 ));
  Register #(.width(32), .trigger("rising"), .Select("low")) register_1 (
    .D(multiplexer_1_out), .en(en), .Q(PC_2), .clk(clk));  // open: clr
  Register #(.width(32), .trigger("rising"), .Select("low")) register_2 (
    .D(multiplexer_2_out), .en(en), .Q(IR_2), .clk(clk));  // open: clr
  Register #(.width(32), .trigger("rising"), .Select("low")) register_3 (
    .D(multiplexer_3_out), .en(en), .Q(PC_4_2), .clk(clk));  // open: clr
  Register #(.width(1), .trigger("rising"), .Select("low")) register_4 (
    .D(multiplexer_4_out), .en(en), .Q(RegWrite_2), .clk(clk));  // open: clr
  Register #(.width(5), .trigger("rising"), .Select("low")) register_5 (
    .D(multiplexer_5_out), .en(en), .Q(W_num_2), .clk(clk));  // open: clr
  Register #(.width(32), .trigger("rising"), .Select("low")) register_6 (
    .D(multiplexer_6_out), .en(en), .Q(R1_2), .clk(clk));  // open: clr
  Register #(.width(32), .trigger("rising"), .Select("low")) register_7 (
    .D(multiplexer_7_out), .en(en), .Q(R2_2), .clk(clk));  // open: clr
  Register #(.width(32), .trigger("rising"), .Select("low")) register_8 (
    .D(multiplexer_8_out), .en(en), .Q(SignExt_2), .clk(clk));  // open: clr
  Multiplexer #(.select(1), .width(4), .disabled("Z"), .enable("false")) multiplexer_9 (
    .in0(AluOP), .in1(4'b0000), .out(multiplexer_9_out), .sel(\清空 ));
  Multiplexer #(.select(1), .width(1), .disabled("Z"), .enable("false")) multiplexer_10 (
    .in0(MemWrite), .in1(1'b0), .out(multiplexer_10_out), .sel(\清空 ));
  Multiplexer #(.select(1), .width(1), .disabled("Z"), .enable("false")) multiplexer_11 (
    .in0(AluSrcB), .in1(1'b0), .out(multiplexer_11_out), .sel(\清空 ));
  Multiplexer #(.select(1), .width(1), .disabled("Z"), .enable("false")) multiplexer_12 (
    .in0(MemToReg), .in1(1'b0), .out(multiplexer_12_out), .sel(\清空 ));
  Multiplexer #(.select(1), .width(1), .disabled("Z"), .enable("false")) multiplexer_13 (
    .in0(Bne), .in1(1'b0), .out(multiplexer_13_out), .sel(\清空 ));
  Register #(.width(1), .trigger("rising"), .Select("low")) register_9 (
    .D(multiplexer_10_out), .en(en), .Q(MemWrite_2), .clk(clk));  // open: clr
  Register #(.width(1), .trigger("rising"), .Select("low")) register_10 (
    .D(multiplexer_11_out), .en(en), .Q(AluSrcB_2), .clk(clk));  // open: clr
  Register #(.width(4), .trigger("rising"), .Select("low")) register_11 (
    .D(multiplexer_9_out), .en(en), .Q(AluOP_2), .clk(clk));  // open: clr
  Register #(.width(1), .trigger("rising"), .Select("low")) register_12 (
    .D(multiplexer_12_out), .en(en), .Q(MemToReg_2), .clk(clk));  // open: clr
  Register #(.width(1), .trigger("rising"), .Select("low")) register_13 (
    .D(multiplexer_13_out), .en(en), .Q(Bne_2), .clk(clk));  // open: clr
  Multiplexer #(.select(1), .width(1), .disabled("Z"), .enable("false")) multiplexer_14 (
    .in0(Beq), .in1(1'b0), .out(multiplexer_14_out), .sel(\清空 ));
  Multiplexer #(.select(1), .width(1), .disabled("Z"), .enable("false")) multiplexer_15 (
    .in0(Jmp), .in1(1'b0), .out(multiplexer_15_out), .sel(\清空 ));
  Multiplexer #(.select(1), .width(1), .disabled("Z"), .enable("false")) multiplexer_16 (
    .in0(Jr), .in1(1'b0), .out(multiplexer_16_out), .sel(\清空 ));
  Multiplexer #(.select(1), .width(1), .disabled("Z"), .enable("false")) multiplexer_17 (
    .in0(Jal), .in1(1'b0), .out(multiplexer_17_out), .sel(\清空 ));
  Multiplexer #(.select(1), .width(1), .disabled("Z"), .enable("false")) multiplexer_18 (
    .in0(Syscall), .in1(1'b0), .out(multiplexer_18_out), .sel(\清空 ));
  Multiplexer #(.select(1), .width(1), .disabled("Z"), .enable("false")) multiplexer_19 (
    .in0(LH), .in1(1'b0), .out(multiplexer_19_out), .sel(\清空 ));
  Multiplexer #(.select(1), .width(1), .disabled("Z"), .enable("false")) multiplexer_20 (
    .in0(BLTZ), .in1(1'b0), .out(multiplexer_20_out), .sel(\清空 ));
  Register #(.width(1), .trigger("rising"), .Select("low")) register_14 (
    .D(multiplexer_14_out), .en(en), .Q(Beq_2), .clk(clk));  // open: clr
  Register #(.width(1), .trigger("rising"), .Select("low")) register_15 (
    .D(multiplexer_15_out), .en(en), .Q(Jmp_2), .clk(clk));  // open: clr
  Register #(.width(1), .trigger("rising"), .Select("low")) register_16 (
    .D(multiplexer_16_out), .en(en), .Q(Jr_2), .clk(clk), .cs(undriven), .preset(undriven));  // open: clr
  Register #(.width(1), .trigger("rising"), .Select("low")) register_17 (
    .D(multiplexer_17_out), .en(en), .Q(Jal_2), .clk(clk), .cs(undriven_2), .preset(undriven_2));  // open: clr
  Register #(.width(1), .trigger("rising"), .Select("low")) register_18 (
    .D(multiplexer_18_out), .en(en), .Q(Syscall_2), .clk(clk));  // open: clr
  Register #(.width(1), .trigger("rising"), .Select("low")) register_19 (
    .D(multiplexer_19_out), .en(en), .Q(LH_2), .clk(clk));  // open: clr
  Register #(.width(1), .trigger("rising"), .Select("low")) register_20 (
    .D(multiplexer_20_out), .en(en), .Q(BLTZ_2), .clk(clk));  // open: clr

  // Other names for the same wires on the sheet: clr = \清空 
endmodule

module IF_ID (
  input  clk,
  input  en,
  input  [31:0] PC_4,
  input  \清空 ,
  input  [31:0] IR,
  input  [31:0] PC,
  output [31:0] PC_4_2,
  output [31:0] IR_2,
  output [31:0] PC_2
);

  wire [31:0] multiplexer_1_out, multiplexer_2_out, multiplexer_3_out;

  Multiplexer #(.select(1), .width(32), .disabled("Z"), .enable("false")) multiplexer_1 (
    .in0(PC_4), .in1({32{1'b0}}), .out(multiplexer_1_out), .sel(\清空 ));
  Multiplexer #(.select(1), .width(32), .disabled("Z"), .enable("false")) multiplexer_2 (
    .in0(IR), .in1({32{1'b0}}), .out(multiplexer_2_out), .sel(\清空 ));
  Multiplexer #(.select(1), .width(32), .disabled("Z"), .enable("false")) multiplexer_3 (
    .in0(PC), .in1({32{1'b0}}), .out(multiplexer_3_out), .sel(\清空 ));
  Register #(.width(32), .trigger("rising"), .Select("low")) register_1 (
    .D(multiplexer_1_out), .en(en), .Q(PC_4_2), .clk(clk));  // open: clr
  Register #(.width(32), .trigger("rising"), .Select("low")) register_2 (
    .D(multiplexer_2_out), .en(en), .Q(IR_2), .clk(clk));  // open: clr
  Register #(.width(32), .trigger("rising"), .Select("low")) register_3 (
    .D(multiplexer_3_out), .en(en), .Q(PC_2), .clk(clk));  // open: clr
endmodule

module EX_MEM (
  input  clk,
  input  en,
  input  [31:0] PC,
  input  \清空 ,
  input  [31:0] IR,
  input  [31:0] PC_4,
  input  RegWrite,
  input  [4:0] W_num,
  input  MemWrite,
  input  MemToReg,
  input  Jal,
  input  Syscall,
  input  [31:0] R1,
  input  [31:0] R2,
  input  [31:0] ALUres,
  input  LH,
  output [31:0] PC_2,
  output [31:0] IR_2,
  output [31:0] PC_4_2,
  output RegWrite_2,
  output [4:0] W_num_2,
  output MemWrite_2,
  output MemToReg_2,
  output Jal_2,
  output Syscall_2,
  output [31:0] R1_2,
  output [31:0] R2_2,
  output [31:0] ALUres_2,
  output LH_2
);

  wire multiplexer_1_out, multiplexer_7_out, multiplexer_9_out, multiplexer_10_out, multiplexer_11_out,
       multiplexer_12_out;
  wire [4:0] multiplexer_8_out;
  wire [31:0] multiplexer_2_out, multiplexer_3_out, multiplexer_4_out, multiplexer_5_out, multiplexer_6_out,
       multiplexer_13_out;

  Multiplexer #(.select(1), .width(1), .disabled("Z"), .enable("false")) multiplexer_1 (
    .in0(Jal), .in1(1'b0), .out(multiplexer_1_out), .sel(\清空 ));
  Multiplexer #(.select(1), .width(32), .disabled("Z"), .enable("false")) multiplexer_2 (
    .in0(R2), .in1({32{1'b0}}), .out(multiplexer_2_out), .sel(\清空 ));
  Multiplexer #(.select(1), .width(32), .disabled("Z"), .enable("false")) multiplexer_3 (
    .in0(ALUres), .in1({32{1'b0}}), .out(multiplexer_3_out), .sel(\清空 ));
  Multiplexer #(.select(1), .width(32), .disabled("Z"), .enable("false")) multiplexer_4 (
    .in0(PC), .in1({32{1'b0}}), .out(multiplexer_4_out), .sel(\清空 ));
  Multiplexer #(.select(1), .width(32), .disabled("Z"), .enable("false")) multiplexer_5 (
    .in0(IR), .in1({32{1'b0}}), .out(multiplexer_5_out), .sel(\清空 ));
  Multiplexer #(.select(1), .width(32), .disabled("Z"), .enable("false")) multiplexer_6 (
    .in0(PC_4), .in1({32{1'b0}}), .out(multiplexer_6_out), .sel(\清空 ));
  Multiplexer #(.select(1), .width(1), .disabled("Z"), .enable("false")) multiplexer_7 (
    .in0(RegWrite), .in1(1'b0), .out(multiplexer_7_out), .sel(\清空 ));
  Multiplexer #(.select(1), .width(5), .disabled("Z"), .enable("false")) multiplexer_8 (
    .in0(W_num), .in1({5{1'b0}}), .out(multiplexer_8_out), .sel(\清空 ));
  Multiplexer #(.select(1), .width(1), .disabled("Z"), .enable("false")) multiplexer_9 (
    .in0(MemWrite), .in1(1'b0), .out(multiplexer_9_out), .sel(\清空 ));
  Multiplexer #(.select(1), .width(1), .disabled("Z"), .enable("false")) multiplexer_10 (
    .in0(MemToReg), .in1(1'b0), .out(multiplexer_10_out), .sel(\清空 ));
  Multiplexer #(.select(1), .width(1), .disabled("Z"), .enable("false")) multiplexer_11 (
    .in0(Syscall), .in1(1'b0), .out(multiplexer_11_out), .sel(\清空 ));
  Multiplexer #(.select(1), .width(1), .disabled("Z"), .enable("false")) multiplexer_12 (
    .in0(LH), .in1(1'b0), .out(multiplexer_12_out), .sel(\清空 ));
  Register #(.width(32), .trigger("rising"), .Select("low")) register_1 (
    .D(multiplexer_4_out), .en(en), .Q(PC_2), .clk(clk));  // open: clr
  Register #(.width(32), .trigger("rising"), .Select("low")) register_2 (
    .D(multiplexer_5_out), .en(en), .Q(IR_2), .clk(clk));  // open: clr
  Register #(.width(32), .trigger("rising"), .Select("low")) register_3 (
    .D(multiplexer_6_out), .en(en), .Q(PC_4_2), .clk(clk));  // open: clr
  Register #(.width(1), .trigger("rising"), .Select("low")) register_4 (
    .D(multiplexer_7_out), .en(en), .Q(RegWrite_2), .clk(clk));  // open: clr
  Register #(.width(5), .trigger("rising"), .Select("low")) register_5 (
    .D(multiplexer_8_out), .en(en), .Q(W_num_2), .clk(clk));  // open: clr
  Register #(.width(1), .trigger("rising"), .Select("low")) register_6 (
    .D(multiplexer_9_out), .en(en), .Q(MemWrite_2), .clk(clk));  // open: clr
  Register #(.width(1), .trigger("rising"), .Select("low")) register_7 (
    .D(multiplexer_10_out), .en(en), .Q(MemToReg_2), .clk(clk));  // open: clr
  Register #(.width(1), .trigger("rising"), .Select("low")) register_8 (
    .D(multiplexer_1_out), .en(en), .Q(Jal_2), .clk(clk));  // open: clr
  Register #(.width(1), .trigger("rising"), .Select("low")) register_9 (
    .D(multiplexer_11_out), .en(en), .Q(Syscall_2), .clk(clk));  // open: clr
  Register #(.width(32), .trigger("rising"), .Select("low")) register_10 (
    .D(multiplexer_2_out), .en(en), .Q(R2_2), .clk(clk));  // open: clr
  Register #(.width(32), .trigger("rising"), .Select("low")) register_11 (
    .D(multiplexer_3_out), .en(en), .Q(ALUres_2), .clk(clk));  // open: clr
  Register #(.width(1), .trigger("rising"), .Select("low")) register_12 (
    .D(multiplexer_12_out), .en(en), .Q(LH_2), .clk(clk));  // open: clr
  Multiplexer #(.select(1), .width(32), .disabled("Z"), .enable("false")) multiplexer_13 (
    .in0(R1), .in1({32{1'b0}}), .out(multiplexer_13_out), .sel(\清空 ));
  Register #(.width(32), .trigger("rising"), .Select("low")) register_13 (
    .D(multiplexer_13_out), .en(en), .Q(R1_2), .clk(clk));  // open: clr
endmodule

module MEM_WB (
  input  clk,
  input  en,
  input  [31:0] PC,
  input  [31:0] IR,
  input  [31:0] PC_4,
  input  RegWrite,
  input  [4:0] W_num,
  input  MemToReg,
  input  Jal,
  input  Syscall,
  input  [31:0] MemData,
  input  [31:0] R2,
  input  [31:0] R1,
  input  [31:0] ALUres,
  input  LH,
  input  \LH片选 ,
  output [31:0] PC_2,
  output [31:0] IR_2,
  output [31:0] PC_4_2,
  output RegWrite_2,
  output [4:0] W_num_2,
  output MemToReg_2,
  output Jal_2,
  output Syscall_2,
  output [31:0] MemData_2,
  output [31:0] R1_2,
  output [31:0] R1_3,
  output [31:0] ALUres_2,
  output LH_2,
  output \LH片选_2 
);

  Register #(.width(32), .trigger("rising"), .Select("low")) register_1 (
    .D(PC), .en(en), .Q(PC_2), .clk(clk));  // open: clr
  Register #(.width(32), .trigger("rising"), .Select("low")) register_2 (
    .D(IR), .en(en), .Q(IR_2), .clk(clk));  // open: clr
  Register #(.width(32), .trigger("rising"), .Select("low")) register_3 (
    .D(PC_4), .en(en), .Q(PC_4_2), .clk(clk));  // open: clr
  Register #(.width(1), .trigger("rising"), .Select("low")) register_4 (
    .D(RegWrite), .en(en), .Q(RegWrite_2), .clk(clk));  // open: clr
  Register #(.width(5), .trigger("rising"), .Select("low")) register_5 (
    .D(W_num), .en(en), .Q(W_num_2), .clk(clk));  // open: clr
  Register #(.width(1), .trigger("rising"), .Select("low")) register_6 (
    .D(Jal), .en(en), .Q(Jal_2), .clk(clk));  // open: clr
  Register #(.width(32), .trigger("rising"), .Select("low")) register_7 (
    .D(MemData), .en(en), .Q(MemData_2), .clk(clk));  // open: clr
  Register #(.width(32), .trigger("rising"), .Select("low")) register_8 (
    .D(ALUres), .en(en), .Q(ALUres_2), .clk(clk));  // open: clr
  Register #(.width(1), .trigger("rising"), .Select("low")) register_9 (
    .D(LH), .en(en), .Q(LH_2), .clk(clk));  // open: clr
  Register #(.width(1), .trigger("rising"), .Select("low")) register_10 (
    .D(\LH片选 ), .en(en), .Q(\LH片选_2 ), .clk(clk));  // open: clr
  Register #(.width(1), .trigger("rising"), .Select("low")) register_11 (
    .D(MemToReg), .en(en), .Q(MemToReg_2), .clk(clk));  // open: clr
  Register #(.width(1), .trigger("rising"), .Select("low")) register_12 (
    .D(Syscall), .en(en), .Q(Syscall_2), .clk(clk));  // open: clr
  Register #(.width(32), .trigger("rising"), .Select("low")) register_13 (
    .D(R1), .en(en), .Q(R1_3), .clk(clk));  // open: clr
  Register #(.width(32), .trigger("rising"), .Select("low")) register_14 (
    .D(R2), .en(en), .Q(R1_2), .clk(clk));  // open: clr
endmodule

module \IR判断电路  (
  input  [31:0] \被比较IR ,
  input  [31:0] \比较IR ,
  input  Syscall,
  output [1:0] BA,
  output out_5
);

  wire and_1_out, and_4_out, and_11_out, and_12_out, both, both2, comparator_2_eq, comparator_3_eq,
       comparator_4_eq, comparator_5_eq, comparator_6_eq, comparator_8_eq, comparator_9_eq, comparator_10_eq,
       comparator_11_eq, comparator_12_eq, comparator_13_eq, comparator_14_eq, comparator_15_eq,
       comparator_16_eq, comparator_17_eq, comparator_18_eq, comparator_19_eq, comparator_20_eq,
       comparator_21_eq, comparator_22_eq, comparator_23_eq, comparator_24_eq, comparator_25_eq,
       comparator_26_eq, comparator_27_eq, comparator_28_eq, multiplexer_2_out, not_1_out, not_2_out,
       not_3_out, not_4_out, not_5_out, not_6_out, not_7_out, not_8_out, not_9_out, not_10_out, not_11_out,
       not_12_out, or_3_out, or_4_out, or_5_out, or_6_out, R1, R2;
  wire [1:0] and_2_out, and_5_out, and_7_out, and_9_out;

  Comparator #(.width(6), .mode("twosComplement")) comparator_1 (
    .a(\比较IR [31:26]), .b({6{1'b0}}), .eq(R2));  // open: gt, lt
  Comparator #(.width(6), .mode("twosComplement")) comparator_2 (
    .a(\比较IR [31:26]), .b(6'b101011), .eq(comparator_2_eq));  // open: gt, lt
  Comparator #(.width(6), .mode("twosComplement")) comparator_3 (
    .a(\比较IR [31:26]), .b(6'b000100), .eq(comparator_3_eq));  // open: gt, lt
  Comparator #(.width(6), .mode("twosComplement")) comparator_4 (
    .a(\比较IR [31:26]), .b(6'b000101), .eq(comparator_4_eq));  // open: gt, lt
  Comparator #(.width(6), .mode("twosComplement")) comparator_5 (
    .a(\被比较IR [31:26]), .b(6'b000100), .eq(comparator_5_eq));  // open: gt, lt
  Comparator #(.width(6), .mode("twosComplement")) comparator_6 (
    .a(\被比较IR [31:26]), .b(6'b000101), .eq(comparator_6_eq));  // open: gt, lt
  Comparator #(.width(6), .mode("twosComplement")) comparator_7 (
    .a(\被比较IR [31:26]), .b({6{1'b0}}), .eq(R1));  // open: gt, lt
  or or_1 (both2, comparator_3_eq, comparator_2_eq, comparator_4_eq);
  or or_2 (both, comparator_5_eq, comparator_6_eq);
  Comparator #(.width(5), .mode("twosComplement")) comparator_8 (
    .a(\被比较IR [25:21]), .b(\比较IR [20:16]), .eq(comparator_8_eq));  // open: gt, lt
  not not_1 (not_1_out, comparator_9_eq);
  Comparator #(.width(5), .mode("twosComplement")) comparator_9 (
    .a(\比较IR [20:16]), .b({5{1'b0}}), .eq(comparator_9_eq));  // open: gt, lt
  Comparator #(.width(5), .mode("twosComplement")) comparator_10 (
    .a(\被比较IR [25:21]), .b(\比较IR [20:16]), .eq(comparator_10_eq));  // open: gt, lt
  not not_2 (not_2_out, comparator_11_eq);
  Comparator #(.width(5), .mode("twosComplement")) comparator_11 (
    .a(\比较IR [20:16]), .b({5{1'b0}}), .eq(comparator_11_eq));  // open: gt, lt
  Comparator #(.width(5), .mode("twosComplement")) comparator_12 (
    .a(\被比较IR [20:16]), .b(\比较IR [20:16]), .eq(comparator_12_eq));  // open: gt, lt
  not not_3 (not_3_out, comparator_13_eq);
  Comparator #(.width(5), .mode("twosComplement")) comparator_13 (
    .a(\比较IR [20:16]), .b({5{1'b0}}), .eq(comparator_13_eq));  // open: gt, lt
  Comparator #(.width(5), .mode("twosComplement")) comparator_14 (
    .a(\被比较IR [25:21]), .b(\比较IR [15:11]), .eq(comparator_14_eq));  // open: gt, lt
  not not_4 (not_4_out, comparator_15_eq);
  Comparator #(.width(5), .mode("twosComplement")) comparator_15 (
    .a(\比较IR [15:11]), .b({5{1'b0}}), .eq(comparator_15_eq));  // open: gt, lt
  Comparator #(.width(5), .mode("twosComplement")) comparator_16 (
    .a(\被比较IR [25:21]), .b(\比较IR [15:11]), .eq(comparator_16_eq));  // open: gt, lt
  Comparator #(.width(5), .mode("twosComplement")) comparator_17 (
    .a(\比较IR [15:11]), .b({5{1'b0}}), .eq(comparator_17_eq));  // open: gt, lt
  Comparator #(.width(5), .mode("twosComplement")) comparator_18 (
    .a(\被比较IR [20:16]), .b(\比较IR [15:11]), .eq(comparator_18_eq));  // open: gt, lt
  Comparator #(.width(5), .mode("twosComplement")) comparator_19 (
    .a(\比较IR [15:11]), .b({5{1'b0}}), .eq(comparator_19_eq));  // open: gt, lt
  Comparator #(.width(5), .mode("twosComplement")) comparator_20 (
    .a(\被比较IR [25:21]), .b(\比较IR [20:16]), .eq(comparator_20_eq));  // open: gt, lt
  Comparator #(.width(5), .mode("twosComplement")) comparator_21 (
    .a(\比较IR [20:16]), .b({5{1'b0}}), .eq(comparator_21_eq));  // open: gt, lt
  Comparator #(.width(5), .mode("twosComplement")) comparator_22 (
    .a(\被比较IR [20:16]), .b(\比较IR [20:16]), .eq(comparator_22_eq));  // open: gt, lt
  Comparator #(.width(5), .mode("twosComplement")) comparator_23 (
    .a(\比较IR [20:16]), .b({5{1'b0}}), .eq(comparator_23_eq));  // open: gt, lt
  Comparator #(.width(5), .mode("twosComplement")) comparator_24 (
    .a(\被比较IR [25:21]), .b(\比较IR [15:11]), .eq(comparator_24_eq));  // open: gt, lt
  Comparator #(.width(5), .mode("twosComplement")) comparator_25 (
    .a(\比较IR [15:11]), .b({5{1'b0}}), .eq(comparator_25_eq));  // open: gt, lt
  Comparator #(.width(5), .mode("twosComplement")) comparator_26 (
    .a(\被比较IR [20:16]), .b(\比较IR [15:11]), .eq(comparator_26_eq));  // open: gt, lt
  Comparator #(.width(5), .mode("twosComplement")) comparator_27 (
    .a(\比较IR [15:11]), .b({5{1'b0}}), .eq(comparator_27_eq));  // open: gt, lt
  and and_1 (and_1_out, comparator_8_eq, not_1_out);
  and and_2 (and_2_out[0], comparator_10_eq, not_2_out);
  and and_3 (and_2_out[1], comparator_12_eq, not_3_out);
  and and_4 (and_4_out, comparator_14_eq, not_4_out);
  and and_5 (and_5_out[0], comparator_16_eq, not_5_out);
  not not_5 (not_5_out, comparator_17_eq);
  and and_6 (and_5_out[1], comparator_18_eq, not_6_out);
  not not_6 (not_6_out, comparator_19_eq);
  and and_7 (and_7_out[0], comparator_20_eq, not_7_out);
  not not_7 (not_7_out, comparator_21_eq);
  and and_8 (and_7_out[1], comparator_22_eq, not_8_out);
  not not_8 (not_8_out, comparator_23_eq);
  not not_9 (not_9_out, comparator_25_eq);
  not not_10 (not_10_out, comparator_27_eq);
  or or_3 (or_3_out, and_2_out[0], and_2_out[1]);
  or or_4 (or_4_out, and_5_out[0], and_5_out[1]);
  or or_5 (or_5_out, and_7_out[0], and_7_out[1]);
  and and_9 (and_9_out[0], comparator_24_eq, not_9_out);
  and and_10 (and_9_out[1], comparator_26_eq, not_10_out);
  or or_6 (or_6_out, and_9_out[0], and_9_out[1]);
  Multiplexer #(.select(3), .width(2), .disabled("Z"), .enable("false")) multiplexer_1 (
    .in0(2'b01), .in1(and_2_out), .in2(2'b01), .in3(and_5_out), .in4(and_7_out), .in5(and_7_out),
    .in6(and_9_out), .in7(and_9_out), .out(BA), .sel({both, R2, R1}));
  Multiplexer #(.select(3), .width(1), .disabled("Z"), .enable("false")) multiplexer_2 (
    .in0(and_1_out), .in1(or_3_out), .in2(and_4_out), .in3(or_4_out), .in4(or_5_out), .in5(or_5_out),
    .in6(or_6_out), .in7(or_6_out), .out(multiplexer_2_out), .sel({both, R2, R1}));
  Comparator #(.width(32), .mode("twosComplement")) comparator_28 (
    .a(\比较IR ), .b({32{1'b0}}), .eq(comparator_28_eq));  // open: gt, lt
  not not_11 (not_11_out, comparator_28_eq);
  not not_12 (not_12_out, both2);
  and and_11 (and_11_out, not_12_out, multiplexer_2_out);
  and and_12 (and_12_out, Syscall, not_11_out);
  or or_7 (out_5, and_11_out, and_12_out);

  // Other names for the same wires on the sheet: rd2[4:0] = \比较IR [15:11]; rt2[4:0] = \比较IR [20:16];
  //   rs2[4:0] = \比较IR [25:21]; rd1[4:0] = \被比较IR [15:11]; rt1[4:0] = \被比较IR [20:16]; rs1[4:0] = \被比较IR [25:21]

  // Notes on the sheet:
  //   OP
endmodule

module \重定向判断电路  (
  input  [31:0] \被比较IR ,
  input  [31:0] \比较IR ,
  input  Syscall,
  output [1:0] BA,
  output out_5
);

  wire and_1_out, and_2_out, and_3_out, and_4_out, and_5_out, and_6_out, and_7_out, and_8_out, and_9_out,
       and_10_out, and_11_out, and_12_out, both, both2, comparator_2_eq, comparator_3_eq, comparator_4_eq,
       comparator_6_eq, comparator_7_eq, comparator_9_eq, comparator_10_eq, comparator_11_eq,
       comparator_12_eq, comparator_13_eq, comparator_14_eq, comparator_15_eq, comparator_16_eq,
       comparator_17_eq, comparator_18_eq, comparator_19_eq, comparator_20_eq, comparator_21_eq,
       comparator_22_eq, comparator_23_eq, comparator_24_eq, comparator_25_eq, comparator_26_eq,
       comparator_27_eq, comparator_28_eq, comparator_29_eq, comparator_30_eq, comparator_31_eq,
       comparator_32_eq, comparator_33_eq, comparator_34_eq, comparator_35_eq, comparator_36_eq,
       comparator_37_eq, comparator_38_eq, comparator_39_eq, multiplexer_1_out, multiplexer_2_out,
       multiplexer_5_out, multiplexer_14_out, not_1_out, not_2_out, not_3_out, not_4_out, not_5_out,
       not_6_out, not_7_out, not_8_out, not_9_out, not_10_out, not_11_out, not_12_out, or_3_out, or_4_out,
       or_5_out, or_6_out, R1, R2, sw;
  wire [1:0] multiplexer_3_out, multiplexer_6_out, multiplexer_8_out, multiplexer_10_out, multiplexer_12_out;

  Comparator #(.width(6), .mode("twosComplement")) comparator_1 (
    .a(\比较IR [31:26]), .b({6{1'b0}}), .eq(R2));  // open: gt, lt
  Comparator #(.width(6), .mode("twosComplement")) comparator_2 (
    .a(\比较IR [31:26]), .b(6'b101011), .eq(comparator_2_eq));  // open: gt, lt
  Comparator #(.width(6), .mode("twosComplement")) comparator_3 (
    .a(\比较IR [31:26]), .b(6'b000100), .eq(comparator_3_eq));  // open: gt, lt
  Comparator #(.width(6), .mode("twosComplement")) comparator_4 (
    .a(\比较IR [31:26]), .b(6'b000101), .eq(comparator_4_eq));  // open: gt, lt
  Comparator #(.width(6), .mode("twosComplement")) comparator_5 (
    .a(\被比较IR [31:26]), .b(6'b101011), .eq(sw));  // open: gt, lt
  Comparator #(.width(6), .mode("twosComplement")) comparator_6 (
    .a(\被比较IR [31:26]), .b(6'b000100), .eq(comparator_6_eq));  // open: gt, lt
  Comparator #(.width(6), .mode("twosComplement")) comparator_7 (
    .a(\被比较IR [31:26]), .b(6'b000101), .eq(comparator_7_eq));  // open: gt, lt
  Comparator #(.width(6), .mode("twosComplement")) comparator_8 (
    .a(\被比较IR [31:26]), .b({6{1'b0}}), .eq(R1));  // open: gt, lt
  or or_1 (both2, comparator_3_eq, comparator_2_eq, comparator_4_eq);
  or or_2 (both, comparator_6_eq, comparator_7_eq);
  Comparator #(.width(5), .mode("twosComplement")) comparator_9 (
    .a(5'b00010), .b(\比较IR [20:16]), .eq(comparator_9_eq));  // open: gt, lt
  Comparator #(.width(5), .mode("twosComplement")) comparator_10 (
    .a(5'b00010), .b(\比较IR [20:16]), .eq(comparator_10_eq));  // open: gt, lt
  Comparator #(.width(5), .mode("twosComplement")) comparator_11 (
    .a(5'b00100), .b(\比较IR [20:16]), .eq(comparator_11_eq));  // open: gt, lt
  Comparator #(.width(5), .mode("twosComplement")) comparator_12 (
    .a(5'b00010), .b(\比较IR [15:11]), .eq(comparator_12_eq));  // open: gt, lt
  Comparator #(.width(5), .mode("twosComplement")) comparator_13 (
    .a(5'b00010), .b(\比较IR [15:11]), .eq(comparator_13_eq));  // open: gt, lt
  Comparator #(.width(5), .mode("twosComplement")) comparator_14 (
    .a(5'b00100), .b(\比较IR [15:11]), .eq(comparator_14_eq));  // open: gt, lt
  Comparator #(.width(5), .mode("twosComplement")) comparator_15 (
    .a(5'b00010), .b(\比较IR [20:16]), .eq(comparator_15_eq));  // open: gt, lt
  Comparator #(.width(5), .mode("twosComplement")) comparator_16 (
    .a(5'b00100), .b(\比较IR [20:16]), .eq(comparator_16_eq));  // open: gt, lt
  Comparator #(.width(5), .mode("twosComplement")) comparator_17 (
    .a(5'b00010), .b(\比较IR [15:11]), .eq(comparator_17_eq));  // open: gt, lt
  Comparator #(.width(5), .mode("twosComplement")) comparator_18 (
    .a(5'b00100), .b(\比较IR [15:11]), .eq(comparator_18_eq));  // open: gt, lt
  Comparator #(.width(5), .mode("twosComplement")) comparator_19 (
    .a(\被比较IR [25:21]), .b(\比较IR [20:16]), .eq(comparator_19_eq));  // open: gt, lt
  Comparator #(.width(5), .mode("twosComplement")) comparator_20 (
    .a(\比较IR [20:16]), .b({5{1'b0}}), .eq(comparator_20_eq));  // open: gt, lt
  not not_1 (not_1_out, comparator_20_eq);
  Comparator #(.width(5), .mode("twosComplement")) comparator_21 (
    .a(\被比较IR [25:21]), .b(\比较IR [20:16]), .eq(comparator_21_eq));  // open: gt, lt
  Comparator #(.width(5), .mode("twosComplement")) comparator_22 (
    .a(\比较IR [20:16]), .b({5{1'b0}}), .eq(comparator_22_eq));  // open: gt, lt
  not not_2 (not_2_out, comparator_22_eq);
  Comparator #(.width(5), .mode("twosComplement")) comparator_23 (
    .a(\被比较IR [20:16]), .b(\比较IR [20:16]), .eq(comparator_23_eq));  // open: gt, lt
  not not_3 (not_3_out, comparator_24_eq);
  Comparator #(.width(5), .mode("twosComplement")) comparator_24 (
    .a(\比较IR [20:16]), .b({5{1'b0}}), .eq(comparator_24_eq));  // open: gt, lt
  Comparator #(.width(5), .mode("twosComplement")) comparator_25 (
    .a(\被比较IR [25:21]), .b(\比较IR [15:11]), .eq(comparator_25_eq));  // open: gt, lt
  Comparator #(.width(5), .mode("twosComplement")) comparator_26 (
    .a(\比较IR [15:11]), .b({5{1'b0}}), .eq(comparator_26_eq));  // open: gt, lt
  Comparator #(.width(5), .mode("twosComplement")) comparator_27 (
    .a(\被比较IR [25:21]), .b(\比较IR [15:11]), .eq(comparator_27_eq));  // open: gt, lt
  Comparator #(.width(5), .mode("twosComplement")) comparator_28 (
    .a(\比较IR [15:11]), .b({5{1'b0}}), .eq(comparator_28_eq));  // open: gt, lt
  Comparator #(.width(5), .mode("twosComplement")) comparator_29 (
    .a(\被比较IR [20:16]), .b(\比较IR [15:11]), .eq(comparator_29_eq));  // open: gt, lt
  Comparator #(.width(5), .mode("twosComplement")) comparator_30 (
    .a(\比较IR [15:11]), .b({5{1'b0}}), .eq(comparator_30_eq));  // open: gt, lt
  Comparator #(.width(5), .mode("twosComplement")) comparator_31 (
    .a(\被比较IR [25:21]), .b(\比较IR [20:16]), .eq(comparator_31_eq));  // open: gt, lt
  Comparator #(.width(5), .mode("twosComplement")) comparator_32 (
    .a(\比较IR [20:16]), .b({5{1'b0}}), .eq(comparator_32_eq));  // open: gt, lt
  Comparator #(.width(5), .mode("twosComplement")) comparator_33 (
    .a(\被比较IR [20:16]), .b(\比较IR [20:16]), .eq(comparator_33_eq));  // open: gt, lt
  Comparator #(.width(5), .mode("twosComplement")) comparator_34 (
    .a(\比较IR [20:16]), .b({5{1'b0}}), .eq(comparator_34_eq));  // open: gt, lt
  Comparator #(.width(5), .mode("twosComplement")) comparator_35 (
    .a(\被比较IR [25:21]), .b(\比较IR [15:11]), .eq(comparator_35_eq));  // open: gt, lt
  Comparator #(.width(5), .mode("twosComplement")) comparator_36 (
    .a(\比较IR [15:11]), .b({5{1'b0}}), .eq(comparator_36_eq));  // open: gt, lt
  Comparator #(.width(5), .mode("twosComplement")) comparator_37 (
    .a(\被比较IR [20:16]), .b(\比较IR [15:11]), .eq(comparator_37_eq));  // open: gt, lt
  Comparator #(.width(5), .mode("twosComplement")) comparator_38 (
    .a(\比较IR [15:11]), .b({5{1'b0}}), .eq(comparator_38_eq));  // open: gt, lt
  and and_1 (and_1_out, comparator_19_eq, not_1_out);
  and and_2 (and_2_out, comparator_21_eq, not_2_out);
  and and_3 (and_3_out, comparator_23_eq, not_3_out);
  and and_4 (and_4_out, comparator_25_eq, not_4_out);
  not not_4 (not_4_out, comparator_26_eq);
  and and_5 (and_5_out, comparator_27_eq, not_5_out);
  not not_5 (not_5_out, comparator_28_eq);
  not not_6 (not_6_out, comparator_30_eq);
  and and_6 (and_6_out, comparator_31_eq, not_7_out);
  not not_7 (not_7_out, comparator_32_eq);
  not not_8 (not_8_out, comparator_34_eq);
  not not_9 (not_9_out, comparator_36_eq);
  not not_10 (not_10_out, comparator_38_eq);
  Multiplexer #(.select(1), .width(1), .disabled("Z"), .enable("false")) multiplexer_1 (
    .in0(multiplexer_2_out), .in1(or_3_out), .out(multiplexer_1_out), .sel(sw));
  Multiplexer #(.select(1), .width(1), .disabled("Z"), .enable("false")) multiplexer_2 (
    .in0(and_1_out), .in1(comparator_9_eq), .out(multiplexer_2_out), .sel(Syscall));
  Multiplexer #(.select(1), .width(1), .disabled("Z"), .enable("false")) multiplexer_3 (
    .in0(and_2_out), .in1(comparator_10_eq), .out(multiplexer_3_out[0]), .sel(Syscall));
  Multiplexer #(.select(1), .width(1), .disabled("Z"), .enable("false")) multiplexer_4 (
    .in0(and_3_out), .in1(comparator_11_eq), .out(multiplexer_3_out[1]), .sel(Syscall));
  Multiplexer #(.select(1), .width(1), .disabled("Z"), .enable("false")) multiplexer_5 (
    .in0(and_4_out), .in1(comparator_13_eq), .out(multiplexer_5_out), .sel(Syscall));
  Multiplexer #(.select(1), .width(1), .disabled("Z"), .enable("false")) multiplexer_6 (
    .in0(and_5_out), .in1(comparator_12_eq), .out(multiplexer_6_out[0]), .sel(Syscall));
  and and_7 (and_7_out, comparator_29_eq, not_6_out);
  Multiplexer #(.select(1), .width(1), .disabled("Z"), .enable("false")) multiplexer_7 (
    .in0(and_7_out), .in1(comparator_14_eq), .out(multiplexer_6_out[1]), .sel(Syscall));
  Multiplexer #(.select(1), .width(1), .disabled("Z"), .enable("false")) multiplexer_8 (
    .in0(and_6_out), .in1(comparator_15_eq), .out(multiplexer_8_out[0]), .sel(Syscall));
  and and_8 (and_8_out, comparator_33_eq, not_8_out);
  Multiplexer #(.select(1), .width(1), .disabled("Z"), .enable("false")) multiplexer_9 (
    .in0(and_8_out), .in1(comparator_16_eq), .out(multiplexer_8_out[1]), .sel(Syscall));
  and and_9 (and_9_out, comparator_35_eq, not_9_out);
  Multiplexer #(.select(1), .width(1), .disabled("Z"), .enable("false")) multiplexer_10 (
    .in0(and_9_out), .in1(comparator_17_eq), .out(multiplexer_10_out[0]), .sel(Syscall));
  Multiplexer #(.select(1), .width(1), .disabled("Z"), .enable("false")) multiplexer_11 (
    .in0(and_10_out), .in1(comparator_18_eq), .out(multiplexer_10_out[1]), .sel(Syscall));
  and and_10 (and_10_out, comparator_37_eq, not_10_out);
  or or_3 (or_3_out, multiplexer_3_out[0], multiplexer_3_out[1]);
  or or_4 (or_4_out, multiplexer_6_out[0], multiplexer_6_out[1]);
  or or_5 (or_5_out, multiplexer_8_out[0], multiplexer_8_out[1]);
  or or_6 (or_6_out, multiplexer_10_out[0], multiplexer_10_out[1]);
  Multiplexer #(.select(1), .width(2), .disabled("Z"), .enable("false")) multiplexer_12 (
    .in0(2'b01), .in1(multiplexer_3_out), .out(multiplexer_12_out), .sel(sw));
  Multiplexer #(.select(3), .width(2), .disabled("Z"), .enable("false")) multiplexer_13 (
    .in0(multiplexer_12_out), .in1(multiplexer_3_out), .in2(2'b01), .in3(multiplexer_6_out),
    .in4(multiplexer_8_out), .in5(multiplexer_8_out), .in6(multiplexer_10_out), .in7(multiplexer_10_out),
    .out(BA), .sel({both, R2, R1}));
  not not_11 (not_11_out, both2);
  Multiplexer #(.select(3), .width(1), .disabled("Z"), .enable("false")) multiplexer_14 (
    .in0(multiplexer_1_out), .in1(or_3_out), .in2(multiplexer_5_out), .in3(or_4_out), .in4(or_5_out),
    .in5(or_5_out), .in6(or_6_out), .in7(or_6_out), .out(multiplexer_14_out), .sel({both, R2, R1}));
  Comparator #(.width(32), .mode("twosComplement")) comparator_39 (
    .a(\比较IR ), .b({32{1'b0}}), .eq(comparator_39_eq));  // open: gt, lt
  not not_12 (not_12_out, comparator_39_eq);
  and and_11 (and_11_out, not_11_out, multiplexer_14_out);
  or or_7 (out_5, and_11_out, and_12_out);
  and and_12 (and_12_out, Syscall, not_12_out);

  // Other names for the same wires on the sheet: rd2[4:0] = \比较IR [15:11]; rt2[4:0] = \比较IR [20:16];
  //   rs2[4:0] = \比较IR [25:21]; rd1[4:0] = \被比较IR [15:11]; rt1[4:0] = \被比较IR [20:16]; rs1[4:0] = \被比较IR [25:21]

  // Notes on the sheet:
  //   OP
endmodule
